// Logisim project 6位原码阵列乘法器.circ as structural Verilog: 7 circuits, main circuit 6位原码阵列乘法器
// 5位阵列乘法器
module \_5位无符号阵列乘法器_横向  (
  input  [4:0] X,
  input  [4:0] Y,
  output [9:0] \乘积 
);

  wire \n1位全加器fa_2_cout , \n1位全加器fa_2_si , \n1位全加器fa_3_cout , \n1位全加器fa_4_cout , \n1位全加器fa_4_si ,
       \n1位全加器fa_5_cout , \n1位全加器fa_5_si , \n1位全加器fa_6_cout , \n1位全加器fa_7_cout , \n1位全加器fa_7_si ,
       \n1位全加器fa_8_cout , \n1位全加器fa_8_si , \n1位全加器fa_9_cout , \n1位全加器fa_9_si , \n1位全加器fa_10_cout ,
       \n1位全加器fa_11_cout , \n1位全加器fa_11_si , \n1位全加器fa_12_cout , \n1位全加器fa_12_si , \n1位全加器fa_13_cout ,
       \n1位全加器fa_13_si , \n1位全加器fa_14_cout , \n1位全加器fa_15_cout , \n1位全加器fa_15_si , \n1位全加器fa_16_cout ,
       \n1位全加器fa_16_si , \n1位全加器fa_17_cout , \n1位全加器fa_18_cout , \n1位全加器fa_18_si , \n1位全加器fa_19_cout ,
       \n1位全加器fa_20_cout , X0Y1, X0Y2, X0Y3, X0Y4, X1Y0, X1Y1, X1Y2, X1Y3, X1Y4, X2Y0, X2Y1, X2Y2, X2Y3,
       X2Y4, X3Y0, X3Y1, X3Y2, X3Y3, X3Y4, X4Y0, X4Y1, X4Y2, X4Y3, X4Y4;

  // Probe on X
  \_1位全加器FA  \u_1位全加器fa_1  (.Cout(\乘积 [9]), .Si(\乘积 [8]), .Cin(X4Y4), .Xi(\n1位全加器fa_3_cout ), .Yi(\n1位全加器fa_2_cout ));
  \与门阵列  \u_与门阵列_1  (
    .X(X), .XY4({X4Y4, X3Y4, X2Y4, X1Y4, X0Y4}), .XY3({X4Y3, X3Y3, X2Y3, X1Y3, X0Y3}),
    .XY2({X4Y2, X3Y2, X2Y2, X1Y2, X0Y2}), .XY1({X4Y1, X3Y1, X2Y1, X1Y1, X0Y1}),
    .XY0({X4Y0, X3Y0, X2Y0, X1Y0, \乘积 [0]}), .Y(Y));
  \_1位全加器FA  \u_1位全加器fa_2  (
    .Cout(\n1位全加器fa_2_cout ), .Si(\n1位全加器fa_2_si ), .Cin(X4Y3), .Xi(\n1位全加器fa_5_cout ), .Yi(\n1位全加器fa_4_cout ));
  \_1位全加器FA  \u_1位全加器fa_3  (
    .Cout(\n1位全加器fa_3_cout ), .Si(\乘积 [7]), .Cin(X3Y4), .Xi(\n1位全加器fa_6_cout ), .Yi(\n1位全加器fa_2_si ));
  \_1位全加器FA  \u_1位全加器fa_4  (
    .Cout(\n1位全加器fa_4_cout ), .Si(\n1位全加器fa_4_si ), .Cin(X4Y2), .Xi(\n1位全加器fa_8_cout ), .Yi(\n1位全加器fa_7_cout ));
  \_1位全加器FA  \u_1位全加器fa_5  (
    .Cout(\n1位全加器fa_5_cout ), .Si(\n1位全加器fa_5_si ), .Cin(X3Y3), .Xi(\n1位全加器fa_9_cout ), .Yi(\n1位全加器fa_4_si ));
  \_1位全加器FA  \u_1位全加器fa_6  (
    .Cout(\n1位全加器fa_6_cout ), .Si(\乘积 [6]), .Cin(X2Y4), .Xi(\n1位全加器fa_10_cout ), .Yi(\n1位全加器fa_5_si ));
  // Probe on Y
  \_1位全加器FA  \u_1位全加器fa_7  (
    .Cout(\n1位全加器fa_7_cout ), .Si(\n1位全加器fa_7_si ), .Cin(X4Y1), .Xi(\n1位全加器fa_11_cout ), .Yi(1'b0));
  \_1位全加器FA  \u_1位全加器fa_8  (
    .Cout(\n1位全加器fa_8_cout ), .Si(\n1位全加器fa_8_si ), .Cin(X3Y2), .Xi(\n1位全加器fa_12_cout ), .Yi(\n1位全加器fa_7_si ));
  \_1位全加器FA  \u_1位全加器fa_9  (
    .Cout(\n1位全加器fa_9_cout ), .Si(\n1位全加器fa_9_si ), .Cin(X2Y3), .Xi(\n1位全加器fa_13_cout ), .Yi(\n1位全加器fa_8_si ));
  \_1位全加器FA  \u_1位全加器fa_10  (
    .Cout(\n1位全加器fa_10_cout ), .Si(\乘积 [5]), .Cin(X1Y4), .Xi(\n1位全加器fa_14_cout ), .Yi(\n1位全加器fa_9_si ));
  \_1位全加器FA  \u_1位全加器fa_11  (
    .Cout(\n1位全加器fa_11_cout ), .Si(\n1位全加器fa_11_si ), .Cin(X3Y1), .Xi(\n1位全加器fa_15_cout ), .Yi(X4Y0));
  \_1位全加器FA  \u_1位全加器fa_12  (
    .Cout(\n1位全加器fa_12_cout ), .Si(\n1位全加器fa_12_si ), .Cin(X2Y2), .Xi(\n1位全加器fa_16_cout ),
    .Yi(\n1位全加器fa_11_si ));
  \_1位全加器FA  \u_1位全加器fa_13  (
    .Cout(\n1位全加器fa_13_cout ), .Si(\n1位全加器fa_13_si ), .Cin(X1Y3), .Xi(\n1位全加器fa_17_cout ),
    .Yi(\n1位全加器fa_12_si ));
  \_1位全加器FA  \u_1位全加器fa_14  (.Cout(\n1位全加器fa_14_cout ), .Si(\乘积 [4]), .Cin(X0Y4), .Xi(1'b0), .Yi(\n1位全加器fa_13_si ));
  \_1位全加器FA  \u_1位全加器fa_15  (
    .Cout(\n1位全加器fa_15_cout ), .Si(\n1位全加器fa_15_si ), .Cin(X2Y1), .Xi(\n1位全加器fa_18_cout ), .Yi(X3Y0));
  \_1位全加器FA  \u_1位全加器fa_16  (
    .Cout(\n1位全加器fa_16_cout ), .Si(\n1位全加器fa_16_si ), .Cin(X1Y2), .Xi(\n1位全加器fa_19_cout ),
    .Yi(\n1位全加器fa_15_si ));
  \_1位全加器FA  \u_1位全加器fa_17  (.Cout(\n1位全加器fa_17_cout ), .Si(\乘积 [3]), .Cin(X0Y3), .Xi(1'b0), .Yi(\n1位全加器fa_16_si ));
  // Probe on \乘积 
  \_1位全加器FA  \u_1位全加器fa_18  (
    .Cout(\n1位全加器fa_18_cout ), .Si(\n1位全加器fa_18_si ), .Cin(X1Y1), .Xi(\n1位全加器fa_20_cout ), .Yi(X2Y0));
  \_1位全加器FA  \u_1位全加器fa_19  (.Cout(\n1位全加器fa_19_cout ), .Si(\乘积 [2]), .Cin(X0Y2), .Xi(1'b0), .Yi(\n1位全加器fa_18_si ));
  // Probe on X
  // Probe on Y
  // Probe on \乘积 
  \_1位全加器FA  \u_1位全加器fa_20  (.Cout(\n1位全加器fa_20_cout ), .Si(\乘积 [1]), .Cin(X0Y1), .Xi(1'b0), .Yi(X1Y0));

  // Other names for the same wires on the sheet: P[9:0] = \乘积 ; P0 = \乘积 [0]; X0Y0 = \乘积 [0];
  //   XY0[4:0] = {X4Y0, X3Y0, X2Y0, X1Y0, \乘积 [0]}; P1 = \乘积 [1]; P2 = \乘积 [2]; P3 = \乘积 [3]; P4 = \乘积 [4];
  //   P5 = \乘积 [5]; P6 = \乘积 [6]; P7 = \乘积 [7]; P8 = \乘积 [8]; P9 = \乘积 [9]; XY1[4:0] = {X4Y1, X3Y1, X2Y1, X1Y1, X0Y1};
  //   XY2[4:0] = {X4Y2, X3Y2, X2Y2, X1Y2, X0Y2}; XY3[4:0] = {X4Y3, X3Y3, X2Y3, X1Y3, X0Y3};
  //   XY4[4:0] = {X4Y4, X3Y4, X2Y4, X1Y4, X0Y4}

  // Notes on the sheet:
  //   X: pull=down
  //   Y: pull=down
  //   输入引脚区
  //   输出引脚区
  //   5位无符号阵列乘法器（横向）
  //   ×
  //   =
  //   输入：X、Y          5位无符号数
  //   输出：乘积P        10位无符号数
endmodule

// 阵列乘法器
module \_5位无符号阵列乘法器_斜向  (
  input  [4:0] X,
  input  [4:0] Y,
  output [9:0] \乘积 
);

  wire \n1位全加器fa_2_cout , \n1位全加器fa_2_si , \n1位全加器fa_3_cout , \n1位全加器fa_4_cout , \n1位全加器fa_4_si ,
       \n1位全加器fa_5_cout , \n1位全加器fa_5_si , \n1位全加器fa_6_cout , \n1位全加器fa_7_cout , \n1位全加器fa_7_si ,
       \n1位全加器fa_8_cout , \n1位全加器fa_8_si , \n1位全加器fa_9_cout , \n1位全加器fa_9_si , \n1位全加器fa_10_cout ,
       \n1位全加器fa_11_cout , \n1位全加器fa_11_si , \n1位全加器fa_12_cout , \n1位全加器fa_12_si , \n1位全加器fa_13_cout ,
       \n1位全加器fa_13_si , \n1位全加器fa_14_cout , \n1位全加器fa_15_cout , \n1位全加器fa_15_si , \n1位全加器fa_16_cout ,
       \n1位全加器fa_16_si , \n1位全加器fa_17_cout , \n1位全加器fa_18_cout , \n1位全加器fa_18_si , \n1位全加器fa_19_cout ,
       \n1位全加器fa_20_cout , X0Y1, X0Y2, X0Y3, X0Y4, X1Y0, X1Y1, X1Y2, X1Y3, X1Y4, X2Y0, X2Y1, X2Y2, X2Y3,
       X2Y4, X3Y0, X3Y1, X3Y2, X3Y3, X3Y4, X4Y0, X4Y1, X4Y2, X4Y3, X4Y4;

  // Probe on X
  \_1位全加器FA  \u_1位全加器fa_1  (.Cout(\乘积 [9]), .Si(\乘积 [8]), .Cin(\n1位全加器fa_2_cout ), .Xi(\n1位全加器fa_3_cout ), .Yi(X4Y4));
  \与门阵列  \u_与门阵列_1  (
    .X(X), .XY4({X4Y4, X3Y4, X2Y4, X1Y4, X0Y4}), .XY3({X4Y3, X3Y3, X2Y3, X1Y3, X0Y3}),
    .XY2({X4Y2, X3Y2, X2Y2, X1Y2, X0Y2}), .XY1({X4Y1, X3Y1, X2Y1, X1Y1, X0Y1}),
    .XY0({X4Y0, X3Y0, X2Y0, X1Y0, \乘积 [0]}), .Y(Y));
  \_1位全加器FA  \u_1位全加器fa_2  (
    .Cout(\n1位全加器fa_2_cout ), .Si(\n1位全加器fa_2_si ), .Cin(\n1位全加器fa_4_cout ), .Xi(X3Y4), .Yi(X4Y3));
  \_1位全加器FA  \u_1位全加器fa_3  (
    .Cout(\n1位全加器fa_3_cout ), .Si(\乘积 [7]), .Cin(\n1位全加器fa_5_cout ), .Xi(\n1位全加器fa_6_cout ),
    .Yi(\n1位全加器fa_2_si ));
  \_1位全加器FA  \u_1位全加器fa_4  (
    .Cout(\n1位全加器fa_4_cout ), .Si(\n1位全加器fa_4_si ), .Cin(\n1位全加器fa_7_cout ), .Xi(X3Y3), .Yi(X4Y2));
  \_1位全加器FA  \u_1位全加器fa_5  (
    .Cout(\n1位全加器fa_5_cout ), .Si(\n1位全加器fa_5_si ), .Cin(\n1位全加器fa_8_cout ), .Xi(X2Y4), .Yi(\n1位全加器fa_4_si ));
  \_1位全加器FA  \u_1位全加器fa_6  (
    .Cout(\n1位全加器fa_6_cout ), .Si(\乘积 [6]), .Cin(\n1位全加器fa_9_cout ), .Xi(\n1位全加器fa_10_cout ),
    .Yi(\n1位全加器fa_5_si ));
  // Probe on Y
  \_1位全加器FA  \u_1位全加器fa_7  (
    .Cout(\n1位全加器fa_7_cout ), .Si(\n1位全加器fa_7_si ), .Cin(\n1位全加器fa_11_cout ), .Xi(X3Y2), .Yi(X4Y1));
  \_1位全加器FA  \u_1位全加器fa_8  (
    .Cout(\n1位全加器fa_8_cout ), .Si(\n1位全加器fa_8_si ), .Cin(\n1位全加器fa_12_cout ), .Xi(X2Y3), .Yi(\n1位全加器fa_7_si ));
  \_1位全加器FA  \u_1位全加器fa_9  (
    .Cout(\n1位全加器fa_9_cout ), .Si(\n1位全加器fa_9_si ), .Cin(\n1位全加器fa_13_cout ), .Xi(X1Y4), .Yi(\n1位全加器fa_8_si ));
  \_1位全加器FA  \u_1位全加器fa_10  (
    .Cout(\n1位全加器fa_10_cout ), .Si(\乘积 [5]), .Cin(\n1位全加器fa_14_cout ), .Xi(1'b0), .Yi(\n1位全加器fa_9_si ));
  \_1位全加器FA  \u_1位全加器fa_11  (.Cout(\n1位全加器fa_11_cout ), .Si(\n1位全加器fa_11_si ), .Cin(1'b0), .Xi(X3Y1), .Yi(X4Y0));
  \_1位全加器FA  \u_1位全加器fa_12  (
    .Cout(\n1位全加器fa_12_cout ), .Si(\n1位全加器fa_12_si ), .Cin(\n1位全加器fa_15_cout ), .Xi(X2Y2),
    .Yi(\n1位全加器fa_11_si ));
  \_1位全加器FA  \u_1位全加器fa_13  (
    .Cout(\n1位全加器fa_13_cout ), .Si(\n1位全加器fa_13_si ), .Cin(\n1位全加器fa_16_cout ), .Xi(X1Y3),
    .Yi(\n1位全加器fa_12_si ));
  \_1位全加器FA  \u_1位全加器fa_14  (
    .Cout(\n1位全加器fa_14_cout ), .Si(\乘积 [4]), .Cin(\n1位全加器fa_17_cout ), .Xi(X0Y4), .Yi(\n1位全加器fa_13_si ));
  \_1位全加器FA  \u_1位全加器fa_15  (.Cout(\n1位全加器fa_15_cout ), .Si(\n1位全加器fa_15_si ), .Cin(1'b0), .Xi(X2Y1), .Yi(X3Y0));
  \_1位全加器FA  \u_1位全加器fa_16  (
    .Cout(\n1位全加器fa_16_cout ), .Si(\n1位全加器fa_16_si ), .Cin(\n1位全加器fa_18_cout ), .Xi(X1Y2),
    .Yi(\n1位全加器fa_15_si ));
  \_1位全加器FA  \u_1位全加器fa_17  (
    .Cout(\n1位全加器fa_17_cout ), .Si(\乘积 [3]), .Cin(\n1位全加器fa_19_cout ), .Xi(X0Y3), .Yi(\n1位全加器fa_16_si ));
  // Probe on \乘积 
  \_1位全加器FA  \u_1位全加器fa_18  (.Cout(\n1位全加器fa_18_cout ), .Si(\n1位全加器fa_18_si ), .Cin(1'b0), .Xi(X1Y1), .Yi(X2Y0));
  \_1位全加器FA  \u_1位全加器fa_19  (
    .Cout(\n1位全加器fa_19_cout ), .Si(\乘积 [2]), .Cin(\n1位全加器fa_20_cout ), .Xi(X0Y2), .Yi(\n1位全加器fa_18_si ));
  // Probe on X
  // Probe on Y
  // Probe on \乘积 
  \_1位全加器FA  \u_1位全加器fa_20  (.Cout(\n1位全加器fa_20_cout ), .Si(\乘积 [1]), .Cin(1'b0), .Xi(X0Y1), .Yi(X1Y0));

  // Other names for the same wires on the sheet: P[9:0] = \乘积 ; P0 = \乘积 [0]; X0Y0 = \乘积 [0];
  //   XY0[4:0] = {X4Y0, X3Y0, X2Y0, X1Y0, \乘积 [0]}; P1 = \乘积 [1]; P2 = \乘积 [2]; P3 = \乘积 [3]; P4 = \乘积 [4];
  //   P5 = \乘积 [5]; P6 = \乘积 [6]; P7 = \乘积 [7]; P8 = \乘积 [8]; P9 = \乘积 [9]; XY1[4:0] = {X4Y1, X3Y1, X2Y1, X1Y1, X0Y1};
  //   XY2[4:0] = {X4Y2, X3Y2, X2Y2, X1Y2, X0Y2}; XY3[4:0] = {X4Y3, X3Y3, X2Y3, X1Y3, X0Y3};
  //   XY4[4:0] = {X4Y4, X3Y4, X2Y4, X1Y4, X0Y4}

  // Notes on the sheet:
  //   Y: pull=down
  //   X: pull=down
  //   输入引脚区
  //   输出引脚区
  //   5位无符号阵列乘法器（斜向）
  //   ×
  //   =
  //   输入：X、Y          5位无符号数
  //   输出：乘积P        10位无符号数
endmodule

module \与门阵列  (
  input  [4:0] X,
  input  [4:0] Y,
  output [4:0] XY0,
  output [4:0] XY1,
  output [4:0] XY2,
  output [4:0] XY3,
  output [4:0] XY4
);

  and and_1 (XY0[4], X[4], Y[0]);
  and and_2 (XY1[4], X[4], Y[1]);
  and and_3 (XY2[4], X[4], Y[2]);
  and and_4 (XY3[4], X[4], Y[3]);
  and and_5 (XY4[4], X[4], Y[4]);
  and and_6 (XY0[3], X[3], Y[0]);
  and and_7 (XY1[3], X[3], Y[1]);
  and and_8 (XY2[3], X[3], Y[2]);
  and and_9 (XY3[3], X[3], Y[3]);
  and and_10 (XY4[3], X[3], Y[4]);
  and and_11 (XY0[2], X[2], Y[0]);
  and and_12 (XY1[2], X[2], Y[1]);
  and and_13 (XY2[2], X[2], Y[2]);
  and and_14 (XY3[2], X[2], Y[3]);
  and and_15 (XY4[2], X[2], Y[4]);
  and and_16 (XY0[1], X[1], Y[0]);
  and and_17 (XY0[0], X[0], Y[0]);
  and and_18 (XY1[1], X[1], Y[1]);
  and and_19 (XY1[0], X[0], Y[1]);
  and and_20 (XY2[0], X[0], Y[2]);
  and and_21 (XY2[1], X[1], Y[2]);
  and and_22 (XY3[0], X[0], Y[3]);
  and and_23 (XY3[1], X[1], Y[3]);
  and and_24 (XY4[0], X[0], Y[4]);
  and and_25 (XY4[1], X[1], Y[4]);

  // Other names for the same wires on the sheet: X0Y0 = XY0[0]; X1Y0 = XY0[1]; X2Y0 = XY0[2]; X3Y0 = XY0[3];
  //   X4Y0 = XY0[4]; X0Y1 = XY1[0]; X1Y1 = XY1[1]; X2Y1 = XY1[2]; X3Y1 = XY1[3]; X4Y1 = XY1[4]; X0Y2 = XY2[0];
  //   X1Y2 = XY2[1]; X2Y2 = XY2[2]; X3Y2 = XY2[3]; X4Y2 = XY2[4]; X0Y3 = XY3[0]; X1Y3 = XY3[1]; X2Y3 = XY3[2];
  //   X3Y3 = XY3[3]; X4Y3 = XY3[4]; X0Y4 = XY4[0]; X1Y4 = XY4[1]; X2Y4 = XY4[2]; X3Y4 = XY4[3]; X4Y4 = XY4[4]

  // Notes on the sheet:
  //   5位乘法与门阵列
endmodule

module \_1位全加器FA  (
  input  Cin,
  input  Xi,
  input  Yi,
  output Cout,
  output Si
);

  wire AND_2_out, AND_out, XOR_2_out;

  or OR (Cout, AND_out, AND_2_out);
  and AND (AND_out, Xi, Yi);
  and AND_2 (AND_2_out, Cin, XOR_2_out);
  xor XOR (Si, Cin, XOR_2_out);
  xor XOR_2 (XOR_2_out, Xi, Yi);

  // Notes on the sheet:
  //   1位全加器（FA）
  //   Si = Xi ^ Yi ^ Cin
  //   Cout = Xi Yi + Cin (Xi ^ Yi)
endmodule

// 6位转补码
module \_6位原码转补码器  (
  input  [5:0] \输入 ,
  output [5:0] out_2
);

  wire and_1_out, and_2_out, and_3_out, and_4_out, and_5_out, or_2_out, or_3_out, or_4_out, or_5_out;

  // OR_Gate or_1 has open pins: in0=\输入 [4], in1=or_2_out, out=open
  buf or_2 (or_2_out, or_3_out);  // OR_Gate
  and and_1 (and_1_out, or_2_out, \输入 [5]);
  xor xor_1 (out_2[4], \输入 [4], and_1_out);
  or or_3 (or_3_out, \输入 [2], or_4_out);
  and and_2 (and_2_out, or_3_out, \输入 [5]);
  xor xor_2 (out_2[3], \输入 [3], and_2_out);
  xor xor_3 (out_2[2], \输入 [2], and_3_out);
  or or_4 (or_4_out, \输入 [1], or_5_out);
  and and_3 (and_3_out, or_4_out, \输入 [5]);
  and and_4 (and_4_out, or_5_out, \输入 [5]);
  xor xor_4 (out_2[1], \输入 [1], and_4_out);
  or or_5 (or_5_out, \输入 [0], 1'b0);
  xor xor_5 (out_2[0], \输入 [0], and_5_out);
  and and_5 (and_5_out, 1'b0, \输入 [5]);

  assign out_2[5] = \输入 [5];

  // Notes on the sheet:
  //   输出
endmodule

module \_6位原码阵列乘法器  (
  input  [5:0] X,
  input  [5:0] Y,
  output [10:0] P
);

  wire comparator_1_eq, comparator_2_eq, comparator_3_eq;
  wire [5:0] X_t, \X真值 , Y_t, \Y真值 ;
  wire [10:0] P_t, \P真值 ;

  \_6位原码转补码器  \u_6位原码转补码器_1  (.\输入 (X), .out_2(X_t));
  \_5位无符号阵列乘法器_横向  \u_5位无符号阵列乘法器_横向_1  (.\乘积 (P[9:0]), .X(X[4:0]), .Y(Y[4:0]));
  Comparator #(.width(6), .mode("twosComplement")) comparator_1 (
    .a(6'b100000), .b(X_t), .eq(comparator_1_eq));  // open: gt, lt
  Multiplexer #(.select(1), .width(6), .disabled("Z"), .enable("false")) multiplexer_1 (
    .in0(X_t), .in1({6{1'b0}}), .out(\X真值 ), .sel(comparator_1_eq));
  \_6位原码转补码器  \u_6位原码转补码器_2  (.\输入 (Y), .out_2(Y_t));
  \_11位原码转补码器  \u_11位原码转补码器_1  (.in_1(P), .out_2(P_t));
  xor xor_1 (P[10], X[5], Y[5]);
  Comparator #(.width(6), .mode("twosComplement")) comparator_2 (
    .a(6'b100000), .b(Y_t), .eq(comparator_2_eq));  // open: gt, lt
  Multiplexer #(.select(1), .width(6), .disabled("Z"), .enable("false")) multiplexer_2 (
    .in0(Y_t), .in1({6{1'b0}}), .out(\Y真值 ), .sel(comparator_2_eq));
  Comparator #(.width(11), .mode("twosComplement")) comparator_3 (
    .a(11'h400), .b(P_t), .eq(comparator_3_eq));  // open: gt, lt
  Multiplexer #(.select(1), .width(11), .disabled("Z"), .enable("false")) multiplexer_3 (
    .in0(P_t), .in1({11{1'b0}}), .out(\P真值 ), .sel(comparator_3_eq));
  // Probe on \X真值 
  // Probe on \Y真值 
  // Probe on \P真值 

  // Other names for the same wires on the sheet: P_t_t[9:0] = P[9:0]; X_t_t[4:0] = X[4:0]; Y_t_t[4:0] = Y[4:0]

  // Notes on the sheet:
  //   输入引脚区
  //    功能说明：6位原码阵列乘法器          输入：X（6位原码）、Y（6位原码）          输出：P（11位原码）= X×Y
  //   输出引脚区
  //   ×
  //   =
endmodule

// 11位转补码
module \_11位原码转补码器  (
  input  [10:0] in_1,
  output [10:0] out_2
);

  wire and_1_out, and_2_out, and_3_out, and_4_out, and_5_out, and_6_out, and_7_out, and_8_out, and_9_out,
       and_10_out, or_2_out, or_3_out, or_4_out, or_5_out, or_6_out, or_7_out, or_8_out, or_9_out, or_10_out;

  // OR_Gate or_1 has open pins: in0=in_1[9], in1=or_2_out, out=open
  or or_2 (or_2_out, in_1[8], or_3_out);
  and and_1 (and_1_out, or_2_out, in_1[10]);
  xor xor_1 (out_2[9], in_1[9], and_1_out);
  or or_3 (or_3_out, in_1[7], or_4_out);
  and and_2 (and_2_out, or_3_out, in_1[10]);
  xor xor_2 (out_2[8], in_1[8], and_2_out);
  and and_3 (and_3_out, or_4_out, in_1[10]);
  xor xor_3 (out_2[7], in_1[7], and_3_out);
  or or_4 (or_4_out, in_1[6], or_5_out);
  xor xor_4 (out_2[6], in_1[6], and_4_out);
  or or_5 (or_5_out, in_1[5], or_6_out);
  and and_4 (and_4_out, or_5_out, in_1[10]);
  or or_6 (or_6_out, in_1[4], or_7_out);
  and and_5 (and_5_out, or_6_out, in_1[10]);
  xor xor_5 (out_2[5], in_1[5], and_5_out);
  or or_7 (or_7_out, in_1[3], or_8_out);
  and and_6 (and_6_out, or_7_out, in_1[10]);
  xor xor_6 (out_2[4], in_1[4], and_6_out);
  and and_7 (and_7_out, or_8_out, in_1[10]);
  xor xor_7 (out_2[3], in_1[3], and_7_out);
  or or_8 (or_8_out, in_1[2], or_9_out);
  xor xor_8 (out_2[2], in_1[2], and_8_out);
  or or_9 (or_9_out, in_1[1], or_10_out);
  and and_8 (and_8_out, or_9_out, in_1[10]);
  or or_10 (or_10_out, in_1[0], 1'b0);
  and and_9 (and_9_out, or_10_out, in_1[10]);
  xor xor_9 (out_2[1], in_1[1], and_9_out);
  and and_10 (and_10_out, 1'b0, in_1[10]);
  xor xor_10 (out_2[0], in_1[0], and_10_out);

  assign out_2[10] = in_1[10];

  // Notes on the sheet:
  //   输入
  //   输出
endmodule
