// Logisim project 8位奇校验传输测试实验.circ as structural Verilog: 4 circuits, main circuit 奇校验传输测试实验
module \奇校验传输测试实验  (
);

  wire and_1_out, and_2_out, C, CLK, CLR_out, OK;
  wire [7:0] counter_1_q, \发送 , \接收 ;
  wire [8:0] \奇校验编码电路_1_奇校验编码 , \随机加扰电路_1_加扰后数据 , \随机加扰电路_1_随机加扰屏蔽字 ;

  Counter #(.width(8), .max('hff), .ongoal("wrap"), .trigger("rising"), .behavior("old")) counter_1 (
    .Q(counter_1_q), .clk(CLK), .clr(CLR_out));  // open: load, D, count, carry, preset
  Button CLR (.out(CLR_out));
  Clock #(.highDuration(1), .lowDuration(1)) \u_时钟  (.out(CLK));
  ROM #(.addrWidth(8), .dataWidth(8), .Select("high")) rom_1 (.addr(counter_1_q), .data(\发送 ));
  // Probe on \发送 
  \奇校验编码电路  \u_奇校验编码电路_1  (.\原始数据 (\发送 ), .\奇校验编码 (\奇校验编码电路_1_奇校验编码 ));
  // Probe on \奇校验编码电路_1_奇校验编码 
  // Probe on \随机加扰电路_1_随机加扰屏蔽字 
  \随机加扰电路  \u_随机加扰电路_1  (
    .\_9位输入 (\奇校验编码电路_1_奇校验编码 ), .\随机加扰屏蔽字 (\随机加扰电路_1_随机加扰屏蔽字 ), .\加扰后数据 (\随机加扰电路_1_加扰后数据 ), .CLK(CLK));
  // Probe on \随机加扰电路_1_加扰后数据 
  \奇校验检错电路  \u_奇校验检错电路_1  (.\检错位 (C), .\奇校验编码 (\随机加扰电路_1_加扰后数据 ), .\数据位 (\接收 ));
  // Probe on \接收 
  Comparator #(.width(8), .mode("twosComplement")) comparator_1 (.a(\发送 ), .b(\接收 ), .eq(OK));  // open: gt, lt
  and and_1 (and_1_out, ~OK, ~C);  // AND_Gate
  and and_2 (and_2_out, C, OK);
  LED #(.active("true")) \u_数据正确  (.in(OK));
  LED #(.active("true")) \u_漏报  (.in(and_1_out));
  LED #(.active("true")) \u_校验位出错  (.in(and_2_out));
  LED #(.active("true")) \u_检错位  (.in(C));

  // Notes on the sheet:
  //   发送方
  //   计数器
  //   ROM存储器
  //   contents of rom_1 (hex, n*v repeats v):
  //   aa d0 c6 bc f3 a7 c7 fa d2 cc fd bf b1 f4 c4 ab fa d8 e3 f3 a7 ac c9 ad aa d0 ed a4 f3 a7 a2 ac c3
  //   bd c6 f3 a7 a2 e4 ba c7 d0 a8 e8 a7 ba da b2 b0 b0 b0 ea b5 c2 b2 b6 d5 cf a2 c9 a2 ac c7 d7 fa d0
  //   eb fa d2 b0 b2 b1 b1 a4 cc b1 d8 e3 a8 e8 cd fa d2 b0 b9 b8 b5 a4 cc b1 a8 e8 df a3 ae bb a3 a7 a3
  //   a3 b0 bc d8 df a7 e0 b6 ac b0 da f7 be d0 d7 ac cc dd e7 f0 ac b7 b3 c5 c5 ac b0 ab e3 f6 ac cc af
  //   b2 c7 ca 32 a3 b1 d3 ce a1 c9 c1 ca b4 d1 a1 a1
  //   比较器
  //   接收方
endmodule

// 奇校验编码
module \奇校验编码电路  (
  input  [7:0] \原始数据 ,
  output [8:0] \奇校验编码 
);

  wire xor_1_out, xor_2_out, xor_3_out, xor_4_out, xor_5_out, xor_6_out;

  xor xor_1 (xor_1_out, \原始数据 [0], \原始数据 [1]);
  xor xor_2 (xor_2_out, \原始数据 [2], \原始数据 [3]);
  xor xor_3 (xor_3_out, \原始数据 [4], \原始数据 [5]);
  xor xor_4 (xor_4_out, \原始数据 [6], \原始数据 [7]);
  xor xor_5 (xor_5_out, xor_1_out, xor_2_out);
  xor xor_6 (xor_6_out, xor_3_out, xor_4_out);
  xnor xnor_1 (\奇校验编码 [8], xor_5_out, xor_6_out);

  assign \奇校验编码 [7:0] = \原始数据 ;

  // Other names for the same wires on the sheet: D1 = \原始数据 [0]; data[7:0] = \原始数据 ; 校验码[8:0] = {\奇校验编码 [8], \原始数据 };
  //   D2 = \原始数据 [1]; D3 = \原始数据 [2]; D4 = \原始数据 [3]; D5 = \原始数据 [4]; D6 = \原始数据 [5]; D7 = \原始数据 [6]; D8 = \原始数据 [7]

  // Notes on the sheet:
  //   输入引脚区
  //   电路功能：实现8位数据位的奇校验编码
  //   输入：8位数据；输出：9位校验码（数据位+校验位）
  //   校验位
  //   奇校验编码电路
  //   输出引脚区
endmodule

// 奇校验检错
module \奇校验检错电路  (
  input  [8:0] \奇校验编码 ,
  output \检错位 ,
  output [7:0] \数据位 
);

  wire xnor_1_out, xor_1_out, xor_2_out, xor_3_out, xor_4_out, xor_5_out, xor_6_out;

  xor xor_1 (xor_1_out, \奇校验编码 [0], \奇校验编码 [1]);
  xor xor_2 (xor_2_out, \奇校验编码 [2], \奇校验编码 [3]);
  xor xor_3 (xor_3_out, \奇校验编码 [4], \奇校验编码 [5]);
  xor xor_4 (xor_4_out, \奇校验编码 [6], \奇校验编码 [7]);
  xor xor_5 (xor_5_out, xor_1_out, xor_2_out);
  xor xor_6 (xor_6_out, xor_3_out, xor_4_out);
  xnor xnor_1 (xnor_1_out, xor_5_out, xor_6_out);
  xor xor_7 (\检错位 , xnor_1_out, \奇校验编码 [8]);

  assign \数据位  = \奇校验编码 [7:0];

  // Other names for the same wires on the sheet: D1 = \奇校验编码 [0]; D2 = \奇校验编码 [1]; D3 = \奇校验编码 [2]; D4 = \奇校验编码 [3];
  //   D5 = \奇校验编码 [4]; D6 = \奇校验编码 [5]; D7 = \奇校验编码 [6]; D8 = \奇校验编码 [7]; P1 = \奇校验编码 [8]

  // Notes on the sheet:
  //   输入引脚区
  //   电路功能：实现9位奇校验编码的检错以及数据提取
  //   输入：奇校验编码；输出：检错位、数据位
  //   奇校验检错电路
  //   输出引脚区
endmodule

// 随机加扰
module \随机加扰电路  (
  input  CLK,
  input  [8:0] \_9位输入 ,
  output [8:0] \随机加扰屏蔽字 ,
  output [8:0] \加扰后数据 
);

  wire [3:0] \随机数_2_out , \随机数_3_out , \随机数_out ;
  wire [8:0] or_1_out;
  wire [15:0] decoder_1_out15, decoder_2_out15, decoder_3_out15;

  Random #(.width(4), .seed(0), .trigger("rising")) \u_随机数  (.clk(CLK), .out(\随机数_out ));  // open: next, clr
  Random #(.width(4), .seed(18), .trigger("rising")) \u_随机数_2  (.clk(CLK), .out(\随机数_2_out ));  // open: next, clr
  Random #(.width(4), .seed(3), .trigger("rising")) \u_随机数_3  (.clk(CLK), .out(\随机数_3_out ));  // open: next, clr
  Decoder #(.select(4), .tristate("false"), .disabled("Z"), .enable("false")) decoder_1 (
    .out0(decoder_1_out15[15]), .out1(decoder_1_out15[14]), .out2(decoder_1_out15[13]),
    .out3(decoder_1_out15[12]), .out4(decoder_1_out15[11]), .out5(decoder_1_out15[10]),
    .out6(decoder_1_out15[9]), .out7(decoder_1_out15[8]), .out8(decoder_1_out15[7]),
    .out9(decoder_1_out15[6]), .out10(decoder_1_out15[5]), .out11(decoder_1_out15[4]),
    .out12(decoder_1_out15[3]), .out13(decoder_1_out15[2]), .out14(decoder_1_out15[1]),
    .out15(decoder_1_out15[0]), .sel(\随机数_out ));
  Decoder #(.select(4), .tristate("false"), .disabled("Z"), .enable("false")) decoder_2 (
    .out0(decoder_2_out15[15]), .out1(decoder_2_out15[14]), .out2(decoder_2_out15[13]),
    .out3(decoder_2_out15[12]), .out4(decoder_2_out15[11]), .out5(decoder_2_out15[10]),
    .out6(decoder_2_out15[9]), .out7(decoder_2_out15[8]), .out8(decoder_2_out15[7]),
    .out9(decoder_2_out15[6]), .out10(decoder_2_out15[5]), .out11(decoder_2_out15[4]),
    .out12(decoder_2_out15[3]), .out13(decoder_2_out15[2]), .out14(decoder_2_out15[1]),
    .out15(decoder_2_out15[0]), .sel(\随机数_2_out ));
  Decoder #(.select(4), .tristate("false"), .disabled("Z"), .enable("false")) decoder_3 (
    .out0(decoder_3_out15[15]), .out1(decoder_3_out15[14]), .out2(decoder_3_out15[13]),
    .out3(decoder_3_out15[12]), .out4(decoder_3_out15[11]), .out5(decoder_3_out15[10]),
    .out6(decoder_3_out15[9]), .out7(decoder_3_out15[8]), .out8(decoder_3_out15[7]),
    .out9(decoder_3_out15[6]), .out10(decoder_3_out15[5]), .out11(decoder_3_out15[4]),
    .out12(decoder_3_out15[3]), .out13(decoder_3_out15[2]), .out14(decoder_3_out15[1]),
    .out15(decoder_3_out15[0]), .sel(\随机数_3_out ));
  assign or_1_out = decoder_1_out15[8:0] | decoder_2_out15[8:0];  // OR_Gate or_1, 9 bits wide
  assign \随机加扰屏蔽字  = or_1_out | decoder_3_out15[8:0];  // OR_Gate or_2, 9 bits wide
  assign \加扰后数据  = \随机加扰屏蔽字  ^ \_9位输入 ;  // XOR_Gate xor_1, 9 bits wide

  // Notes on the sheet:
  //   4-16译码器
  //   4-16译码器
  //   4-16译码器
  //   随机加扰电路
endmodule
