// Logisim project 32位快速加法器（组内并行、组间串行）.circ as structural Verilog: 6 circuits, main circuit 32位快速加法器（组内并行、组间串行）（1）
module \_4位先行进位电路  (
  input  G4,
  input  P4,
  input  G3,
  input  P3,
  input  G2,
  input  P2,
  input  G1,
  input  P1,
  input  Cin,
  output C4,
  output C3,
  output C2,
  output C1,
  output G_star,
  output P_star
);

  wire and_2_out, and_3_out, and_4_out, and_5_out, and_6_out, and_7_out, and_8_out, and_9_out, and_10_out,
       and_11_out;

  and and_1 (P_star, P4, P3, P2, P1);
  or or_1 (G_star, G4, and_3_out, and_2_out, and_4_out);
  and and_2 (and_2_out, P4, P3, G2);
  and and_3 (and_3_out, P4, G3);
  or or_2 (C4, G4, and_3_out, and_2_out, and_4_out, and_5_out);
  and and_4 (and_4_out, P4, P3, P2, G1);
  and and_5 (and_5_out, P4, P3, P2, P1, Cin);
  or or_3 (C3, G3, and_6_out, and_7_out, and_8_out);
  and and_6 (and_6_out, P3, G2);
  and and_7 (and_7_out, P3, P2, G1);
  and and_8 (and_8_out, P3, P2, P1, Cin);
  or or_4 (C2, G2, and_9_out, and_10_out);
  and and_9 (and_9_out, P2, G1);
  and and_10 (and_10_out, P2, P1, Cin);
  or or_5 (C1, G1, and_11_out);
  and and_11 (and_11_out, P1, Cin);

  // Notes on the sheet:
  //   G3: pull=down
  //   P2: pull=down
  //   G2: pull=down
  //   P3: pull=down
  //   P1: pull=down
  //   Cin: pull=down
  //   G4: pull=down
  //   P4: pull=down
  //   G1: pull=down
  //   输入引脚区
  //   请根据以上引脚以及隧道信号设计完成74LS182先行进位电路，尽可能使用多输入逻辑门，并分析电路延迟
  //   4位先行进位电路
  //   输出引脚区
endmodule

module \_4位快速加法器  (
  input  [3:0] X,
  input  [3:0] Y,
  input  C0,
  output [3:0] S,
  output C4,
  output C3,
  output G_star,
  output P_star
);

  wire and_1_out, and_2_out, and_3_out, and_4_out, \n4位先行进位电路_1_c1 , \n4位先行进位电路_1_c2 , xor_2_out, xor_3_out,
       xor_5_out, xor_8_out;

  \_4位先行进位电路  \u_4位先行进位电路_1  (
    .G4(and_1_out), .P4(xor_2_out), .G3(and_2_out), .P3(xor_3_out), .G2(and_3_out), .P2(xor_5_out),
    .G1(and_4_out), .P1(xor_8_out), .Cin(C0), .C4(C4), .C3(C3), .C2(\n4位先行进位电路_1_c2 ), .C1(\n4位先行进位电路_1_c1 ),
    .G_star(G_star), .P_star(P_star));
  and and_1 (and_1_out, X[3], Y[3]);
  xor xor_1 (S[3], C3, xor_2_out);
  xor xor_2 (xor_2_out, X[3], Y[3]);
  and and_2 (and_2_out, X[2], Y[2]);
  xor xor_3 (xor_3_out, X[2], Y[2]);
  xor xor_4 (S[2], \n4位先行进位电路_1_c2 , xor_3_out);
  and and_3 (and_3_out, X[1], Y[1]);
  xor xor_5 (xor_5_out, X[1], Y[1]);
  xor xor_6 (S[1], \n4位先行进位电路_1_c1 , xor_5_out);
  and and_4 (and_4_out, X[0], Y[0]);
  // Probe on X
  // Probe on Y
  // Probe on S
  xor xor_7 (S[0], xor_8_out, C0);
  xor xor_8 (xor_8_out, X[0], Y[0]);
  // Probe on X
  // Probe on Y
  // Probe on S

  // Notes on the sheet:
  //   C0: pull=down
  //   Y: pull=down
  //   X: pull=down
  //   输入引脚区
  //   输出引脚区
  //   功能说明:4位Adder  S=X+Y，C4、C3分别为最高位、次高位进位位，C0为进位输入， G* P*为成组进位生成传递函数
  //   4位快速加法器
  //   +
  //   =
  //   有符号加法
  //   +
  //   =
  //   无符号加法
endmodule

// 16位快速加法器
module \_16位快速加法器_组内并行_组间并行  (
  input  [15:0] X,
  input  [15:0] Y,
  input  C0,
  output C16,
  output C15,
  output G_star,
  output P_star,
  output [15:0] S
);

  wire \n4位先行进位电路_1_c1 , \n4位先行进位电路_1_c2 , \n4位先行进位电路_1_c3 , \n4位快速加法器_1_g_star , \n4位快速加法器_1_p_star ,
       \n4位快速加法器_2_g_star , \n4位快速加法器_2_p_star , \n4位快速加法器_3_g_star , \n4位快速加法器_3_p_star ,
       \n4位快速加法器_4_g_star , \n4位快速加法器_4_p_star ;

  \_4位先行进位电路  \u_4位先行进位电路_1  (
    .G4(\n4位快速加法器_1_g_star ), .P4(\n4位快速加法器_1_p_star ), .G3(\n4位快速加法器_2_g_star ), .P3(\n4位快速加法器_2_p_star ),
    .G2(\n4位快速加法器_3_g_star ), .P2(\n4位快速加法器_3_p_star ), .G1(\n4位快速加法器_4_g_star ), .P1(\n4位快速加法器_4_p_star ),
    .Cin(C0), .C4(C16), .C3(\n4位先行进位电路_1_c3 ), .C2(\n4位先行进位电路_1_c2 ), .C1(\n4位先行进位电路_1_c1 ), .G_star(G_star),
    .P_star(P_star));
  \_4位快速加法器  \u_4位快速加法器_1  (
    .X(X[15:12]), .Y(Y[15:12]), .C0(\n4位先行进位电路_1_c3 ), .S(S[15:12]), .G_star(\n4位快速加法器_1_g_star ),
    .P_star(\n4位快速加法器_1_p_star ), .C3(C15));  // open: C4
  \_4位快速加法器  \u_4位快速加法器_2  (
    .X(X[11:8]), .Y(Y[11:8]), .C0(\n4位先行进位电路_1_c2 ), .S(S[11:8]), .G_star(\n4位快速加法器_2_g_star ),
    .P_star(\n4位快速加法器_2_p_star ));  // open: C4, C3
  \_4位快速加法器  \u_4位快速加法器_3  (
    .X(X[7:4]), .Y(Y[7:4]), .C0(\n4位先行进位电路_1_c1 ), .S(S[7:4]), .G_star(\n4位快速加法器_3_g_star ),
    .P_star(\n4位快速加法器_3_p_star ));  // open: C4, C3
  // Probe on X
  // Probe on Y
  // Probe on S
  // Probe on X
  // Probe on Y
  // Probe on S
  \_4位快速加法器  \u_4位快速加法器_4  (
    .X(X[3:0]), .Y(Y[3:0]), .C0(C0), .S(S[3:0]), .G_star(\n4位快速加法器_4_g_star ), .P_star(\n4位快速加法器_4_p_star ));  // open: C4, C3

  // Other names for the same wires on the sheet: S0[3:0] = S[3:0]; S1[3:0] = S[7:4]; S2[3:0] = S[11:8];
  //   S3[3:0] = S[15:12]; X0[3:0] = X[3:0]; X1[3:0] = X[7:4]; X2[3:0] = X[11:8]; X3[3:0] = X[15:12]; Y0[3:0] = Y[3:0];
  //   Y1[3:0] = Y[7:4]; Y2[3:0] = Y[11:8]; Y3[3:0] = Y[15:12]

  // Notes on the sheet:
  //   X: pull=down
  //   C0: pull=down
  //   Y: pull=down
  //   输入引脚区
  //   输出引脚区
  //   功能说明：16位Adder  S=X＋Y，C16为最高位进位，C15为次高位进位，C0为进位输入， G* P*为成组进位生成传递函数
  //   16位快速加法器（组内并行、组间并行）
  //   +
  //   =
  //   有符号加法
  //   +
  //   =
  //   无符号加法
endmodule

// 16位快速加法器
module \_16位快速加法器_组内并行_组间串行  (
  input  [15:0] X,
  input  [15:0] Y,
  input  C0,
  output C16,
  output C15,
  output OF,
  output [15:0] S
);

  wire \n4位快速加法器_2_c4 , \n4位快速加法器_3_c4 , \n4位快速加法器_4_c4 ;

  xor xor_1 (OF, C16, C15);
  \_4位快速加法器  \u_4位快速加法器_1  (
    .X(X[15:12]), .Y(Y[15:12]), .C0(\n4位快速加法器_2_c4 ), .S(S[15:12]), .C4(C16), .C3(C15));  // open: G_star, P_star
  \_4位快速加法器  \u_4位快速加法器_2  (
    .X(X[11:8]), .Y(Y[11:8]), .C0(\n4位快速加法器_3_c4 ), .S(S[11:8]), .C4(\n4位快速加法器_2_c4 ));  // open: G_star, P_star, C3
  \_4位快速加法器  \u_4位快速加法器_3  (
    .X(X[7:4]), .Y(Y[7:4]), .C0(\n4位快速加法器_4_c4 ), .S(S[7:4]), .C4(\n4位快速加法器_3_c4 ));  // open: G_star, P_star, C3
  // Probe on X
  // Probe on Y
  // Probe on S
  \_4位快速加法器  \u_4位快速加法器_4  (
    .X(X[3:0]), .Y(Y[3:0]), .C0(C0), .S(S[3:0]), .C4(\n4位快速加法器_4_c4 ));  // open: G_star, P_star, C3
  // Probe on X
  // Probe on Y
  // Probe on S

  // Other names for the same wires on the sheet: S0[3:0] = S[3:0]; S1[3:0] = S[7:4]; S2[3:0] = S[11:8];
  //   S3[3:0] = S[15:12]; X0[3:0] = X[3:0]; X1[3:0] = X[7:4]; X2[3:0] = X[11:8]; X3[3:0] = X[15:12]; Y0[3:0] = Y[3:0];
  //   Y1[3:0] = Y[7:4]; Y2[3:0] = Y[11:8]; Y3[3:0] = Y[15:12]

  // Notes on the sheet:
  //   X: pull=down
  //   Y: pull=down
  //   C0: pull=down
  //   输入引脚区
  //   输出引脚区
  //   功能说明：16位快速加法器       输入：X、Y、C0        输出：S、C16、C15（最高数据位的进位）、OF（溢出标志）       
  //   16位快速加法器（组内并行、组间串行）
  //   +
  //   =
  //   有符号加法
  //   +
  //   =
  //   无符号加法
endmodule

module \_32位快速加法器_组内并行_组间串行__1  (
  input  [31:0] X,
  input  [31:0] Y,
  input  C0,
  output C32,
  output C31,
  output OF,
  output [31:0] S
);

  wire \n16位快速加法器_组内并行_组间并行_2_c16 ;

  xor xor_1 (OF, C32, C31);
  \_16位快速加法器_组内并行_组间并行  \u_16位快速加法器_组内并行_组间并行_1  (
    .X(X[31:16]), .Y(Y[31:16]), .C0(\n16位快速加法器_组内并行_组间并行_2_c16 ), .S(S[31:16]), .C16(C32), .C15(C31));  // open: G_star, P_star
  \_16位快速加法器_组内并行_组间并行  \u_16位快速加法器_组内并行_组间并行_2  (
    .X(X[15:0]), .Y(Y[15:0]), .C0(C0), .S(S[15:0]), .C16(\n16位快速加法器_组内并行_组间并行_2_c16 ));  // open: C15, G_star, P_star
  // Probe on X
  // Probe on Y
  // Probe on S
  // Probe on X
  // Probe on Y
  // Probe on S

  // Other names for the same wires on the sheet: S0[15:0] = S[15:0]; S1[15:0] = S[31:16]; X0[15:0] = X[15:0];
  //   X1[15:0] = X[31:16]; Y0[15:0] = Y[15:0]; Y1[15:0] = Y[31:16]

  // Notes on the sheet:
  //   C0: pull=down
  //   Y: pull=down
  //   X: pull=down
  //   输入引脚区
  //   输出引脚区
  //   功能说明：32位快速加法器               输入：X、Y、C0                输出：S、C32、C31（最高数据位的进位）、OF      
  //   32位快速加法器（组内并行、组间串行）
  //   （16位加法器采用：组内并行、组间并行）
  //   +
  //   =
  //   有符号加法
  //   +
  //   =
  //   无符号加法
endmodule

module \_32位快速加法器_组内并行_组间串行__2  (
  input  [31:0] X,
  input  [31:0] Y,
  input  C0,
  output C32,
  output C31,
  output OF,
  output [31:0] S
);

  wire \n16位快速加法器_组内并行_组间串行_2_c16 ;

  xor xor_1 (OF, C32, C31);
  \_16位快速加法器_组内并行_组间串行  \u_16位快速加法器_组内并行_组间串行_1  (
    .X(X[31:16]), .Y(Y[31:16]), .C0(\n16位快速加法器_组内并行_组间串行_2_c16 ), .S(S[31:16]), .C16(C32), .C15(C31));  // open: OF
  \_16位快速加法器_组内并行_组间串行  \u_16位快速加法器_组内并行_组间串行_2  (
    .X(X[15:0]), .Y(Y[15:0]), .C0(C0), .S(S[15:0]), .C16(\n16位快速加法器_组内并行_组间串行_2_c16 ));  // open: C15, OF
  // Probe on X
  // Probe on Y
  // Probe on S
  // Probe on X
  // Probe on Y
  // Probe on S

  // Other names for the same wires on the sheet: S0[15:0] = S[15:0]; S1[15:0] = S[31:16]; X0[15:0] = X[15:0];
  //   X1[15:0] = X[31:16]; Y0[15:0] = Y[15:0]; Y1[15:0] = Y[31:16]

  // Notes on the sheet:
  //   Y: pull=down
  //   X: pull=down
  //   C0: pull=down
  //   输入引脚区
  //   输出引脚区
  //   功能说明：32位快速加法器               输入：X、Y、C0                输出：S、C32、C31（最高数据位的进位）、OF      
  //   32位快速加法器（组内并行、组间串行）
  //   （16位加法器采用：组内并行、组间串行）
  //   +
  //   =
  //   有符号加法
  //   +
  //   =
  //   无符号加法
endmodule
