// Logisim project 8位原码一位乘法器.circ as structural Verilog: 9 circuits, main circuit 1位全加器（FA）
// 8位无符号一位乘法器
module \_8位无符号数一位乘法器  (
  input  [7:0] X,
  input  [7:0] Y,
  output [15:0] \乘积 
);

  wire CLK, comparator_1_eq, d_ff_1_q, END, not_1_out, RST;
  wire [0:0] \n8位串行加法器_1_s ;
  wire [3:0] counter_1_q;
  wire [7:0] multiplexer_1_out, multiplexer_2_out, \n8位串行加法器_1_cout ;

  Button \u_复位  (.out(RST));
  // Probe on \乘积 [15:8]
  Register #(.width(8), .trigger("rising"), .Select("low")) register_1 (
    .D(\n8位串行加法器_1_cout ), .en(not_1_out), .Q(\乘积 [15:8]), .clk(CLK), .clr(RST));
  \_8位串行加法器  \u_8位串行加法器_1  (
    .X(\乘积 [15:8]), .Y(multiplexer_1_out), .Cin(1'b0), .S({\n8位串行加法器_1_cout [6:0], \n8位串行加法器_1_s [0]}),
    .Cout(\n8位串行加法器_1_cout [7]));  // open: out_6
  Multiplexer #(.select(1), .width(8), .disabled("Z"), .enable("false")) multiplexer_1 (
    .in0({8{1'b0}}), .in1(X), .out(multiplexer_1_out), .sel(\乘积 [0]));
  Button u_CLK (.out(CLK));
  Multiplexer #(.select(1), .width(8), .disabled("Z"), .enable("false")) multiplexer_2 (
    .in0(Y), .in1({\n8位串行加法器_1_s [0], \乘积 [7:1]}), .out(multiplexer_2_out), .sel(d_ff_1_q));
  // Probe on \乘积 [7:0]
  Register #(.width(8), .trigger("rising"), .Select("low")) Y_2 (
    .D(multiplexer_2_out), .en(not_1_out), .Q(\乘积 [7:0]), .clk(CLK), .clr(RST));
  Counter #(.width(4), .max('hf), .ongoal("wrap"), .trigger("rising"), .behavior("old")) counter_1 (
    .count(not_1_out), .Q(counter_1_q), .clk(CLK), .clr(RST));  // open: load, D, carry, preset
  D_Flip_Flop #(.trigger("rising"), .Pre_Clr_Positions("LEGACY"), .NegatePresetClear("false"), .enable("true"), .NewFFLayout("false")) d_ff_1 (
    .clk(CLK), .D(1'b1), .Q(d_ff_1_q), .reset(RST));  // open: Qn, preset, en
  Comparator #(.width(4), .mode("unsigned")) comparator_1 (
    .a(counter_1_q), .b(4'b1001), .eq(comparator_1_eq));  // open: gt, lt
  not not_1 (not_1_out, comparator_1_eq);
  LED #(.active("true")) led_1 (.in(END));
  not not_2 (END, not_1_out);
  // Probe on X
  // Probe on Y
  // Probe on \乘积 

  // Notes on the sheet:
  //   输入引脚区
  //   ∑
  //   功能说明: 8位无符号数一位乘法器                输入：X、Y 为8位无符号数               输出：乘积=X*Y 为16位无符号数
  //   首先设置X、Y值，然后按“复位”按钮，接下去按“CLK”按钮多次，直到“END”指示灯变红，此时观看乘积是不是正确？
  //   8位无符号数一位乘法器
  //   输出引脚区
  //   ×
  //   =
endmodule

module \_8位原码一位乘法器  (
  input  [7:0] X,
  input  [7:0] Y,
  output [15:0] \乘积 ,
  output [7:0] out_4,
  output [7:0] out_5
);

  wire CLK, comparator_1_eq, d_ff_1_q, END, not_2_out, RST;
  wire [0:0] \n8位串行加法器_1_s ;
  wire [3:0] counter_1_q;
  wire [7:0] multiplexer_1_out, multiplexer_2_out, \n8位串行加法器_1_cout , \X真值 , \Y真值 ;
  wire [15:0] \乘积真值 ;
  wire [15:15] \乘积真值1 ;

  \_8位原码转补码  \u_8位原码转补码_1  (.X(Y), .XBUMA(\Y真值 ));
  \_8位原码转补码  \u_8位原码转补码_2  (.X(X), .XBUMA(\X真值 ));
  xor xor_1 (\乘积真值1 [15], Y[7], X[7]);
  \_16位原码转补码  \u_16位原码转补码_1  (.X({\乘积真值1 [15], \乘积 [14:0]}), .XBUMA(\乘积真值 ));
  Button \u_复位  (.out(RST));
  Button u_CLK (.out(CLK));
  Register #(.width(8), .trigger("rising"), .Select("low")) register_1 (
    .D(\n8位串行加法器_1_cout ), .en(not_2_out), .Q(\乘积 [15:8]), .clk(CLK), .clr(RST));
  \_8位串行加法器  \u_8位串行加法器_1  (
    .X(\乘积 [15:8]), .Y(multiplexer_1_out), .Cin(1'b0), .S({\n8位串行加法器_1_cout [6:0], \n8位串行加法器_1_s [0]}),
    .Cout(\n8位串行加法器_1_cout [7]));  // open: out_6
  Multiplexer #(.select(1), .width(8), .disabled("Z"), .enable("false")) multiplexer_1 (
    .in0({8{1'b0}}), .in1({1'b0, X[6:0]}), .out(multiplexer_1_out), .sel(\乘积 [0]));
  // Probe on \乘积 [15:8]
  Multiplexer #(.select(1), .width(8), .disabled("Z"), .enable("false")) multiplexer_2 (
    .in0({1'b0, Y[6:0]}), .in1({\n8位串行加法器_1_s [0], \乘积 [7:1]}), .out(multiplexer_2_out), .sel(d_ff_1_q));
  LED #(.active("true")) led_1 (.in(END));
  // Probe on \乘积 [7:0]
  Register #(.width(8), .trigger("rising"), .Select("low")) Y_2 (
    .D(multiplexer_2_out), .en(not_2_out), .Q(\乘积 [7:0]), .clk(CLK), .clr(RST));
  not not_1 (END, not_2_out);
  Counter #(.width(4), .max('hf), .ongoal("wrap"), .trigger("rising"), .behavior("old")) counter_1 (
    .count(not_2_out), .Q(counter_1_q), .clk(CLK), .clr(RST));  // open: load, D, carry, preset
  not not_2 (not_2_out, comparator_1_eq);
  Comparator #(.width(4), .mode("unsigned")) comparator_1 (
    .a(counter_1_q), .b(4'b1001), .eq(comparator_1_eq));  // open: gt, lt
  D_Flip_Flop #(.trigger("rising"), .Pre_Clr_Positions("LEGACY"), .NegatePresetClear("false"), .enable("true"), .NewFFLayout("false")) d_ff_1 (
    .clk(CLK), .D(1'b1), .Q(d_ff_1_q), .reset(RST));  // open: Qn, preset, en
  // Probe on \乘积真值 
  // Probe on \X真值 
  // Probe on \Y真值 

  assign out_4 = {1'b0, X[6:0]};
  assign out_5 = {1'b0, Y[6:0]};

  // Other names for the same wires on the sheet: X_0[6:0] = X[6:0]; X_t[6:0] = X[6:0]; Y_0[6:0] = Y[6:0];
  //   Y_t[6:0] = Y[6:0]; 乘积真值1[14:0] = \乘积 [14:0]

  // Notes on the sheet:
  //   输入引脚区
  //   功能说明: 8位原码一位乘法器                输入：X、Y为 8位原码               输出：乘积=X*Y 为16位原码
  //   8位原码一位乘法器
  //   首先设置X、Y值，然后按“复位”按钮，接下去按“CLK”按钮多次，直到“END”指示灯变红，此时观看乘积是不是正确？
  //   ∑
  //   输出引脚区
  //   ×
  //   =
endmodule

module \_8位补码一位乘法器_简化版  (
  input  [7:0] X,
  input  [7:0] Y,
  output [15:0] \乘积 
);

  wire and_1_out, CLK, comparator_1_eq, comparator_2_eq, d_ff_1_q, END, not_3_out, RST;
  wire [0:0] \n8位串行加法器_1_s_2 ;
  wire [1:1] Yn_1_2_q;
  wire [3:0] counter_1_q;
  wire [7:0] multiplexer_1_out, multiplexer_2_out, \n8位串行加法器_1_s , not_1_out;
  wire [15:0] negator_1_out, \乘积_star ;

  Register #(.width(8), .trigger("rising"), .Select("low")) register (
    .D({{2{\n8位串行加法器_1_s [7]}}, \n8位串行加法器_1_s [5:0]}), .en(not_3_out), .Q(\乘积_star [15:8]), .clk(CLK),
    .clr(RST));
  assign not_1_out = ~X;  // NOT_Gate not_1, 8 bits wide
  // Probe on \乘积_star [15:8]
  Multiplexer #(.select(1), .width(8), .disabled("Z"), .enable("false")) multiplexer_1 (
    .in0(Y), .in1({\n8位串行加法器_1_s_2 [0], \乘积_star [7:1]}), .out(multiplexer_1_out), .sel(d_ff_1_q));
  \_8位串行加法器  \u_8位串行加法器_1  (
    .X(\乘积_star [15:8]), .Y(multiplexer_2_out), .Cin(and_1_out),
    .S({\n8位串行加法器_1_s [7], \n8位串行加法器_1_s [5:0], \n8位串行加法器_1_s_2 [0]}));  // open: Cout, out_6
  Multiplexer #(.select(2), .width(8), .disabled("Z"), .enable("false")) multiplexer_2 (
    .in0({8{1'b0}}), .in1(not_1_out), .in2(X), .in3({8{1'b0}}), .out(multiplexer_2_out),
    .sel({Yn_1_2_q[1], \乘积_star [0]}));
  Button \u_复位  (.out(RST));
  // Probe on \乘积_star [7:0]
  Register #(.width(8), .trigger("rising"), .Select("low")) Y_2 (
    .D(multiplexer_1_out), .en(not_3_out), .Q(\乘积_star [7:0]), .clk(CLK), .clr(RST));
  and and_1 (and_1_out, ~Yn_1_2_q[1], \乘积_star [0]);  // AND_Gate
  Counter #(.width(4), .max('hf), .ongoal("wrap"), .trigger("rising"), .behavior("old")) counter_1 (
    .count(not_3_out), .Q(counter_1_q), .clk(CLK), .clr(RST));  // open: load, D, carry, preset
  // Probe on Yn_1_2_q[1]
  Register #(.width(1), .trigger("rising"), .Select("low")) Yn_1_2 (
    .D(\乘积_star [0]), .en(not_3_out), .Q(Yn_1_2_q[1]), .clk(CLK), .clr(RST));
  Comparator #(.width(4), .mode("unsigned")) comparator_1 (
    .a(counter_1_q), .b(4'b1001), .eq(comparator_1_eq));  // open: gt, lt
  D_Flip_Flop #(.trigger("rising"), .Pre_Clr_Positions("LEGACY"), .NegatePresetClear("false"), .enable("true"), .NewFFLayout("false")) d_ff_1 (
    .clk(CLK), .D(1'b1), .Q(d_ff_1_q), .reset(RST));  // open: Qn, preset, en
  Button \u_时钟  (.out(CLK));
  not not_2 (END, not_3_out);
  not not_3 (not_3_out, comparator_1_eq);
  // Probe on \乘积_star 
  // Probe on \乘积_star 
  LED #(.active("true")) led_1 (.in(END));
  Negator #(.width(16)) negator_1 (.in(\乘积_star ), .out(negator_1_out));
  Comparator #(.width(8), .mode("twosComplement")) comparator_2 (
    .a(X), .b(8'h80), .eq(comparator_2_eq));  // open: gt, lt
  Multiplexer #(.select(1), .width(16), .disabled("Z"), .enable("false")) multiplexer_3 (
    .in0(\乘积_star ), .in1(negator_1_out), .out(\乘积 ), .sel(comparator_2_eq));
  // Probe on X
  // Probe on Y
  // Probe on \乘积 
  // Probe on \乘积 

  // Notes on the sheet:
  //   输入引脚区
  //   功能说明: 8位补码一位乘法器                输入：X、Y 为8位补码               输出：乘积=X*Y 为16位补码
  //   首先设置X、Y值，然后按“复位”按钮，接下去按“CLK”按钮多次，直到“END”指示灯变红，此时观看乘积是不是正确？
  //   8位补码一位乘法器（简化版）
  //   输出引脚区
  //   ×
  //   =
endmodule

module \_8位补码一位乘法器_复杂版  (
  input  [7:0] X,
  input  [7:0] Y,
  output [15:0] \乘积 
);

  wire and_1_out, CLK, comparator_1_eq, d_ff_1_q, END, not_3_out, RST, XYZ, XZ, YZ;
  wire [0:0] \n8位串行加法器_1_s_2 ;
  wire [1:0] PS;
  wire [1:1] Yn_1_2_q;
  wire [3:0] counter_1_q;
  wire [7:0] multiplexer_1_out, multiplexer_2_out, \n8位串行加法器_1_s , not_1_out;
  wire [14:0] PX_star, PY_star;
  wire [15:0] multiplexer_3_out, P_star;
  wire [15:15] negator_1_out, negator_2_out, PX;

  // Probe on X
  Register #(.width(8), .trigger("rising"), .Select("low")) register (
    .D({{2{\n8位串行加法器_1_s [7]}}, \n8位串行加法器_1_s [5:0]}), .en(not_3_out), .Q(P_star[15:8]), .clk(CLK), .clr(RST));
  assign not_1_out = ~X;  // NOT_Gate not_1, 8 bits wide
  // Probe on Y
  // Probe on P_star[15:8]
  Multiplexer #(.select(1), .width(8), .disabled("Z"), .enable("false")) multiplexer_1 (
    .in0(Y), .in1({\n8位串行加法器_1_s_2 [0], P_star[7:1]}), .out(multiplexer_1_out), .sel(d_ff_1_q));
  \_8位串行加法器  \u_8位串行加法器_1  (
    .X(P_star[15:8]), .Y(multiplexer_2_out), .Cin(and_1_out),
    .S({\n8位串行加法器_1_s [7], \n8位串行加法器_1_s [5:0], \n8位串行加法器_1_s_2 [0]}));  // open: Cout, out_6
  Multiplexer #(.select(2), .width(8), .disabled("Z"), .enable("false")) multiplexer_2 (
    .in0({8{1'b0}}), .in1(not_1_out), .in2(X), .in3({8{1'b0}}), .out(multiplexer_2_out),
    .sel({Yn_1_2_q[1], P_star[0]}));
  Button \u_复位  (.out(RST));
  // Probe on P_star[7:0]
  Register #(.width(8), .trigger("rising"), .Select("low")) Y_2 (
    .D(multiplexer_1_out), .en(not_3_out), .Q(P_star[7:0]), .clk(CLK), .clr(RST));
  and and_1 (and_1_out, ~Yn_1_2_q[1], P_star[0]);  // AND_Gate
  Counter #(.width(4), .max('hf), .ongoal("wrap"), .trigger("rising"), .behavior("old")) counter_1 (
    .count(not_3_out), .Q(counter_1_q), .clk(CLK), .clr(RST));  // open: load, D, carry, preset
  // Probe on Yn_1_2_q[1]
  Register #(.width(1), .trigger("rising"), .Select("low")) Yn_1_2 (
    .D(P_star[0]), .en(not_3_out), .Q(Yn_1_2_q[1]), .clk(CLK), .clr(RST));
  Comparator #(.width(4), .mode("unsigned")) comparator_1 (
    .a(counter_1_q), .b(4'b1001), .eq(comparator_1_eq));  // open: gt, lt
  D_Flip_Flop #(.trigger("rising"), .Pre_Clr_Positions("LEGACY"), .NegatePresetClear("false"), .enable("true"), .NewFFLayout("false")) d_ff_1 (
    .clk(CLK), .D(1'b1), .Q(d_ff_1_q), .reset(RST));  // open: Qn, preset, en
  Button \u_时钟  (.out(CLK));
  not not_2 (END, not_3_out);
  not not_3 (not_3_out, comparator_1_eq);
  // Probe on \乘积 
  xor xor_1 (XYZ, XZ, YZ);
  Negator #(.width(16)) negator_1 (.in({PX[15], X, {7{1'b0}}}), .out({negator_1_out[15], PX_star}));
  Comparator #(.width(8), .mode("twosComplement")) comparator_2 (.a(X), .b(8'h80), .eq(PS[0]));  // open: gt, lt
  Comparator #(.width(8), .mode("twosComplement")) comparator_3 (.a(Y), .b(8'h80), .eq(PS[1]));  // open: gt, lt
  or or_1 (XZ, X[0], X[1], X[2], X[3], X[4], X[5], X[6], X[7]);
  LED #(.active("true")) led_1 (.in(END));
  xor xor_2 (PX[15], X[7], Y[7]);
  Negator #(.width(16)) negator_2 (.in({PX[15], Y, {7{1'b0}}}), .out({negator_2_out[15], PY_star}));
  Multiplexer #(.select(2), .width(16), .disabled("Z"), .enable("false")) multiplexer_3 (
    .in0(P_star), .in1({PX[15], PY_star}), .in2({PX[15], PX_star}), .in3(16'h4000), .out(multiplexer_3_out),
    .sel(PS));
  // Probe on X
  // Probe on Y
  // Probe on \乘积 
  or or_2 (YZ, Y[0], Y[1], Y[2], Y[3], Y[4], Y[5], Y[6], Y[7]);
  Multiplexer #(.select(1), .width(16), .disabled("Z"), .enable("false")) multiplexer_4 (
    .in0(multiplexer_3_out), .in1({16{1'b0}}), .out(\乘积 ), .sel(XYZ));

  // Other names for the same wires on the sheet: P[15:0] = \乘积 ; PX[14:7] = X; SX = X[7]; PY[15:7] = {PX[15], Y};
  //   SY = Y[7]; PX_star[15] = PX[15]; PY_star[15] = PX[15]; SP = PX[15]

  // Notes on the sheet:
  //   输入引脚区
  //   功能说明: 8位补码一位乘法器                输入：X、Y 为8位补码               输出：乘积=X*Y 为16位补码
  //   首先设置X、Y值，然后按“复位”按钮，接下去按“CLK”按钮多次，直到“END”指示灯变红，此时观看乘积是不是正确？
  //   8位补码一位乘法器（复杂版）
  //   输出引脚区
  //   ×
  //   =
endmodule

module \_8位补码一位乘法器_用8位无符号数一位乘法器实现  (
  input  [7:0] X,
  input  [7:0] Y,
  output [15:0] \乘积 
);

  wire CLK, END, RST;

  // Probe on X
  // Probe on Y
  Button \u_复位  (.out(RST));
  Button \u_时钟  (.out(CLK));
  // Probe on \乘积 
  LED #(.active("true")) led_1 (.in(END));
  // Probe on X
  // Probe on Y
  // Probe on \乘积 

  // Notes on the sheet:
  //   输入引脚区
  //   首先设置X、Y值，然后按“复位”按钮，接下去按“CLK”按钮多次，直到“END”指示灯变红，此时观看乘积是不是正确？
  //   功能说明: 8位补码一位乘法器（用8位无符号数一位乘法器实现）                输入：X、Y 为8位补码               输出：乘积=X*Y 为16位补码
  //   请同学们在此处设计电路！
  //   8位补码一位乘法器（用8位无符号数一位乘法器实现）
  //   输出引脚区
  //   ×
  //   =
endmodule

module \_8位串行加法器  (
  input  [7:0] X,
  input  [7:0] Y,
  input  Cin,
  output [7:0] S,
  output Cout,
  output out_6
);

  wire \n1位全加器_fa_2_cout , \n1位全加器_fa_3_cout , \n1位全加器_fa_4_cout , \n1位全加器_fa_5_cout , \n1位全加器_fa_6_cout ,
       \n1位全加器_fa_7_cout , \n1位全加器_fa_8_cout ;

  xor xor_1 (out_6, Cout, \n1位全加器_fa_2_cout );
  \_1位全加器_FA  \u_1位全加器_fa_1  (.Cout(Cout), .Si(S[7]), .Cin(\n1位全加器_fa_2_cout ), .Xi(X[7]), .Yi(Y[7]));
  \_1位全加器_FA  \u_1位全加器_fa_2  (.Cout(\n1位全加器_fa_2_cout ), .Si(S[6]), .Cin(\n1位全加器_fa_3_cout ), .Xi(X[6]), .Yi(Y[6]));
  \_1位全加器_FA  \u_1位全加器_fa_3  (.Cout(\n1位全加器_fa_3_cout ), .Si(S[5]), .Cin(\n1位全加器_fa_4_cout ), .Xi(X[5]), .Yi(Y[5]));
  \_1位全加器_FA  \u_1位全加器_fa_4  (.Cout(\n1位全加器_fa_4_cout ), .Si(S[4]), .Cin(\n1位全加器_fa_5_cout ), .Xi(X[4]), .Yi(Y[4]));
  \_1位全加器_FA  \u_1位全加器_fa_5  (.Cout(\n1位全加器_fa_5_cout ), .Si(S[3]), .Cin(\n1位全加器_fa_6_cout ), .Xi(X[3]), .Yi(Y[3]));
  \_1位全加器_FA  \u_1位全加器_fa_6  (.Cout(\n1位全加器_fa_6_cout ), .Si(S[2]), .Cin(\n1位全加器_fa_7_cout ), .Xi(X[2]), .Yi(Y[2]));
  // Probe on X
  // Probe on Y
  // Probe on S
  \_1位全加器_FA  \u_1位全加器_fa_7  (.Cout(\n1位全加器_fa_7_cout ), .Si(S[1]), .Cin(\n1位全加器_fa_8_cout ), .Xi(X[1]), .Yi(Y[1]));
  // Probe on X
  // Probe on Y
  // Probe on S
  \_1位全加器_FA  \u_1位全加器_fa_8  (.Cout(\n1位全加器_fa_8_cout ), .Si(S[0]), .Cin(Cin), .Xi(X[0]), .Yi(Y[0]));

  // Other names for the same wires on the sheet: OF = out_6

  // Notes on the sheet:
  //   X: pull=down
  //   Y: pull=down
  //   Cin: pull=down
  //   输入引脚区
  //   符号位
  //   输出引脚区
  //   8位串行加法器
  //   OF
  //   +
  //   有符号加法
  //   +
  //   =
  //   无符号加法
endmodule

// FA
module \_1位全加器_FA  (
  input  Cin,
  input  Xi,
  input  Yi,
  output Cout,
  output Si
);

  wire AND_2_out, AND_out, XOR_2_out;

  and AND (AND_out, Xi, Yi);
  or OR (Cout, AND_out, AND_2_out);
  and AND_2 (AND_2_out, Cin, XOR_2_out);
  xor XOR (Si, Cin, XOR_2_out);
  xor XOR_2 (XOR_2_out, Xi, Yi);

  // Notes on the sheet:
  //   Yi: pull=down
  //   Cin: pull=down
  //   Xi: pull=down
  //   Cout = Xi Yi + Cin (Xi ^ Yi)
  //   Si = Xi ^ Yi ^ Cin
  //   1位全加器（FA）
endmodule

module \_8位原码转补码  (
  input  [7:0] X,
  output [7:0] XBUMA
);

  wire and_1_out, and_2_out, and_3_out, and_4_out, and_5_out, and_6_out, and_7_out, xor_1_out, xor_3_out,
       xor_5_out, xor_7_out, xor_9_out, xor_11_out, xor_13_out;

  xor xor_1 (xor_1_out, X[0], X[7]);
  xor xor_2 (XBUMA[0], X[7], xor_1_out);
  xor xor_3 (xor_3_out, X[1], X[7]);
  and and_1 (and_1_out, xor_1_out, X[7]);
  xor xor_4 (XBUMA[1], xor_3_out, and_1_out);
  xor xor_5 (xor_5_out, X[2], X[7]);
  and and_2 (and_2_out, and_1_out, xor_3_out);
  xor xor_6 (XBUMA[2], xor_5_out, and_2_out);
  xor xor_7 (xor_7_out, X[3], X[7]);
  and and_3 (and_3_out, and_2_out, xor_5_out);
  xor xor_8 (XBUMA[3], xor_7_out, and_3_out);
  and and_4 (and_4_out, and_3_out, xor_7_out);
  xor xor_9 (xor_9_out, X[4], X[7]);
  xor xor_10 (XBUMA[4], xor_9_out, and_4_out);
  xor xor_11 (xor_11_out, X[5], X[7]);
  and and_5 (and_5_out, and_4_out, xor_9_out);
  xor xor_12 (XBUMA[5], xor_11_out, and_5_out);
  and and_6 (and_6_out, and_5_out, xor_11_out);
  xor xor_13 (xor_13_out, X[6], X[7]);
  xor xor_14 (XBUMA[6], xor_13_out, and_6_out);
  and and_7 (and_7_out, and_6_out, xor_13_out);
  or or_1 (XBUMA[7], and_7_out, X[7]);

  // Other names for the same wires on the sheet: X补码[7:0] = XBUMA
endmodule

module \_16位原码转补码  (
  input  [15:0] X,
  output [15:0] XBUMA
);

  wire and_1_out, and_2_out, and_3_out, and_4_out, and_5_out, and_6_out, and_7_out, and_8_out, and_9_out,
       and_10_out, and_11_out, and_12_out, and_13_out, and_14_out, and_15_out, xor_1_out, xor_3_out,
       xor_5_out, xor_7_out, xor_9_out, xor_11_out, xor_13_out, xor_15_out, xor_17_out, xor_19_out,
       xor_21_out, xor_23_out, xor_25_out, xor_27_out, xor_29_out;

  xor xor_1 (xor_1_out, X[0], X[15]);
  xor xor_2 (XBUMA[0], X[15], xor_1_out);
  and and_1 (and_1_out, xor_1_out, X[15]);
  xor xor_3 (xor_3_out, X[1], X[15]);
  xor xor_4 (XBUMA[1], xor_3_out, and_1_out);
  xor xor_5 (xor_5_out, X[2], X[15]);
  and and_2 (and_2_out, and_1_out, xor_3_out);
  xor xor_6 (XBUMA[2], xor_5_out, and_2_out);
  and and_3 (and_3_out, and_2_out, xor_5_out);
  xor xor_7 (xor_7_out, X[3], X[15]);
  and and_4 (and_4_out, and_3_out, xor_7_out);
  xor xor_8 (XBUMA[3], xor_7_out, and_3_out);
  xor xor_9 (xor_9_out, X[4], X[15]);
  xor xor_10 (XBUMA[4], xor_9_out, and_4_out);
  and and_5 (and_5_out, and_4_out, xor_9_out);
  xor xor_11 (xor_11_out, X[5], X[15]);
  xor xor_12 (XBUMA[5], xor_11_out, and_5_out);
  xor xor_13 (xor_13_out, X[6], X[15]);
  and and_6 (and_6_out, and_5_out, xor_11_out);
  xor xor_14 (XBUMA[6], xor_13_out, and_6_out);
  and and_7 (and_7_out, and_6_out, xor_13_out);
  xor xor_15 (xor_15_out, X[7], X[15]);
  and and_8 (and_8_out, and_7_out, xor_15_out);
  xor xor_16 (XBUMA[7], xor_15_out, and_7_out);
  xor xor_17 (xor_17_out, X[8], X[15]);
  xor xor_18 (XBUMA[8], xor_17_out, and_8_out);
  xor xor_19 (xor_19_out, X[9], X[15]);
  and and_9 (and_9_out, and_8_out, xor_17_out);
  xor xor_20 (XBUMA[9], xor_19_out, and_9_out);
  and and_10 (and_10_out, and_9_out, xor_19_out);
  xor xor_21 (xor_21_out, X[10], X[15]);
  and and_11 (and_11_out, and_10_out, xor_21_out);
  xor xor_22 (XBUMA[10], xor_21_out, and_10_out);
  xor xor_23 (xor_23_out, X[11], X[15]);
  xor xor_24 (XBUMA[11], xor_23_out, and_11_out);
  xor xor_25 (xor_25_out, X[12], X[15]);
  and and_12 (and_12_out, and_11_out, xor_23_out);
  xor xor_26 (XBUMA[12], xor_25_out, and_12_out);
  and and_13 (and_13_out, and_12_out, xor_25_out);
  xor xor_27 (xor_27_out, X[13], X[15]);
  xor xor_28 (XBUMA[13], xor_27_out, and_13_out);
  xor xor_29 (xor_29_out, X[14], X[15]);
  and and_14 (and_14_out, and_13_out, xor_27_out);
  xor xor_30 (XBUMA[14], xor_29_out, and_14_out);
  and and_15 (and_15_out, and_14_out, xor_29_out);
  or or_1 (XBUMA[15], and_15_out, X[15]);

  // Other names for the same wires on the sheet: X补码[15:0] = XBUMA
endmodule
