// Logisim project 寄存器文件设计实验.circ as structural Verilog: 4 circuits, main circuit 寄存器文件电路（4个寄存器）
module \寄存器文件电路_4个寄存器  (
  input  [1:0] in_1,
  input  [1:0] in_2,
  input  [31:0] in_3,
  input  [1:0] in_4,
  input  in_5,
  input  in_6,
  output [31:0] out_7,
  output [31:0] out_8
);

  wire demultiplexer_1_out0, demultiplexer_1_out1, demultiplexer_1_out2, demultiplexer_1_out3;
  wire [31:0] register_1_q, register_2_q, register_3_q, register_4_q;

  Demultiplexer #(.select(2), .width(1), .tristate("false"), .disabled("Z"), .enable("false")) demultiplexer_1 (
    .out0(demultiplexer_1_out0), .out1(demultiplexer_1_out1), .out2(demultiplexer_1_out2),
    .out3(demultiplexer_1_out3), .in(in_5), .sel(in_4));
  Register #(.width(32), .trigger("rising"), .Select("low")) register_1 (
    .D(in_3), .en(demultiplexer_1_out0), .Q(register_1_q), .clk(in_6));  // open: clr
  Register #(.width(32), .trigger("rising"), .Select("low")) register_2 (
    .D(in_3), .en(demultiplexer_1_out1), .Q(register_2_q), .clk(in_6));  // open: clr
  Register #(.width(32), .trigger("rising"), .Select("low")) register_3 (
    .D(in_3), .en(demultiplexer_1_out2), .Q(register_3_q), .clk(in_6));  // open: clr
  Register #(.width(32), .trigger("rising"), .Select("low")) register_4 (
    .D(in_3), .en(demultiplexer_1_out3), .Q(register_4_q), .clk(in_6));  // open: clr
  Multiplexer #(.select(2), .width(32), .disabled("Z"), .enable("false")) multiplexer_1 (
    .in0(register_1_q), .in1(register_2_q), .in2(register_3_q), .in3(register_4_q), .out(out_7), .sel(in_1));
  Multiplexer #(.select(2), .width(32), .disabled("Z"), .enable("false")) multiplexer_2 (
    .in0(register_1_q), .in1(register_2_q), .in2(register_3_q), .in3(register_4_q), .out(out_8), .sel(in_2));

  // Other names for the same wires on the sheet: CLK = in_6; Din[31:0] = in_3; R1_num[1:0] = in_1; R2_num[1:0] = in_2;
  //   RD1[31:0] = out_7; RD2[31:0] = out_8; W_num[1:0] = in_4; WE = in_5

  // Notes on the sheet:
  //   输入引脚
  //   寄存器文件电路（4个寄存器）
  //   输出引脚
endmodule

module \寄存器文件电路_4个寄存器_测试电路  (
  input  [1:0] R1_num,
  input  [1:0] R2_num,
  input  [1:0] W_num,
  input  WE,
  input  [31:0] Din,
  output [31:0] RD1,
  output [31:0] RD2
);

  wire clock_1_out;

  // Probe on Din
  Clock #(.highDuration(1), .lowDuration(1)) clock_1 (.out(clock_1_out));
  // Probe on RD1
  \寄存器文件电路_4个寄存器  \u_寄存器文件电路_4个寄存器_1  (
    .in_1(R1_num), .in_2(R2_num), .in_3(Din), .in_4(W_num), .in_5(WE), .in_6(clock_1_out), .out_7(RD1),
    .out_8(RD2));
  // Probe on RD2
endmodule

module \寄存器文件电路_4个寄存器_R0_0  (
  input  [1:0] in_1,
  input  [1:0] in_2,
  input  [31:0] in_3,
  input  [1:0] in_4,
  input  in_5,
  input  in_6,
  output [31:0] out_7,
  output [31:0] out_8
);

  wire demultiplexer_1_out0, demultiplexer_1_out1, demultiplexer_1_out2, demultiplexer_1_out3;
  wire [31:0] register_1_q, register_2_q, register_3_q, register_4_q;

  Demultiplexer #(.select(2), .width(1), .tristate("false"), .disabled("Z"), .enable("false")) demultiplexer_1 (
    .out0(demultiplexer_1_out0), .out1(demultiplexer_1_out1), .out2(demultiplexer_1_out2),
    .out3(demultiplexer_1_out3), .in(in_5), .sel(in_4));
  Register #(.width(32), .trigger("rising"), .Select("low")) register_1 (
    .D({32{1'b0}}), .en(demultiplexer_1_out0), .Q(register_1_q), .clk(in_6));  // open: clr
  Register #(.width(32), .trigger("rising"), .Select("low")) register_2 (
    .D(in_3), .en(demultiplexer_1_out1), .Q(register_2_q), .clk(in_6));  // open: clr
  Register #(.width(32), .trigger("rising"), .Select("low")) register_3 (
    .D(in_3), .en(demultiplexer_1_out2), .Q(register_3_q), .clk(in_6));  // open: clr
  Register #(.width(32), .trigger("rising"), .Select("low")) register_4 (
    .D(in_3), .en(demultiplexer_1_out3), .Q(register_4_q), .clk(in_6));  // open: clr
  Multiplexer #(.select(2), .width(32), .disabled("Z"), .enable("false")) multiplexer_1 (
    .in0(register_1_q), .in1(register_2_q), .in2(register_3_q), .in3(register_4_q), .out(out_7), .sel(in_1));
  Multiplexer #(.select(2), .width(32), .disabled("Z"), .enable("false")) multiplexer_2 (
    .in0(register_1_q), .in1(register_2_q), .in2(register_3_q), .in3(register_4_q), .out(out_8), .sel(in_2));

  // Other names for the same wires on the sheet: CLK = in_6; Din[31:0] = in_3; R1_num[1:0] = in_1; R2_num[1:0] = in_2;
  //   RD1[31:0] = out_7; RD2[31:0] = out_8; W_num[1:0] = in_4; WE = in_5

  // Notes on the sheet:
  //   输入引脚
  //   寄存器文件电路（4个寄存器，R0=0）
  //   输出引脚
endmodule

module \寄存器文件电路_4个寄存器_R0_0_测试电路  (
  input  [1:0] R1_num,
  input  [1:0] R2_num,
  input  [1:0] W_num,
  input  WE,
  input  [31:0] Din,
  output [31:0] RD1,
  output [31:0] RD2
);

  wire clock_1_out;

  // Probe on Din
  \寄存器文件电路_4个寄存器_R0_0  \u_寄存器文件电路_4个寄存器_r0_0_1  (
    .in_1(R1_num), .in_2(R2_num), .in_3(Din), .in_4(W_num), .in_5(WE), .in_6(clock_1_out), .out_7(RD1),
    .out_8(RD2));
  Clock #(.highDuration(1), .lowDuration(1)) clock_1 (.out(clock_1_out));
  // Probe on RD2
  // Probe on RD1
endmodule
