// Logisim project 动态分支预测流水线MIPS处理器.circ as structural Verilog: 15 circuits, main circuit 单周期硬布线控制器
module \动态分支预测流水线MIPS处理器  (
  output [31:0] IF_PC,
  output [31:0] ID_PC,
  output [31:0] EX_PC,
  output [31:0] M_PC,
  output [31:0] WB_PC,
  output RegWrite,
  output [31:0] RDin,
  output MemWrite,
  output [31:0] MDin,
  output [31:0] LedData
);

  wire and_1_out, and_2_out, and_3_out, and_4_out, and_5_out, and_6_out, and_7_out, and_8_out, and_9_out,
       and_10_out, BLTZ, BRANCH, CLK, clock_1_out, clock_2_out, comparator_1_eq, comparator_1_lt,
       comparator_2_eq, comparator_3_eq, comparator_5_lt, d_ff_1_q, equal, EX_BLTZ, EX_BRANCH, EX_Branch_t,
       EX_HIT, ex_mem_1_ctout16, \ex_mem_1_传输状态out_表明当前传输数据有效 , EX_SRAV, Go, HIT, \ID_EX_传输状态out_表明当前传输数据有效 ,
       ID_HIT, \if_id_1_传输状态out_表明当前传输数据有效 , Led, MEM_LH, Mem_MemToReg, Mem_RegWrite, mem_wb_1_ctout16_5,
       nand_1_out, not_1_out, or_1_out, or_3_out, or_4_out, or_5_out, or_6_out, or_8_out, or_10_out,
       PredictFailed, register_1_q, RST, \数据相关 ;
  wire [1:0] F, ForwardR1, ForwardR2, ID_EX_wbout5_2;
  wire [2:0] ID_EX_ctrl4_2;
  wire [3:0] CTRL4, ex_mem_1_ctout16_2;
  wire [4:0] ex_mem_1_wbout5, ID_EX_shout5_3, ID_EX_wbout5, mem_wb_1_wbout5, multiplexer_5_out,
       multiplexer_6_out, multiplexer_7_out, multiplexer_8_out, multiplexer_11_out;
  wire [12:0] counter_1_q;
  wire [15:0] CTRL, EX_CTRL, ex_mem_1_ctout16_6, \LoadUse次数 , mem_wb_1_ctout16_6, \总周期数 , \无条件分支数 , \条件分支成功数 ;
  wire [31:0] adder_1_out, adder_4_out, alu_1_result, ALURes, bit_extender_1_out, bit_extender_2_out,
       bit_extender_3_out, Correct, counter_4_q, counter_5_q, counter_6_q, counter_7_q, EX_BranchAddr,
       EX_BRANCHPC, EX_BRANCHPC2, EX_IR, ex_mem_1_ledout32, EX_PC_4, EX_R1, EX_R2, EXALU, ID_EX_r1out32,
       ID_EX_r1out32_2, ID_EX_r1out32_3, ID_IR, IF_IR, JmpAddr, JR_PC, MEM_IR, mips_ram_1_dataout,
       multiplexer_1_out, multiplexer_2_out, multiplexer_9_out, multiplexer_12_out, multiplexer_14_out,
       multiplexer_16_out, multiplexer_17_out, R2, RD, regifile_1_r1, regifile_1_r2, register_2_q,
       shifter_1_out, shifter_2_out, WB_IR;

  D_Flip_Flop #(.trigger("high"), .Pre_Clr_Positions("LEGACY"), .NegatePresetClear("false"), .enable("true"), .NewFFLayout("false")) d_ff_1 (.Q(d_ff_1_q));  // open: clk, D, Qn, preset, en, reset
  Button \u_总复位  (.out(RST));
  Button \u_继续运行  (.out(Go));
  Clock #(.highDuration(1), .lowDuration(1)) clock_1 (.out(clock_1_out));
  // Probe on \总周期数 
  // Probe on \LoadUse次数 
  Comparator #(.width(13), .mode("twosComplement")) comparator_1 (
    .a(counter_1_q), .b(13'hc), .eq(comparator_1_eq), .lt(comparator_1_lt));  // open: gt
  Clock #(.highDuration(1), .lowDuration(1)) clock_2 (.out(clock_2_out));
  Multiplexer #(.select(1), .width(32), .disabled("Z"), .enable("false")) multiplexer_1 (
    .in0(adder_1_out), .in1(JmpAddr), .out(multiplexer_1_out), .sel(HIT));
  Hex_Digit_Display hex_digit_display_1 (.value(LedData[31:28]));  // open: dp
  // Probe on \无条件分支数 
  // Probe on \条件分支成功数 
  nand nand_1 (nand_1_out, d_ff_1_q, comparator_1_eq);
  Counter #(.width(13), .max('h1fff), .ongoal("stay"), .trigger("rising"), .behavior("old")) counter_1 (
    .count(comparator_1_lt), .Q(counter_1_q), .clk(clock_2_out));  // open: load, D, carry, clr, preset
  Multiplexer #(.select(1), .width(32), .disabled("Z"), .enable("false")) multiplexer_2 (
    .in0(multiplexer_1_out), .in1(Correct), .out(multiplexer_2_out), .sel(PredictFailed));
  and and_1 (and_1_out, ~\数据相关 , not_1_out);  // AND_Gate
  and and_2 (and_2_out, mem_wb_1_ctout16_6[4], ~mem_wb_1_ctout16_5);  // AND_Gate
  Multiplexer #(.select(1), .width(32), .disabled("Z"), .enable("false")) multiplexer_3 (
    .in0(EX_PC_4), .in1(multiplexer_16_out), .out(Correct), .sel(BRANCH));
  BHT bht_1 (
    .JumpAddr(EX_BranchAddr), .IF_PC(IF_PC), .EX_PC(EX_PC), .EX_Branch(EX_Branch_t), .CLK(CLK),
    .in_6(BRANCH), .Jump(HIT), .DataOut(JmpAddr));
  Hex_Digit_Display hex_digit_display_2 (.value(LedData[27:24]));  // open: dp
  Hex_Digit_Display hex_digit_display_3 (.value(LedData[23:20]));  // open: dp
  assign CLK = nand_1_out ? clock_2_out : 1'bz;  // Controlled_Buffer controlled_buffer_1
  Register #(.width(32), .trigger("rising"), .Select("low")) PC (
    .D(multiplexer_2_out), .en(and_1_out), .Q(IF_PC), .clk(CLK), .clr(RST));
  Counter #(.width(16), .max('hffff), .ongoal("wrap"), .trigger("rising"), .behavior("old")) counter_2 (
    .count(not_1_out), .Q(\总周期数 ), .clk(CLK), .clr(RST));  // open: load, D, carry, preset
  Register #(.width(1), .trigger("rising"), .Select("low")) register_1 (
    .D(mem_wb_1_ctout16_6[4]), .en(and_2_out), .Q(register_1_q), .clk(CLK), .clr(or_1_out));
  not not_1 (not_1_out, register_1_q);
  or or_1 (or_1_out, RST, Go);
  or or_2 (BRANCH, EX_BRANCH, BLTZ, EX_CTRL[6], EX_CTRL[15], EX_CTRL[14]);
  Hex_Digit_Display hex_digit_display_4 (.value(LedData[19:16]));  // open: dp
  Hex_Digit_Display hex_digit_display_5 (.value(LedData[15:12]));  // open: dp
  Pull_Resistor #(.pull(1)) pull_resistor_1 (.node(CLK));
  Adder #(.width(32)) adder_1 (.a(IF_PC), .b(32'h4), .out(adder_1_out));  // open: cin, cout
  and and_3 (and_3_out, \数据相关 , not_1_out);
  Hex_Digit_Display hex_digit_display_6 (.value(LedData[11:8]));  // open: dp
  Hex_Digit_Display hex_digit_display_7 (.value(LedData[7:4]));  // open: dp
  // Probe on IF_PC[11:0]
  \重定向检测  \u_重定向检测_1  (
    .MEM_MemToReg(Mem_MemToReg), .ID_R1(multiplexer_5_out), .EX_WriteReg(ID_EX_wbout5),
    .EX_RegWrite(EX_CTRL[7]), .MEM_WriteReg(ex_mem_1_wbout5), .MEM_RegWrite(Mem_RegWrite), .OP(ID_IR[31:26]),
    .Func(ID_IR[5:0]), .ID_R2(multiplexer_6_out), .ForwardToR1(ForwardR1), .Load_Use(\数据相关 ),
    .ForwardToR2(ForwardR2), .EX_MemToReg(EX_CTRL[10]));
  ROM #(.addrWidth(10), .dataWidth(32), .Select("high")) rom_1 (.addr(IF_PC[11:2]), .data(IF_IR));
  Counter #(.width(16), .max('hffff), .ongoal("wrap"), .trigger("rising"), .behavior("old")) counter_3 (
    .count(and_3_out), .Q(\LoadUse次数 ), .clk(CLK), .clr(RST));  // open: load, D, carry, preset
  Multiplexer #(.select(1), .width(32), .disabled("Z"), .enable("false")) multiplexer_4 (
    .in0(EX_BRANCHPC), .in1(JR_PC), .out(EX_BranchAddr), .sel(or_5_out));
  Hex_Digit_Display hex_digit_display_8 (.value(LedData[3:0]));  // open: dp
  // Probe on IF_PC[19:0]
  // Probe on IF_IR
  or or_3 (or_3_out, RST, PredictFailed);
  or or_4 (or_4_out, \数据相关 , register_1_q);
  or or_5 (or_5_out, EX_CTRL[14], EX_CTRL[6], EX_CTRL[15]);
  IF_ID if_id_1 (
    .IRin32(IF_IR), .PCin32(IF_PC), .\传输状态In_表明当前传输数据有效 (1'b1), .CLK(CLK), .IRout32(ID_IR), .PCout32(ID_PC),
    .\传输状态Out_表明当前传输数据有效 (\if_id_1_传输状态out_表明当前传输数据有效 ), .\同步清零_气泡_高电平有效 (or_3_out),
    .\使能端_低电平有效_stall_高电平有效 (or_4_out), .CTin16(HIT), .CTout16(ID_HIT));
  // Probe on ID_PC[11:0]
  Multiplexer #(.select(1), .width(5), .disabled("Z"), .enable("false")) multiplexer_5 (
    .in0(ID_IR[25:21]), .in1(5'b00100), .out(multiplexer_5_out), .sel(CTRL[4]));
  Multiplexer #(.select(1), .width(5), .disabled("Z"), .enable("false")) multiplexer_6 (
    .in0(ID_IR[20:16]), .in1(5'b00010), .out(multiplexer_6_out), .sel(CTRL[4]));
  Multiplexer #(.select(1), .width(5), .disabled("Z"), .enable("false")) multiplexer_7 (
    .in0(ID_IR[20:16]), .in1(ID_IR[15:11]), .out(multiplexer_7_out), .sel(CTRL[5]));
  \单周期硬布线控制器  \u_单周期硬布线控制器_1  (
    .OP(ID_IR[31:26]), .Func(ID_IR[5:0]), .ALU_OP(CTRL[3:0]), .MemToReg(CTRL[10]), .MemWrite(CTRL[9]),
    .BLTZ(CTRL4[3]), .LH(CTRL4[2]), .SRAV(CTRL4[1]), .XORI(CTRL4[0]), .AluSrcB(CTRL[8]), .RegWrite(CTRL[7]),
    .SysCALL(CTRL[4]), .SignedExt(CTRL[13]), .RegDst(CTRL[5]), .Beq(CTRL[12]), .Bne(CTRL[11]), .JR(CTRL[14]),
    .JMP(CTRL[15]), .JAL(CTRL[6]));
  Multiplexer #(.select(1), .width(5), .disabled("Z"), .enable("false")) multiplexer_8 (
    .in0(multiplexer_7_out), .in1({5{1'b1}}), .out(multiplexer_8_out), .sel(CTRL[6]));
  xor xor_1 (PredictFailed, EX_HIT, BRANCH);
  Comparator #(.width(32), .mode("twosComplement")) comparator_2 (
    .a(EX_BranchAddr), .b(ID_PC), .eq(comparator_2_eq));  // open: gt, lt
  Comparator #(.width(32), .mode("twosComplement")) comparator_3 (
    .a(EX_BranchAddr), .b(ID_PC), .eq(comparator_3_eq));  // open: gt, lt
  // Probe on ID_PC[19:0]
  // Probe on ID_IR
  Regifile regifile_1 (
    .Din(RDin), .Clk(CLK), .R1(regifile_1_r1), .R2(regifile_1_r2), .WE(RegWrite), .W_num(mem_wb_1_wbout5),
    .R1_num(multiplexer_5_out), .R2_num(multiplexer_6_out));
  assign bit_extender_1_out = {{16{1'b0}}, ID_IR[15:0]};  // Bit_Extender bit_extender_1
  assign bit_extender_2_out = {{16{ID_IR[15]}}, ID_IR[15:0]};  // Bit_Extender bit_extender_2
  assign bit_extender_3_out = {{6{ID_IR[25]}}, ID_IR[25:0]};  // Bit_Extender bit_extender_3
  and and_4 (and_4_out, EX_HIT, ~PredictFailed);  // AND_Gate
  and and_5 (and_5_out, BRANCH, comparator_2_eq);
  and and_6 (and_6_out, BRANCH, ~comparator_3_eq);  // AND_Gate
  and and_7 (and_7_out, EX_HIT, PredictFailed);
  xor xor_2 (PredictFailed, EX_HIT, BRANCH);
  Multiplexer #(.select(1), .width(32), .disabled("Z"), .enable("false")) multiplexer_9 (
    .in0(bit_extender_1_out), .in1(bit_extender_2_out), .out(multiplexer_9_out), .sel(CTRL[13]));
  Shifter #(.width(32), .shift("ll")) shifter_1 (.in(bit_extender_3_out), .\dist (5'b00010), .out(shifter_1_out));
  // Probe on counter_4_q
  Counter #(.width(32), .max('hffffffff), .ongoal("wrap"), .trigger("rising"), .behavior("new")) counter_4 (
    .count(and_4_out), .Q(counter_4_q), .clk(CLK));  // open: load, D, carry, clr, preset, down
  Counter #(.width(32), .max('hffffffff), .ongoal("wrap"), .trigger("rising"), .behavior("old")) counter_5 (
    .count(and_5_out), .Q(counter_5_q), .clk(CLK));  // open: load, D, carry, clr, preset
  Counter #(.width(32), .max('hffffffff), .ongoal("wrap"), .trigger("rising"), .behavior("old")) counter_6 (
    .count(and_6_out), .Q(counter_6_q), .clk(CLK));  // open: load, D, carry, clr, preset
  Counter #(.width(32), .max('hffffffff), .ongoal("wrap"), .trigger("rising"), .behavior("old")) counter_7 (
    .count(and_7_out), .Q(counter_7_q), .clk(CLK));  // open: load, D, carry, clr, preset
  // Probe on EX_PC[11:0]
  // Probe on counter_5_q
  // Probe on counter_6_q
  // Probe on counter_7_q
  // Probe on EX_IR
  or or_6 (or_6_out, RST, \数据相关 , PredictFailed);
  ID_EX ID_EX (
    .R1in32(regifile_1_r1), .R2in32(regifile_1_r2), .IRin32(ID_IR), .PCin32(ID_PC),
    .IMMin32(multiplexer_9_out), .WBin5(multiplexer_8_out), .SHin5(ID_IR[10:6]), .CTin16(CTRL),
    .\传输状态In_表明当前传输数据有效 (\if_id_1_传输状态out_表明当前传输数据有效 ), .CLK(CLK), .R1out32(ID_EX_r1out32), .R2out32(EX_R2),
    .IRout32(EX_IR), .PCout32(EX_PC), .R1out32_2(ID_EX_r1out32_2), .WBout5(ID_EX_wbout5),
    .SHout5_3(ID_EX_shout5_3), .CTout16(EX_CTRL), .\传输状态Out_表明当前传输数据有效 (\ID_EX_传输状态out_表明当前传输数据有效 ),
    .\同步清零_气泡_高电平有效 (or_6_out), .\使能端_低电平有效_stall_高电平有效 (register_1_q), ._26in32(shifter_1_out),
    .R1out32_3(ID_EX_r1out32_3), .FWR1in2(ForwardR1), .WBout5_2(ID_EX_wbout5_2), .FWR2in2(ForwardR2),
    .SHout5_4(F), .CTRL4(CTRL4), .CTRL4_2({EX_BLTZ, ID_EX_ctrl4_2[2], EX_SRAV, ID_EX_ctrl4_2[0]}),
    .ERETin1_2(ID_HIT), .SHout5_2(EX_HIT));  // open: ERETin1, SHout5
  // Probe on EX_PC[19:0]
  and and_8 (and_8_out, Led, EX_CTRL[4]);
  Multiplexer #(.select(2), .width(32), .disabled("Z"), .enable("false")) multiplexer_10 (
    .in0(ID_EX_r1out32), .in1(ALURes), .in2(RD), .in3(EXALU), .out(EX_R1), .sel(ID_EX_wbout5_2));
  Shifter #(.width(32), .shift("ll")) shifter_2 (.in(ID_EX_r1out32_2), .\dist (5'b00010), .out(shifter_2_out));
  Multiplexer #(.select(1), .width(5), .disabled("Z"), .enable("false")) multiplexer_11 (
    .in0(ID_EX_shout5_3), .in1(EX_R1[4:0]), .out(multiplexer_11_out), .sel(EX_SRAV));
  Adder #(.width(32)) adder_2 (.a(EX_PC), .b(32'h4), .out(EX_PC_4));  // open: cin, cout
  Register #(.width(32), .trigger("rising"), .Select("low")) register_2 (
    .D(EX_R1), .en(and_8_out), .Q(register_2_q), .clk(CLK));  // open: clr
  Multiplexer #(.select(1), .width(32), .disabled("Z"), .enable("false")) multiplexer_12 (
    .in0(R2), .in1(ID_EX_r1out32_2), .out(multiplexer_12_out), .sel(EX_CTRL[8]));
  Comparator #(.width(32), .mode("twosComplement")) comparator_4 (.a(R2), .b(32'h22), .eq(Led));  // open: gt, lt
  Adder #(.width(32)) adder_3 (.a(shifter_2_out), .b(EX_PC_4), .out(EX_BRANCHPC));  // open: cin, cout
  // Probe on M_PC[11:0]
  ALU alu_1 (
    .X(EX_R1), .Y(multiplexer_12_out), .AluOP(EX_CTRL[3:0]), .Equal(equal), .Result(alu_1_result),
    .shamt(multiplexer_11_out));  // open: Result_2
  Multiplexer #(.select(1), .width(32), .disabled("Z"), .enable("false")) multiplexer_13 (
    .in0(ID_EX_r1out32_3), .in1(EX_R1), .out(JR_PC), .sel(EX_CTRL[14]));
  Multiplexer #(.select(1), .width(32), .disabled("Z"), .enable("false")) multiplexer_14 (
    .in0(EX_PC_4), .in1(EX_BRANCHPC), .out(multiplexer_14_out), .sel(EX_BRANCH));
  EX_MEM ex_mem_1 (
    .ALUin32(alu_1_result), .Memin32(R2), .IRin32(EX_IR), .PCin32(EX_PC), .WBin5(ID_EX_wbout5),
    .CTin16_2(EX_CTRL), .\传输状态In_表明当前传输数据有效 (\ID_EX_传输状态out_表明当前传输数据有效 ), .CLK(CLK), .ALUout32(EXALU),
    .Memout32(MDin), .IRout32(MEM_IR), .PCout32(M_PC), .WBout5(ex_mem_1_wbout5),
    .CTout16_6({ex_mem_1_ctout16_6[15:11], Mem_MemToReg, MemWrite, ex_mem_1_ctout16_6[8], Mem_RegWrite, ex_mem_1_ctout16_6[6:0]}),
    .\传输状态Out_表明当前传输数据有效 (\ex_mem_1_传输状态out_表明当前传输数据有效 ), .\同步清零_气泡_高电平有效 (RST),
    .\使能端_低电平有效_stall_高电平有效 (register_1_q), .LEDin32(register_2_q), .LEDout32(ex_mem_1_ledout32),
    .CTin16(Led), .CTout16(ex_mem_1_ctout16), .CTin4({EX_BLTZ, ID_EX_ctrl4_2[2], EX_SRAV, ID_EX_ctrl4_2[0]}),
    .CTout16_2({ex_mem_1_ctout16_2[3], MEM_LH, ex_mem_1_ctout16_2[1:0]}));  // open: Resullt2, CTout16_3, ERETin2, CTout16_4, ERETin2_2, CTout16_5
  Multiplexer #(.select(1), .width(32), .disabled("Z"), .enable("false")) multiplexer_15 (
    .in0(multiplexer_14_out), .in1(EX_BRANCHPC), .out(EX_BRANCHPC2), .sel(BLTZ));
  and and_9 (and_9_out, equal, EX_CTRL[12]);
  or or_7 (EX_BRANCH, and_9_out, and_10_out);
  and and_10 (and_10_out, ~equal, EX_CTRL[11]);  // AND_Gate
  // Probe on M_PC[19:0]
  // Probe on MEM_IR
  Multiplexer #(.select(1), .width(32), .disabled("Z"), .enable("false")) multiplexer_16 (
    .in0(EX_BRANCHPC2), .in1(JR_PC), .out(multiplexer_16_out), .sel(EX_CTRL[15]));
  or or_8 (or_8_out, EX_CTRL[11], EX_CTRL[12], EX_BLTZ);
  or or_9 (EX_Branch_t, EX_CTRL[14], or_8_out, EX_CTRL[6], EX_CTRL[15]);
  MIPS_RAM mips_ram_1 (
    .\字节地址 (EXALU[11:2]), .Din(MDin), .DataOut(mips_ram_1_dataout), .CLK(CLK), .WE(MemWrite),
    .Mode(EXALU[1]), .LH(MEM_LH));
  // Probe on WB_PC[11:0]
  MEM_WB mem_wb_1 (
    .ALUin32(EXALU), .MDin32(mips_ram_1_dataout), .IRin32(MEM_IR), .PCin32(M_PC), .WBin5(ex_mem_1_wbout5),
    .CTin16_2({ex_mem_1_ctout16_6[15:11], Mem_MemToReg, MemWrite, ex_mem_1_ctout16_6[8], Mem_RegWrite, ex_mem_1_ctout16_6[6:0]}),
    .\传输状态In_表明当前传输数据有效 (\ex_mem_1_传输状态out_表明当前传输数据有效 ), .CLK(CLK), .ALUout32(ALURes), .MDout32(RD),
    .IRout32(WB_IR), .PCout32(WB_PC), .WBout5(mem_wb_1_wbout5),
    .CTout16_6({mem_wb_1_ctout16_6[15:8], RegWrite, mem_wb_1_ctout16_6[6:0]}), .\同步清零_气泡_高电平有效 (RST),
    .\使能端_低电平有效_stall_高电平有效 (register_1_q), .LEDin32(ex_mem_1_ledout32), .LEDout32(LedData),
    .CTin16(ex_mem_1_ctout16), .CTout16_5(mem_wb_1_ctout16_5),
    .CTin4({ex_mem_1_ctout16_2[3], MEM_LH, ex_mem_1_ctout16_2[1:0]}));  // open: 传输状态Out_表明当前传输数据有效, CTout16, CTout16_2, RE2in32, ERETin1, CTout16_3, ERETin1_2, CTout16_4
  // Probe on WB_PC[19:0]
  // Probe on WB_IR
  Multiplexer #(.select(1), .width(32), .disabled("Z"), .enable("false")) multiplexer_17 (
    .in0(ALURes), .in1(RD), .out(multiplexer_17_out), .sel(mem_wb_1_ctout16_6[10]));
  Counter #(.width(16), .max('hffff), .ongoal("wrap"), .trigger("rising"), .behavior("old")) counter_8 (
    .count(EX_CTRL[15]), .Q(\无条件分支数 ), .clk(CLK), .clr(RST));  // open: load, D, carry, preset
  or or_10 (or_10_out, BLTZ, EX_BRANCH);
  Comparator #(.width(32), .mode("twosComplement")) comparator_5 (
    .a(EX_R1), .b({32{1'b0}}), .lt(comparator_5_lt));  // open: gt, eq
  Multiplexer #(.select(1), .width(32), .disabled("Z"), .enable("false")) multiplexer_18 (
    .in0(multiplexer_17_out), .in1(adder_4_out), .out(RDin), .sel(mem_wb_1_ctout16_6[6]));
  Counter #(.width(16), .max('hffff), .ongoal("wrap"), .trigger("rising"), .behavior("old")) counter_9 (
    .count(or_10_out), .Q(\条件分支成功数 ), .clk(CLK), .clr(RST));  // open: load, D, carry, preset
  Multiplexer #(.select(2), .width(32), .disabled("Z"), .enable("false")) multiplexer_19 (
    .in0(EX_R2), .in1(ALURes), .in2(RD), .in3(EXALU), .out(R2), .sel(F));
  Adder #(.width(32)) adder_4 (.a(WB_PC), .b(32'h4), .out(adder_4_out));  // open: cin, cout
  and and_11 (BLTZ, comparator_5_lt, EX_BLTZ);

  // Other names for the same wires on the sheet: SignedExt = CTRL[13]; EX_JAL = EX_CTRL[6]; EX_RegWrite = EX_CTRL[7];
  //   EX_MemToReg = EX_CTRL[10]; EX_JR = EX_CTRL[14]; EX_JMP = EX_CTRL[15]; MEM_PC[31:0] = M_PC;
  //   插入气泡数[15:0] = \LoadUse次数 

  // Notes on the sheet:
  //   指令存储器
  //   contents of rom_1 (hex, n*v repeats v):
  //   20110005 8000c04 20110001 20120002 8000c07 20110001 20120002 8000c0a 20110001 20120002 8000c0d
  //   20110001 20120002 8000c10 20110001 20120002 8000c13 20110001 20120002 8000c16 20110001 20120002
  //   8000c19 20110001 20120002 2231ffff 1620ffec 20100001 201200ff 20110001 20130003 12120003 12100002
  //   20110001 20120002 16310003 16320002 20110001 20120002 c000c2a 2002000a c 20100000 22100001 102020
  //   20020022 c 3e00008
  //   OP
  //   Func
  //   rs
  //   rt
  //   rd
  //   JMP
  //   JR
  //   OP
  //   Func
  //   Syscall
  //   Beq
  //   Bne
  //   MemToReg
  //   MemWrite
  //   AluOP
  //   AluSrcB
  //   RegWrite
  //   JAL
  //   RegDst
  //   动态分支预测流水线MIPS处理器
  //   Syscall
  //   AluOP
  //   AluSrcB
  //   Bne
  //   MemWrite
  //   数据存储器
  //   Syscall
  //   MemToReg
  //   RegWrite
  //   JAL
endmodule

module \单周期硬布线控制器  (
  input  [5:0] OP,
  input  [5:0] Func,
  output [3:0] ALU_OP,
  output MemToReg,
  output MemWrite,
  output BLTZ,
  output LH,
  output SRAV,
  output XORI,
  output AluSrcB,
  output RegWrite,
  output SysCALL,
  output SignedExt,
  output RegDst,
  output Beq,
  output Bne,
  output JR,
  output JMP,
  output JAL
);

  \运算器控制器  \u_运算器控制器_1  (
    .OP0(OP[0]), .OP1(OP[1]), .OP2(OP[2]), .OP3(OP[3]), .OP4(OP[4]), .OP5(OP[5]), .F0(Func[0]), .F1(Func[1]),
    .F2(Func[2]), .F3(Func[3]), .F4(Func[4]), .F5(Func[5]), .S0(ALU_OP[0]), .S1(ALU_OP[1]), .S2(ALU_OP[2]),
    .S3(ALU_OP[3]));
  \控制信号生成  \u_控制信号生成_1  (
    .OP0(OP[0]), .OP1(OP[1]), .OP2(OP[2]), .OP3(OP[3]), .OP4(OP[4]), .OP5(OP[5]), .F0(Func[0]), .F1(Func[1]),
    .F2(Func[2]), .F3(Func[3]), .F4(Func[4]), .F5(Func[5]), .MemToReg(MemToReg), .MemWrite(MemWrite),
    .BLTZ(BLTZ), .LH(LH), .SRAV(SRAV), .XORI(XORI), .ALU_SRC(AluSrcB), .RegWrite(RegWrite),
    .SysCALL(SysCALL), .SignedExt(SignedExt), .RegDst(RegDst), .BEQ(Beq), .BNE(Bne), .JR(JR), .JUMP(JMP),
    .JAL(JAL));

  // Other names for the same wires on the sheet: OP_CODE[5:0] = OP

  // Notes on the sheet:
  //   运算器控制器，根据指令生成运算器功能选择信号
  //   控制信号生成，产生数据通路需要的其他控制信号
endmodule

module \运算器控制器  (
  input  OP0,
  input  OP1,
  input  OP2,
  input  OP3,
  input  OP4,
  input  OP5,
  input  F0,
  input  F1,
  input  F2,
  input  F3,
  input  F4,
  input  F5,
  output S0,
  output S1,
  output S2,
  output S3
);

  wire and_1_out, and_2_out, and_3_out, and_4_out, and_5_out, and_6_out, and_7_out, and_8_out, and_9_out,
       and_10_out, and_11_out, and_12_out, and_13_out, and_14_out, and_15_out, and_16_out, and_17_out,
       and_18_out, and_19_out, and_20_out, and_21_out, and_22_out, and_23_out, and_24_out, and_25_out,
       and_26_out, and_27_out, and_28_out, and_29_out, and_30_out, and_31_out, and_32_out, and_33_out,
       and_34_out, and_35_out, and_36_out, and_37_out, and_38_out, and_39_out, not_1_out, not_2_out,
       not_3_out, not_4_out, not_5_out, not_6_out, not_7_out, not_8_out, not_9_out, not_10_out, not_11_out,
       not_12_out, not_13_out, not_14_out, not_15_out, not_16_out, not_17_out, not_18_out, not_19_out,
       not_20_out, not_21_out, not_22_out, not_23_out, not_24_out, not_25_out, not_26_out, not_27_out,
       not_28_out, not_29_out, not_30_out, not_31_out, not_32_out, not_33_out, not_34_out, not_35_out,
       not_36_out, not_37_out, not_38_out, not_39_out, not_40_out, not_41_out, not_42_out, not_43_out,
       not_44_out, not_45_out, not_46_out, not_47_out, not_48_out, not_49_out, not_50_out, not_51_out,
       not_52_out, not_53_out, not_54_out, not_55_out, not_56_out, not_57_out, not_58_out, not_59_out,
       not_60_out, not_61_out, not_62_out, not_63_out, not_64_out, not_65_out, not_66_out, not_67_out,
       not_68_out, not_69_out, not_70_out, not_71_out, not_72_out, not_73_out, not_74_out, not_75_out,
       not_76_out, not_77_out, not_78_out, not_79_out, not_80_out, not_81_out, not_82_out, not_83_out,
       not_84_out, not_85_out, not_86_out, not_87_out, not_88_out, not_89_out, not_90_out, not_91_out,
       not_92_out, not_93_out, not_94_out, not_95_out, not_96_out, not_97_out, not_98_out, not_99_out,
       not_100_out, not_101_out, not_102_out, not_103_out, not_104_out, not_105_out, not_106_out,
       not_107_out, not_108_out, not_109_out, not_110_out, not_111_out, not_112_out, not_113_out,
       not_114_out, not_115_out, not_116_out, not_117_out, not_118_out, not_119_out, not_120_out,
       not_121_out, not_122_out, not_123_out, not_124_out, not_125_out, not_126_out, not_127_out,
       not_128_out, not_129_out, not_130_out, not_131_out, not_132_out, not_133_out, not_134_out,
       not_135_out, not_136_out, not_137_out, not_138_out, not_139_out, not_140_out, not_141_out,
       not_142_out, not_143_out, not_144_out, not_145_out, not_146_out, not_147_out, not_148_out,
       not_149_out, not_150_out, not_151_out, not_152_out, not_153_out, not_154_out, not_155_out,
       not_156_out, not_157_out, not_158_out, not_159_out, not_160_out, not_161_out, not_162_out,
       not_163_out, not_164_out, not_165_out, not_166_out, not_167_out, not_168_out, not_169_out,
       not_170_out, not_171_out, not_172_out, not_173_out, not_174_out, not_175_out, not_176_out,
       not_177_out, not_178_out, not_179_out, not_180_out, not_181_out, not_182_out, not_183_out,
       not_184_out, not_185_out, not_186_out, not_187_out, not_188_out, not_189_out, not_190_out,
       not_191_out, not_192_out, not_193_out, not_194_out, not_195_out, not_196_out, not_197_out,
       not_198_out, not_199_out, not_200_out, not_201_out, not_202_out, not_203_out, not_204_out,
       not_205_out, not_206_out, not_207_out, not_208_out, not_209_out, not_210_out, not_211_out,
       not_212_out, not_213_out, not_214_out, not_215_out, not_216_out, not_217_out, not_218_out,
       not_219_out, not_220_out, not_221_out, not_222_out, not_223_out, not_224_out, not_225_out,
       not_226_out, not_227_out, not_228_out, not_229_out, not_230_out, not_231_out, not_232_out,
       not_233_out, not_234_out, not_235_out, not_236_out, not_237_out, not_238_out, not_239_out,
       not_240_out, not_241_out, not_242_out, not_243_out, not_244_out, not_245_out, not_246_out,
       not_247_out, not_248_out, not_249_out, not_250_out, not_251_out, not_252_out, not_253_out,
       not_254_out, not_255_out, not_256_out, not_257_out, not_258_out, not_259_out;

  not not_1 (not_1_out, OP5);
  not not_2 (not_2_out, OP4);
  not not_3 (not_3_out, OP3);
  not not_4 (not_4_out, OP2);
  not not_5 (not_5_out, OP1);
  not not_6 (not_6_out, OP0);
  not not_7 (not_7_out, F5);
  not not_8 (not_8_out, F4);
  not not_9 (not_9_out, F3);
  not not_10 (not_10_out, F2);
  not not_11 (not_11_out, OP5);
  not not_12 (not_12_out, OP4);
  not not_13 (not_13_out, OP3);
  not not_14 (not_14_out, OP2);
  not not_15 (not_15_out, OP1);
  not not_16 (not_16_out, OP0);
  not not_17 (not_17_out, F4);
  not not_18 (not_18_out, F3);
  not not_19 (not_19_out, F2);
  not not_20 (not_20_out, F1);
  not not_21 (not_21_out, F0);
  not not_22 (not_22_out, OP5);
  not not_23 (not_23_out, OP4);
  not not_24 (not_24_out, OP3);
  not not_25 (not_25_out, OP2);
  not not_26 (not_26_out, OP1);
  not not_27 (not_27_out, OP0);
  not not_28 (not_28_out, F4);
  not not_29 (not_29_out, F3);
  not not_30 (not_30_out, F2);
  not not_31 (not_31_out, F1);
  not not_32 (not_32_out, OP5);
  not not_33 (not_33_out, OP4);
  not not_34 (not_34_out, OP3);
  not not_35 (not_35_out, OP2);
  not not_36 (not_36_out, OP1);
  not not_37 (not_37_out, OP0);
  not not_38 (not_38_out, F4);
  not not_39 (not_39_out, F3);
  not not_40 (not_40_out, F1);
  not not_41 (not_41_out, F0);
  not not_42 (not_42_out, OP5);
  not not_43 (not_43_out, OP4);
  not not_44 (not_44_out, OP3);
  not not_45 (not_45_out, OP2);
  not not_46 (not_46_out, OP1);
  not not_47 (not_47_out, OP0);
  not not_48 (not_48_out, F4);
  not not_49 (not_49_out, F2);
  not not_50 (not_50_out, F0);
  not not_51 (not_51_out, OP5);
  not not_52 (not_52_out, OP4);
  not not_53 (not_53_out, OP2);
  not not_54 (not_54_out, OP1);
  not not_55 (not_55_out, OP0);
  not not_56 (not_56_out, OP5);
  not not_57 (not_57_out, OP4);
  not not_58 (not_58_out, OP1);
  not not_59 (not_59_out, OP0);
  not not_60 (not_60_out, OP5);
  not not_61 (not_61_out, OP4);
  not not_62 (not_62_out, OP2);
  not not_63 (not_63_out, OP1);
  not not_64 (not_64_out, OP5);
  not not_65 (not_65_out, OP4);
  not not_66 (not_66_out, OP2);
  not not_67 (not_67_out, OP0);
  not not_68 (not_68_out, OP4);
  not not_69 (not_69_out, OP3);
  not not_70 (not_70_out, OP2);
  not not_71 (not_71_out, OP4);
  not not_72 (not_72_out, OP2);
  not not_73 (not_73_out, OP5);
  not not_74 (not_74_out, OP4);
  not not_75 (not_75_out, OP3);
  not not_76 (not_76_out, OP2);
  not not_77 (not_77_out, OP1);
  not not_78 (not_78_out, OP0);
  not not_79 (not_79_out, F5);
  not not_80 (not_80_out, F4);
  not not_81 (not_81_out, F3);
  not not_82 (not_82_out, OP5);
  not not_83 (not_83_out, OP4);
  not not_84 (not_84_out, OP0);
  not not_85 (not_85_out, OP4);
  not not_86 (not_86_out, OP3);
  not not_87 (not_87_out, OP2);
  not not_88 (not_88_out, OP1);
  not not_89 (not_89_out, OP5);
  not not_90 (not_90_out, OP4);
  not not_91 (not_91_out, OP3);
  not not_92 (not_92_out, OP2);
  not not_93 (not_93_out, OP1);
  not not_94 (not_94_out, OP0);
  not not_95 (not_95_out, F5);
  not not_96 (not_96_out, F4);
  not not_97 (not_97_out, F3);
  not not_98 (not_98_out, F2);
  not not_99 (not_99_out, F0);
  not not_100 (not_100_out, OP5);
  not not_101 (not_101_out, OP4);
  not not_102 (not_102_out, OP3);
  not not_103 (not_103_out, OP2);
  not not_104 (not_104_out, OP1);
  not not_105 (not_105_out, OP0);
  not not_106 (not_106_out, F4);
  not not_107 (not_107_out, F3);
  not not_108 (not_108_out, F2);
  not not_109 (not_109_out, F0);
  not not_110 (not_110_out, OP5);
  not not_111 (not_111_out, OP4);
  not not_112 (not_112_out, OP3);
  not not_113 (not_113_out, OP2);
  not not_114 (not_114_out, OP1);
  not not_115 (not_115_out, OP0);
  not not_116 (not_116_out, F4);
  not not_117 (not_117_out, F3);
  not not_118 (not_118_out, F1);
  not not_119 (not_119_out, F0);
  not not_120 (not_120_out, OP5);
  not not_121 (not_121_out, OP4);
  not not_122 (not_122_out, OP3);
  not not_123 (not_123_out, OP2);
  not not_124 (not_124_out, OP1);
  not not_125 (not_125_out, OP0);
  not not_126 (not_126_out, F4);
  not not_127 (not_127_out, F3);
  not not_128 (not_128_out, OP5);
  not not_129 (not_129_out, OP4);
  not not_130 (not_130_out, OP3);
  not not_131 (not_131_out, OP2);
  not not_132 (not_132_out, OP1);
  not not_133 (not_133_out, OP0);
  not not_134 (not_134_out, F4);
  not not_135 (not_135_out, F2);
  not not_136 (not_136_out, F0);
  not not_137 (not_137_out, OP5);
  not not_138 (not_138_out, OP4);
  not not_139 (not_139_out, OP1);
  not not_140 (not_140_out, OP0);
  not not_141 (not_141_out, OP5);
  not not_142 (not_142_out, OP4);
  not not_143 (not_143_out, OP2);
  not not_144 (not_144_out, OP0);
  not not_145 (not_145_out, OP5);
  not not_146 (not_146_out, OP4);
  not not_147 (not_147_out, OP3);
  not not_148 (not_148_out, OP2);
  not not_149 (not_149_out, OP1);
  not not_150 (not_150_out, OP0);
  not not_151 (not_151_out, F4);
  not not_152 (not_152_out, F3);
  not not_153 (not_153_out, F2);
  not not_154 (not_154_out, F1);
  not not_155 (not_155_out, F0);
  not not_156 (not_156_out, OP5);
  not not_157 (not_157_out, OP4);
  not not_158 (not_158_out, OP3);
  not not_159 (not_159_out, OP2);
  not not_160 (not_160_out, OP1);
  not not_161 (not_161_out, OP0);
  not not_162 (not_162_out, F4);
  not not_163 (not_163_out, F3);
  not not_164 (not_164_out, F2);
  not not_165 (not_165_out, F1);
  not not_166 (not_166_out, OP5);
  not not_167 (not_167_out, OP4);
  not not_168 (not_168_out, OP3);
  not not_169 (not_169_out, OP2);
  not not_170 (not_170_out, OP1);
  not not_171 (not_171_out, OP0);
  not not_172 (not_172_out, F4);
  not not_173 (not_173_out, F3);
  not not_174 (not_174_out, F2);
  not not_175 (not_175_out, F0);
  not not_176 (not_176_out, OP5);
  not not_177 (not_177_out, OP4);
  not not_178 (not_178_out, OP3);
  not not_179 (not_179_out, OP2);
  not not_180 (not_180_out, OP1);
  not not_181 (not_181_out, OP0);
  not not_182 (not_182_out, F4);
  not not_183 (not_183_out, F3);
  not not_184 (not_184_out, F1);
  not not_185 (not_185_out, F0);
  not not_186 (not_186_out, OP5);
  not not_187 (not_187_out, OP4);
  not not_188 (not_188_out, OP3);
  not not_189 (not_189_out, OP2);
  not not_190 (not_190_out, OP1);
  not not_191 (not_191_out, OP0);
  not not_192 (not_192_out, F4);
  not not_193 (not_193_out, F2);
  not not_194 (not_194_out, OP5);
  not not_195 (not_195_out, OP4);
  not not_196 (not_196_out, OP2);
  not not_197 (not_197_out, OP1);
  not not_198 (not_198_out, OP0);
  not not_199 (not_199_out, OP5);
  not not_200 (not_200_out, OP4);
  not not_201 (not_201_out, OP1);
  not not_202 (not_202_out, OP0);
  not not_203 (not_203_out, OP5);
  not not_204 (not_204_out, OP4);
  not not_205 (not_205_out, OP2);
  not not_206 (not_206_out, OP1);
  not not_207 (not_207_out, OP4);
  not not_208 (not_208_out, OP3);
  not not_209 (not_209_out, OP2);
  not not_210 (not_210_out, OP4);
  not not_211 (not_211_out, OP2);
  not not_212 (not_212_out, OP4);
  not not_213 (not_213_out, OP3);
  not not_214 (not_214_out, OP2);
  not not_215 (not_215_out, OP1);
  not not_216 (not_216_out, OP5);
  not not_217 (not_217_out, OP4);
  not not_218 (not_218_out, OP3);
  not not_219 (not_219_out, OP2);
  not not_220 (not_220_out, OP1);
  not not_221 (not_221_out, OP0);
  not not_222 (not_222_out, F4);
  not not_223 (not_223_out, F3);
  not not_224 (not_224_out, F1);
  not not_225 (not_225_out, OP5);
  not not_226 (not_226_out, OP4);
  not not_227 (not_227_out, OP3);
  not not_228 (not_228_out, OP2);
  not not_229 (not_229_out, OP1);
  not not_230 (not_230_out, OP0);
  not not_231 (not_231_out, F4);
  not not_232 (not_232_out, F3);
  not not_233 (not_233_out, OP5);
  not not_234 (not_234_out, OP4);
  not not_235 (not_235_out, OP3);
  not not_236 (not_236_out, OP2);
  not not_237 (not_237_out, OP1);
  not not_238 (not_238_out, OP0);
  not not_239 (not_239_out, F4);
  not not_240 (not_240_out, F2);
  not not_241 (not_241_out, F0);
  not not_242 (not_242_out, OP5);
  not not_243 (not_243_out, OP4);
  not not_244 (not_244_out, OP3);
  not not_245 (not_245_out, OP2);
  not not_246 (not_246_out, OP1);
  not not_247 (not_247_out, OP0);
  not not_248 (not_248_out, F4);
  not not_249 (not_249_out, F2);
  not not_250 (not_250_out, OP5);
  not not_251 (not_251_out, OP4);
  not not_252 (not_252_out, OP2);
  not not_253 (not_253_out, OP0);
  not not_254 (not_254_out, OP5);
  not not_255 (not_255_out, OP4);
  not not_256 (not_256_out, OP1);
  not not_257 (not_257_out, OP5);
  not not_258 (not_258_out, OP4);
  not not_259 (not_259_out, OP0);
  and and_1 (and_1_out, not_1_out, not_2_out, not_3_out, not_4_out, not_5_out, not_6_out, not_7_out, not_8_out, not_9_out, not_10_out, F1, F0);
  and and_2 (and_2_out, not_11_out, not_12_out, not_13_out, not_14_out, not_15_out, not_16_out, F5, not_17_out, not_18_out, not_19_out, not_20_out, not_21_out);
  and and_3 (and_3_out, not_22_out, not_23_out, not_24_out, not_25_out, not_26_out, not_27_out, F5, not_28_out, not_29_out, not_30_out, not_31_out, F0);
  and and_4 (and_4_out, not_32_out, not_33_out, not_34_out, not_35_out, not_36_out, not_37_out, F5, not_38_out, not_39_out, F2, not_40_out, not_41_out);
  and and_5 (and_5_out, not_42_out, not_43_out, not_44_out, not_45_out, not_46_out, not_47_out, F5, not_48_out, F3, not_49_out, F1, not_50_out);
  and and_6 (and_6_out, not_51_out, not_52_out, OP3, not_53_out, not_54_out, not_55_out);
  and and_7 (and_7_out, not_56_out, not_57_out, OP3, OP2, not_58_out, not_59_out);
  and and_8 (and_8_out, not_60_out, not_61_out, OP3, not_62_out, not_63_out, OP0);
  and and_9 (and_9_out, not_64_out, not_65_out, OP3, not_66_out, OP1, not_67_out);
  and and_10 (and_10_out, OP5, not_68_out, not_69_out, not_70_out, OP1, OP0);
  and and_11 (and_11_out, OP5, not_71_out, OP3, not_72_out, OP1, OP0);
  and and_12 (and_12_out, not_73_out, not_74_out, not_75_out, not_76_out, not_77_out, not_78_out, not_79_out, not_80_out, not_81_out, F2, F1, F0);
  and and_13 (and_13_out, not_82_out, not_83_out, OP3, OP2, OP1, not_84_out);
  and and_14 (and_14_out, OP5, not_85_out, not_86_out, not_87_out, not_88_out, OP0);
  and and_15 (and_15_out, not_89_out, not_90_out, not_91_out, not_92_out, not_93_out, not_94_out, not_95_out, not_96_out, not_97_out, not_98_out, F1, not_99_out);
  and and_16 (and_16_out, not_100_out, not_101_out, not_102_out, not_103_out, not_104_out, not_105_out, F5, not_106_out, not_107_out, not_108_out, F1, not_109_out);
  and and_17 (and_17_out, not_110_out, not_111_out, not_112_out, not_113_out, not_114_out, not_115_out, F5, not_116_out, not_117_out, F2, not_118_out, not_119_out);
  and and_18 (and_18_out, not_120_out, not_121_out, not_122_out, not_123_out, not_124_out, not_125_out, F5, not_126_out, not_127_out, F2, F1, F0);
  and and_19 (and_19_out, not_128_out, not_129_out, not_130_out, not_131_out, not_132_out, not_133_out, F5, not_134_out, F3, not_135_out, F1, not_136_out);
  and and_20 (and_20_out, not_137_out, not_138_out, OP3, OP2, not_139_out, not_140_out);
  and and_21 (and_21_out, not_141_out, not_142_out, OP3, not_143_out, OP1, not_144_out);
  and and_22 (and_22_out, not_145_out, not_146_out, not_147_out, not_148_out, not_149_out, not_150_out, F5, not_151_out, not_152_out, not_153_out, not_154_out, not_155_out);
  and and_23 (and_23_out, not_156_out, not_157_out, not_158_out, not_159_out, not_160_out, not_161_out, F5, not_162_out, not_163_out, not_164_out, not_165_out, F0);
  and and_24 (and_24_out, not_166_out, not_167_out, not_168_out, not_169_out, not_170_out, not_171_out, F5, not_172_out, not_173_out, not_174_out, F1, not_175_out);
  and and_25 (and_25_out, not_176_out, not_177_out, not_178_out, not_179_out, not_180_out, not_181_out, F5, not_182_out, not_183_out, F2, not_184_out, not_185_out);
  and and_26 (and_26_out, not_186_out, not_187_out, not_188_out, not_189_out, not_190_out, not_191_out, F5, not_192_out, F3, not_193_out, F1, F0);
  and and_27 (and_27_out, not_194_out, not_195_out, OP3, not_196_out, not_197_out, not_198_out);
  and and_28 (and_28_out, not_199_out, not_200_out, OP3, OP2, not_201_out, not_202_out);
  and and_29 (and_29_out, not_203_out, not_204_out, OP3, not_205_out, not_206_out, OP0);
  and and_30 (and_30_out, OP5, not_207_out, not_208_out, not_209_out, OP1, OP0);
  and and_31 (and_31_out, OP5, not_210_out, OP3, not_211_out, OP1, OP0);
  and and_32 (and_32_out, OP5, not_212_out, not_213_out, not_214_out, not_215_out, OP0);
  and and_33 (and_33_out, not_216_out, not_217_out, not_218_out, not_219_out, not_220_out, not_221_out, F5, not_222_out, not_223_out, F2, not_224_out, F0);
  and and_34 (and_34_out, not_225_out, not_226_out, not_227_out, not_228_out, not_229_out, not_230_out, F5, not_231_out, not_232_out, F2, F1, F0);
  and and_35 (and_35_out, not_233_out, not_234_out, not_235_out, not_236_out, not_237_out, not_238_out, F5, not_239_out, F3, not_240_out, F1, not_241_out);
  and and_36 (and_36_out, not_242_out, not_243_out, not_244_out, not_245_out, not_246_out, not_247_out, F5, not_248_out, F3, not_249_out, F1, F0);
  and and_37 (and_37_out, not_250_out, not_251_out, OP3, not_252_out, OP1, not_253_out);
  and and_38 (and_38_out, not_254_out, not_255_out, OP3, OP2, not_256_out, OP0);
  and and_39 (and_39_out, not_257_out, not_258_out, OP3, OP2, OP1, not_259_out);
  or or_1 (S1, and_15_out, and_16_out, and_17_out, and_18_out, and_19_out, and_20_out, and_21_out);
  or or_2 (S2, and_22_out, and_23_out, and_24_out, and_25_out, and_26_out, and_27_out, and_28_out, and_29_out, and_30_out, and_31_out, and_32_out);
  or or_3 (S3, and_33_out, and_34_out, and_35_out, and_36_out, and_37_out, and_38_out, and_39_out);
  or or_4 (S0, and_1_out, and_2_out, and_3_out, and_4_out, and_5_out, and_6_out, and_7_out, and_8_out, and_9_out, and_10_out, and_11_out, and_12_out, and_13_out, and_14_out);
endmodule

module \控制信号生成  (
  input  OP0,
  input  OP1,
  input  OP2,
  input  OP3,
  input  OP4,
  input  OP5,
  input  F0,
  input  F1,
  input  F2,
  input  F3,
  input  F4,
  input  F5,
  output MemToReg,
  output MemWrite,
  output BLTZ,
  output LH,
  output SRAV,
  output XORI,
  output ALU_SRC,
  output RegWrite,
  output SysCALL,
  output SignedExt,
  output RegDst,
  output BEQ,
  output BNE,
  output JR,
  output JUMP,
  output JAL
);

  wire and_7_out, and_8_out, and_9_out, and_10_out, and_11_out, and_12_out, and_13_out, and_14_out,
       and_15_out, and_16_out, and_17_out, and_18_out, and_19_out, and_21_out, and_22_out, and_23_out,
       and_24_out, and_25_out, and_26_out, and_27_out, and_28_out, and_29_out, and_30_out, and_31_out,
       and_32_out, and_33_out, and_34_out, and_38_out, and_39_out, not_1_out, not_2_out, not_3_out,
       not_4_out, not_5_out, not_6_out, not_7_out, not_8_out, not_9_out, not_10_out, not_11_out, not_12_out,
       not_13_out, not_14_out, not_15_out, not_16_out, not_17_out, not_18_out, not_19_out, not_20_out,
       not_21_out, not_22_out, not_23_out, not_24_out, not_25_out, not_26_out, not_27_out, not_28_out,
       not_29_out, not_30_out, not_31_out, not_32_out, not_33_out, not_34_out, not_35_out, not_36_out,
       not_37_out, not_38_out, not_39_out, not_40_out, not_41_out, not_42_out, not_43_out, not_44_out,
       not_45_out, not_46_out, not_47_out, not_48_out, not_49_out, not_50_out, not_51_out, not_52_out,
       not_53_out, not_54_out, not_55_out, not_56_out, not_57_out, not_58_out, not_59_out, not_60_out,
       not_61_out, not_62_out, not_63_out, not_64_out, not_65_out, not_66_out, not_67_out, not_68_out,
       not_69_out, not_70_out, not_71_out, not_72_out, not_73_out, not_74_out, not_75_out, not_76_out,
       not_77_out, not_78_out, not_79_out, not_80_out, not_81_out, not_82_out, not_83_out, not_84_out,
       not_85_out, not_86_out, not_87_out, not_88_out, not_89_out, not_90_out, not_91_out, not_92_out,
       not_93_out, not_94_out, not_95_out, not_96_out, not_97_out, not_98_out, not_99_out, not_100_out,
       not_101_out, not_102_out, not_103_out, not_104_out, not_105_out, not_106_out, not_107_out,
       not_108_out, not_109_out, not_110_out, not_111_out, not_112_out, not_113_out, not_114_out,
       not_115_out, not_116_out, not_117_out, not_118_out, not_119_out, not_120_out, not_121_out,
       not_122_out, not_123_out, not_124_out, not_125_out, not_126_out, not_127_out, not_128_out,
       not_129_out, not_130_out, not_131_out, not_132_out, not_133_out, not_134_out, not_135_out,
       not_136_out, not_137_out, not_138_out, not_139_out, not_140_out, not_141_out, not_142_out,
       not_143_out, not_144_out, not_145_out, not_146_out, not_147_out, not_148_out, not_149_out,
       not_150_out, not_151_out, not_152_out, not_153_out, not_154_out, not_155_out, not_156_out,
       not_157_out, not_158_out, not_159_out, not_160_out, not_161_out, not_162_out, not_163_out,
       not_164_out, not_165_out, not_166_out, not_167_out, not_168_out, not_169_out, not_170_out,
       not_171_out, not_172_out, not_173_out, not_174_out, not_175_out, not_176_out, not_177_out,
       not_178_out, not_179_out, not_180_out, not_181_out, not_182_out, not_183_out, not_184_out,
       not_185_out, not_186_out, not_187_out, not_188_out, not_189_out, not_190_out, not_191_out,
       not_192_out, not_193_out, not_194_out, not_195_out, not_196_out, not_197_out, not_198_out,
       not_199_out, not_200_out, not_201_out, not_202_out, not_203_out, not_204_out, not_205_out,
       not_206_out, not_207_out, not_208_out, not_209_out, not_210_out, not_211_out, not_212_out,
       not_213_out, not_214_out, not_215_out, not_216_out;

  not not_1 (not_1_out, OP2);
  not not_2 (not_2_out, OP3);
  not not_3 (not_3_out, OP4);
  not not_4 (not_4_out, OP2);
  not not_5 (not_5_out, OP4);
  not not_6 (not_6_out, OP1);
  not not_7 (not_7_out, OP2);
  not not_8 (not_8_out, OP3);
  not not_9 (not_9_out, OP4);
  not not_10 (not_10_out, OP5);
  not not_11 (not_11_out, OP1);
  not not_12 (not_12_out, OP2);
  not not_13 (not_13_out, OP3);
  not not_14 (not_14_out, OP4);
  not not_15 (not_15_out, OP0);
  not not_16 (not_16_out, OP1);
  not not_17 (not_17_out, OP2);
  not not_18 (not_18_out, OP3);
  not not_19 (not_19_out, OP4);
  not not_20 (not_20_out, OP5);
  not not_21 (not_21_out, F3);
  not not_22 (not_22_out, F4);
  not not_23 (not_23_out, F5);
  not not_24 (not_24_out, OP0);
  not not_25 (not_25_out, OP4);
  not not_26 (not_26_out, OP5);
  not not_27 (not_27_out, OP0);
  not not_28 (not_28_out, OP4);
  not not_29 (not_29_out, OP5);
  not not_30 (not_30_out, OP1);
  not not_31 (not_31_out, OP4);
  not not_32 (not_32_out, OP5);
  not not_33 (not_33_out, OP2);
  not not_34 (not_34_out, OP3);
  not not_35 (not_35_out, OP4);
  not not_36 (not_36_out, OP2);
  not not_37 (not_37_out, OP4);
  not not_38 (not_38_out, OP0);
  not not_39 (not_39_out, OP1);
  not not_40 (not_40_out, OP2);
  not not_41 (not_41_out, OP4);
  not not_42 (not_42_out, OP5);
  not not_43 (not_43_out, F0);
  not not_44 (not_44_out, F2);
  not not_45 (not_45_out, F3);
  not not_46 (not_46_out, F4);
  not not_47 (not_47_out, OP0);
  not not_48 (not_48_out, OP1);
  not not_49 (not_49_out, OP2);
  not not_50 (not_50_out, OP4);
  not not_51 (not_51_out, OP5);
  not not_52 (not_52_out, F1);
  not not_53 (not_53_out, F3);
  not not_54 (not_54_out, F4);
  not not_55 (not_55_out, OP0);
  not not_56 (not_56_out, OP1);
  not not_57 (not_57_out, OP2);
  not not_58 (not_58_out, OP4);
  not not_59 (not_59_out, OP5);
  not not_60 (not_60_out, F2);
  not not_61 (not_61_out, F4);
  not not_62 (not_62_out, OP0);
  not not_63 (not_63_out, OP1);
  not not_64 (not_64_out, OP2);
  not not_65 (not_65_out, OP4);
  not not_66 (not_66_out, OP5);
  not not_67 (not_67_out, F3);
  not not_68 (not_68_out, F4);
  not not_69 (not_69_out, F5);
  not not_70 (not_70_out, OP0);
  not not_71 (not_71_out, OP1);
  not not_72 (not_72_out, OP2);
  not not_73 (not_73_out, OP4);
  not not_74 (not_74_out, OP5);
  not not_75 (not_75_out, F3);
  not not_76 (not_76_out, F4);
  not not_77 (not_77_out, OP0);
  not not_78 (not_78_out, OP4);
  not not_79 (not_79_out, OP5);
  not not_80 (not_80_out, OP1);
  not not_81 (not_81_out, OP4);
  not not_82 (not_82_out, OP5);
  not not_83 (not_83_out, OP2);
  not not_84 (not_84_out, OP3);
  not not_85 (not_85_out, OP4);
  not not_86 (not_86_out, OP2);
  not not_87 (not_87_out, OP3);
  not not_88 (not_88_out, OP4);
  not not_89 (not_89_out, OP0);
  not not_90 (not_90_out, OP1);
  not not_91 (not_91_out, OP2);
  not not_92 (not_92_out, OP3);
  not not_93 (not_93_out, OP4);
  not not_94 (not_94_out, OP5);
  not not_95 (not_95_out, F0);
  not not_96 (not_96_out, F1);
  not not_97 (not_97_out, F4);
  not not_98 (not_98_out, F5);
  not not_99 (not_99_out, OP5);
  not not_100 (not_100_out, OP4);
  not not_101 (not_101_out, OP3);
  not not_102 (not_102_out, OP1);
  not not_103 (not_103_out, OP0);
  not not_104 (not_104_out, OP5);
  not not_105 (not_105_out, OP4);
  not not_106 (not_106_out, OP3);
  not not_107 (not_107_out, OP1);
  not not_108 (not_108_out, OP5);
  not not_109 (not_109_out, OP4);
  not not_110 (not_110_out, OP2);
  not not_111 (not_111_out, OP1);
  not not_112 (not_112_out, OP0);
  not not_113 (not_113_out, OP5);
  not not_114 (not_114_out, OP4);
  not not_115 (not_115_out, OP2);
  not not_116 (not_116_out, OP1);
  not not_117 (not_117_out, OP5);
  not not_118 (not_118_out, OP4);
  not not_119 (not_119_out, OP2);
  not not_120 (not_120_out, OP0);
  not not_121 (not_121_out, OP4);
  not not_122 (not_122_out, OP3);
  not not_123 (not_123_out, OP2);
  not not_124 (not_124_out, OP4);
  not not_125 (not_125_out, OP2);
  not not_126 (not_126_out, OP4);
  not not_127 (not_127_out, OP3);
  not not_128 (not_128_out, OP2);
  not not_129 (not_129_out, OP1);
  not not_130 (not_130_out, OP5);
  not not_131 (not_131_out, OP4);
  not not_132 (not_132_out, OP3);
  not not_133 (not_133_out, OP2);
  not not_134 (not_134_out, OP1);
  not not_135 (not_135_out, OP0);
  not not_136 (not_136_out, OP1);
  not not_137 (not_137_out, OP2);
  not not_138 (not_138_out, OP3);
  not not_139 (not_139_out, OP4);
  not not_140 (not_140_out, OP5);
  not not_141 (not_141_out, F0);
  not not_142 (not_142_out, F2);
  not not_143 (not_143_out, F3);
  not not_144 (not_144_out, F4);
  not not_145 (not_145_out, OP0);
  not not_146 (not_146_out, OP1);
  not not_147 (not_147_out, OP2);
  not not_148 (not_148_out, OP3);
  not not_149 (not_149_out, OP4);
  not not_150 (not_150_out, OP5);
  not not_151 (not_151_out, F1);
  not not_152 (not_152_out, F3);
  not not_153 (not_153_out, F4);
  not not_154 (not_154_out, OP0);
  not not_155 (not_155_out, OP1);
  not not_156 (not_156_out, OP2);
  not not_157 (not_157_out, OP3);
  not not_158 (not_158_out, OP4);
  not not_159 (not_159_out, OP5);
  not not_160 (not_160_out, F2);
  not not_161 (not_161_out, F4);
  not not_162 (not_162_out, OP0);
  not not_163 (not_163_out, OP1);
  not not_164 (not_164_out, OP2);
  not not_165 (not_165_out, OP3);
  not not_166 (not_166_out, OP4);
  not not_167 (not_167_out, OP5);
  not not_168 (not_168_out, F3);
  not not_169 (not_169_out, F4);
  not not_170 (not_170_out, F5);
  not not_171 (not_171_out, OP0);
  not not_172 (not_172_out, OP1);
  not not_173 (not_173_out, OP2);
  not not_174 (not_174_out, OP3);
  not not_175 (not_175_out, OP4);
  not not_176 (not_176_out, OP5);
  not not_177 (not_177_out, F3);
  not not_178 (not_178_out, F4);
  not not_179 (not_179_out, OP0);
  not not_180 (not_180_out, OP1);
  not not_181 (not_181_out, OP3);
  not not_182 (not_182_out, OP4);
  not not_183 (not_183_out, OP5);
  not not_184 (not_184_out, OP1);
  not not_185 (not_185_out, OP3);
  not not_186 (not_186_out, OP4);
  not not_187 (not_187_out, OP5);
  not not_188 (not_188_out, OP0);
  not not_189 (not_189_out, OP1);
  not not_190 (not_190_out, OP2);
  not not_191 (not_191_out, OP3);
  not not_192 (not_192_out, OP4);
  not not_193 (not_193_out, OP5);
  not not_194 (not_194_out, F0);
  not not_195 (not_195_out, F1);
  not not_196 (not_196_out, F2);
  not not_197 (not_197_out, F4);
  not not_198 (not_198_out, F5);
  not not_199 (not_199_out, OP0);
  not not_200 (not_200_out, OP2);
  not not_201 (not_201_out, OP3);
  not not_202 (not_202_out, OP4);
  not not_203 (not_203_out, OP5);
  not not_204 (not_204_out, F0);
  not not_205 (not_205_out, F1);
  not not_206 (not_206_out, F2);
  not not_207 (not_207_out, F4);
  not not_208 (not_208_out, F5);
  not not_209 (not_209_out, OP2);
  not not_210 (not_210_out, OP3);
  not not_211 (not_211_out, OP4);
  not not_212 (not_212_out, OP5);
  not not_213 (not_213_out, OP2);
  not not_214 (not_214_out, OP3);
  not not_215 (not_215_out, OP4);
  not not_216 (not_216_out, OP5);
  and and_1 (MemToReg, OP0, not_1_out, not_2_out, not_3_out, OP5);
  and and_2 (MemWrite, OP0, OP1, not_4_out, OP3, not_5_out, OP5);
  and and_3 (BLTZ, OP0, not_6_out, not_7_out, not_8_out, not_9_out, not_10_out);
  and and_4 (LH, OP0, not_11_out, not_12_out, not_13_out, not_14_out, OP5);
  and and_5 (SRAV, not_15_out, not_16_out, not_17_out, not_18_out, not_19_out, not_20_out, F0, F1, F2, not_21_out, not_22_out, not_23_out);
  and and_6 (XORI, not_24_out, OP1, OP2, OP3, not_25_out, not_26_out);
  and and_7 (and_7_out, not_27_out, OP3, not_28_out, not_29_out);
  and and_8 (and_8_out, not_30_out, OP3, not_31_out, not_32_out);
  and and_9 (and_9_out, OP0, not_33_out, not_34_out, not_35_out, OP5);
  and and_10 (and_10_out, OP0, OP1, not_36_out, not_37_out, OP5);
  and and_11 (and_11_out, not_38_out, not_39_out, not_40_out, not_41_out, not_42_out, not_43_out, not_44_out, not_45_out, not_46_out);
  and and_12 (and_12_out, not_47_out, not_48_out, not_49_out, not_50_out, not_51_out, not_52_out, not_53_out, not_54_out, F5);
  and and_13 (and_13_out, not_55_out, not_56_out, not_57_out, not_58_out, not_59_out, F1, not_60_out, F3, not_61_out, F5);
  and and_14 (and_14_out, not_62_out, not_63_out, not_64_out, not_65_out, not_66_out, F0, F1, not_67_out, not_68_out, not_69_out);
  and and_15 (and_15_out, not_70_out, not_71_out, not_72_out, not_73_out, not_74_out, F0, F1, F2, not_75_out, not_76_out);
  and and_16 (and_16_out, not_77_out, OP3, not_78_out, not_79_out);
  and and_17 (and_17_out, not_80_out, OP3, not_81_out, not_82_out);
  and and_18 (and_18_out, OP0, not_83_out, not_84_out, not_85_out, OP5);
  and and_19 (and_19_out, OP0, OP1, not_86_out, not_87_out, not_88_out);
  and and_20 (SysCALL, not_89_out, not_90_out, not_91_out, not_92_out, not_93_out, not_94_out, not_95_out, not_96_out, F2, F3, not_97_out, not_98_out);
  and and_21 (and_21_out, not_99_out, not_100_out, not_101_out, OP2, not_102_out, not_103_out);
  and and_22 (and_22_out, not_104_out, not_105_out, not_106_out, OP2, not_107_out, OP0);
  and and_23 (and_23_out, not_108_out, not_109_out, OP3, not_110_out, not_111_out, not_112_out);
  and and_24 (and_24_out, not_113_out, not_114_out, OP3, not_115_out, not_116_out, OP0);
  and and_25 (and_25_out, not_117_out, not_118_out, OP3, not_119_out, OP1, not_120_out);
  and and_26 (and_26_out, OP5, not_121_out, not_122_out, not_123_out, OP1, OP0);
  and and_27 (and_27_out, OP5, not_124_out, OP3, not_125_out, OP1, OP0);
  and and_28 (and_28_out, OP5, not_126_out, not_127_out, not_128_out, not_129_out, OP0);
  and and_29 (and_29_out, not_130_out, not_131_out, not_132_out, not_133_out, not_134_out, OP0);
  and and_30 (and_30_out, not_135_out, not_136_out, not_137_out, not_138_out, not_139_out, not_140_out, not_141_out, not_142_out, not_143_out, not_144_out);
  and and_31 (and_31_out, not_145_out, not_146_out, not_147_out, not_148_out, not_149_out, not_150_out, not_151_out, not_152_out, not_153_out, F5);
  and and_32 (and_32_out, not_154_out, not_155_out, not_156_out, not_157_out, not_158_out, not_159_out, F1, not_160_out, F3, not_161_out, F5);
  and and_33 (and_33_out, not_162_out, not_163_out, not_164_out, not_165_out, not_166_out, not_167_out, F0, F1, not_168_out, not_169_out, not_170_out);
  and and_34 (and_34_out, not_171_out, not_172_out, not_173_out, not_174_out, not_175_out, not_176_out, F0, F1, F2, not_177_out, not_178_out);
  and and_35 (BEQ, not_179_out, not_180_out, OP2, not_181_out, not_182_out, not_183_out);
  and and_36 (BNE, OP0, not_184_out, OP2, not_185_out, not_186_out, not_187_out);
  and and_37 (JR, not_188_out, not_189_out, not_190_out, not_191_out, not_192_out, not_193_out, not_194_out, not_195_out, not_196_out, F3, not_197_out, not_198_out);
  and and_38 (and_38_out, not_199_out, not_200_out, not_201_out, not_202_out, not_203_out, not_204_out, not_205_out, not_206_out, F3, not_207_out, not_208_out);
  and and_39 (and_39_out, OP1, not_209_out, not_210_out, not_211_out, not_212_out);
  and and_40 (JAL, OP0, OP1, not_213_out, not_214_out, not_215_out, not_216_out);
  or or_1 (ALU_SRC, and_7_out, and_8_out, and_9_out, and_10_out);
  or or_2 (RegWrite, and_11_out, and_12_out, and_13_out, and_14_out, and_15_out, and_16_out, and_17_out, and_18_out, and_19_out);
  or or_3 (SignedExt, and_21_out, and_22_out, and_23_out, and_24_out, and_25_out, and_26_out, and_27_out, and_28_out, and_29_out);
  or or_4 (RegDst, and_30_out, and_31_out, and_32_out, and_33_out, and_34_out);
  or or_5 (JUMP, and_38_out, and_39_out);
endmodule

module ALU (
  input  [31:0] X,
  input  [31:0] Y,
  input  [3:0] AluOP,
  input  [4:0] shamt,
  output Equal,
  output [31:0] Result,
  output [31:0] Result_2
);

  wire [0:0] comparator_1_lt, comparator_2_lt;
  wire [31:0] adder_1_out, AND_out, divider_1_out, divider_1_rem, multiplier_1_cout, multiplier_1_out,
       NOR_out, OR_out, shifter_1_out, shifter_2_out, shifter_3_out, subtractor_1_out, XOR_out;

  Shifter #(.width(32), .shift("ll")) shifter_1 (.in(Y), .\dist (shamt), .out(shifter_1_out));
  Shifter #(.width(32), .shift("ar")) shifter_2 (.in(Y), .\dist (shamt), .out(shifter_2_out));
  Shifter #(.width(32), .shift("lr")) shifter_3 (.in(Y), .\dist (shamt), .out(shifter_3_out));
  Multiplier #(.width(32)) multiplier_1 (.a(X), .b(Y), .out(multiplier_1_out), .cout(multiplier_1_cout));  // open: cin
  Divider #(.width(32)) divider_1 (.a(X), .b(Y), .out(divider_1_out), .rem(divider_1_rem));  // open: upper
  Adder #(.width(32)) adder_1 (.a(X), .b(Y), .out(adder_1_out));  // open: cin, cout
  Subtractor #(.width(32)) subtractor_1 (.a(X), .b(Y), .out(subtractor_1_out));  // open: bin, bout
  assign AND_out = X & Y;  // AND_Gate AND, 32 bits wide
  assign OR_out = X | Y;  // OR_Gate OR, 32 bits wide
  assign XOR_out = X ^ Y;  // XOR_Gate XOR, 32 bits wide
  assign NOR_out = ~(X | Y);  // NOR_Gate NOR, 32 bits wide
  Comparator #(.width(32), .mode("twosComplement")) comparator_1 (
    .a(X), .b(Y), .eq(Equal), .lt(comparator_1_lt[0]));  // open: gt
  Comparator #(.width(32), .mode("unsigned")) comparator_2 (.a(X), .b(Y), .lt(comparator_2_lt[0]));  // open: gt, eq
  Multiplexer #(.select(4), .width(32), .disabled("Z"), .enable("false")) multiplexer_1 (
    .in0(shifter_1_out), .in1(shifter_2_out), .in2(shifter_3_out), .in3(multiplier_1_out),
    .in4(divider_1_out), .in5(adder_1_out), .in6(subtractor_1_out), .in7(AND_out), .in8(OR_out),
    .in9(XOR_out), .in10(NOR_out), .in11({{31{1'b0}}, comparator_1_lt[0]}),
    .in12({{31{1'b0}}, comparator_2_lt[0]}), .in13({32{1'b0}}), .in14({32{1'b0}}), .in15({32{1'b0}}),
    .out(Result), .sel(AluOP));
  Multiplexer #(.select(4), .width(32), .disabled("Z"), .enable("false")) multiplexer_2 (
    .in0({32{1'b0}}), .in1({32{1'b0}}), .in2({32{1'b0}}), .in3(multiplier_1_cout), .in4(divider_1_rem),
    .in5({32{1'b0}}), .in6({32{1'b0}}), .in7({32{1'b0}}), .in8({32{1'b0}}), .in9({32{1'b0}}),
    .in10({32{1'b0}}), .in11({32{1'b0}}), .in12({32{1'b0}}), .in13({32{1'b0}}), .in14({32{1'b0}}),
    .in15({32{1'b0}}), .out(Result_2), .sel(AluOP));

  // Other names for the same wires on the sheet: Result2[31:0] = Result_2; S[3:0] = AluOP

  // Notes on the sheet:
  //   输入引脚
  //   输出引脚
endmodule

module Regifile (
  input  [31:0] Din,
  input  Clk,
  input  WE,
  input  [4:0] W_num,
  input  [4:0] R1_num,
  input  [4:0] R2_num,
  output [31:0] R1,
  output [31:0] R2
);

  // RegisterFile registerfile_1: pin names not known; wires that end beside it: Din, Clk, WE, W_num, R1_num, R2_num, R1, R2
endmodule

module IF_ID (
  input  [31:0] IRin32,
  input  [31:0] PCin32,
  input  CTin16,
  input  \传输状态In_表明当前传输数据有效 ,
  input  CLK,
  input  \同步清零_气泡_高电平有效 ,
  input  \使能端_低电平有效_stall_高电平有效 ,
  output [31:0] IRout32,
  output [31:0] PCout32,
  output CTout16,
  output \传输状态Out_表明当前传输数据有效 
);

  wire multiplexer_3_out, multiplexer_4_out, pull_resistor_2_node;
  wire [31:0] multiplexer_1_out, multiplexer_2_out;

  Multiplexer #(.select(1), .width(32), .disabled("Z"), .enable("false")) multiplexer_1 (
    .in0(IRin32), .in1({32{1'b0}}), .out(multiplexer_1_out), .sel(\同步清零_气泡_高电平有效 ));
  Multiplexer #(.select(1), .width(32), .disabled("Z"), .enable("false")) multiplexer_2 (
    .in0(PCin32), .in1({32{1'b0}}), .out(multiplexer_2_out), .sel(\同步清零_气泡_高电平有效 ));
  Multiplexer #(.select(1), .width(1), .disabled("Z"), .enable("false")) multiplexer_3 (
    .in0(CTin16), .in1(1'b0), .out(multiplexer_3_out), .sel(\同步清零_气泡_高电平有效 ));
  Multiplexer #(.select(1), .width(1), .disabled("Z"), .enable("false")) multiplexer_4 (
    .in0(\传输状态In_表明当前传输数据有效 ), .in1(1'b0), .out(multiplexer_4_out), .sel(\同步清零_气泡_高电平有效 ));
  Pull_Resistor #(.pull(0)) pull_resistor_1 (.node(\同步清零_气泡_高电平有效 ));
  Register #(.width(32), .trigger("rising"), .Select("low")) register_1 (
    .D(multiplexer_1_out), .en(pull_resistor_2_node), .Q(IRout32), .clk(CLK));  // open: clr
  Register #(.width(32), .trigger("rising"), .Select("low")) register_2 (
    .D(multiplexer_2_out), .en(pull_resistor_2_node), .Q(PCout32), .clk(CLK));  // open: clr
  Register #(.width(1), .trigger("rising"), .Select("low")) register_3 (
    .D(multiplexer_3_out), .en(pull_resistor_2_node), .Q(CTout16), .clk(CLK));  // open: clr
  Register #(.width(1), .trigger("rising"), .Select("low")) register_4 (
    .D(multiplexer_4_out), .en(pull_resistor_2_node), .Q(\传输状态Out_表明当前传输数据有效 ), .clk(CLK));  // open: clr
  Pull_Resistor #(.pull(0)) pull_resistor_2 (.node(pull_resistor_2_node));
  not not_1 (pull_resistor_2_node, \使能端_低电平有效_stall_高电平有效 );

  // Notes on the sheet:
  //   同步清零_气泡_高电平有效: pull=down
  //   使能端_低电平有效_stall_高电平有效: pull=down
endmodule

module ID_EX (
  input  [31:0] R1in32,
  input  [31:0] R2in32,
  input  [31:0] IRin32,
  input  [31:0] PCin32,
  input  [31:0] IMMin32,
  input  [31:0] _26in32,
  input  [4:0] WBin5,
  input  [3:0] CTRL4,
  input  [1:0] ERETin1,
  input  ERETin1_2,
  input  [4:0] SHin5,
  input  [15:0] CTin16,
  input  [1:0] FWR1in2,
  input  [1:0] FWR2in2,
  input  \传输状态In_表明当前传输数据有效 ,
  input  CLK,
  input  \同步清零_气泡_高电平有效 ,
  input  \使能端_低电平有效_stall_高电平有效 ,
  output [31:0] R1out32,
  output [31:0] R2out32,
  output [31:0] IRout32,
  output [31:0] PCout32,
  output [31:0] R1out32_2,
  output [31:0] R1out32_3,
  output [4:0] WBout5,
  output [3:0] CTRL4_2,
  output [1:0] SHout5,
  output SHout5_2,
  output [4:0] SHout5_3,
  output [15:0] CTout16,
  output [1:0] WBout5_2,
  output [1:0] SHout5_4,
  output \传输状态Out_表明当前传输数据有效 
);

  wire multiplexer_10_out, multiplexer_15_out, pull_resistor_2_node;
  wire [1:0] multiplexer_9_out, multiplexer_13_out, multiplexer_14_out;
  wire [3:0] multiplexer_8_out;
  wire [4:0] multiplexer_7_out, multiplexer_11_out;
  wire [15:0] multiplexer_12_out;
  wire [31:0] multiplexer_1_out, multiplexer_2_out, multiplexer_3_out, multiplexer_4_out, multiplexer_5_out,
       multiplexer_6_out;

  Multiplexer #(.select(1), .width(32), .disabled("Z"), .enable("false")) multiplexer_1 (
    .in0(R1in32), .in1({32{1'b0}}), .out(multiplexer_1_out), .sel(\同步清零_气泡_高电平有效 ));
  Multiplexer #(.select(1), .width(32), .disabled("Z"), .enable("false")) multiplexer_2 (
    .in0(R2in32), .in1({32{1'b0}}), .out(multiplexer_2_out), .sel(\同步清零_气泡_高电平有效 ));
  Multiplexer #(.select(1), .width(32), .disabled("Z"), .enable("false")) multiplexer_3 (
    .in0(IRin32), .in1({32{1'b0}}), .out(multiplexer_3_out), .sel(\同步清零_气泡_高电平有效 ));
  Multiplexer #(.select(1), .width(32), .disabled("Z"), .enable("false")) multiplexer_4 (
    .in0(PCin32), .in1({32{1'b0}}), .out(multiplexer_4_out), .sel(\同步清零_气泡_高电平有效 ));
  Multiplexer #(.select(1), .width(32), .disabled("Z"), .enable("false")) multiplexer_5 (
    .in0(IMMin32), .in1({32{1'b0}}), .out(multiplexer_5_out), .sel(\同步清零_气泡_高电平有效 ));
  Multiplexer #(.select(1), .width(32), .disabled("Z"), .enable("false")) multiplexer_6 (
    .in0(_26in32), .in1({32{1'b0}}), .out(multiplexer_6_out), .sel(\同步清零_气泡_高电平有效 ));
  Multiplexer #(.select(1), .width(5), .disabled("Z"), .enable("false")) multiplexer_7 (
    .in0(WBin5), .in1({5{1'b0}}), .out(multiplexer_7_out), .sel(\同步清零_气泡_高电平有效 ));
  Multiplexer #(.select(1), .width(4), .disabled("Z"), .enable("false")) multiplexer_8 (
    .in0(CTRL4), .in1(4'b0000), .out(multiplexer_8_out), .sel(\同步清零_气泡_高电平有效 ));
  Multiplexer #(.select(1), .width(2), .disabled("Z"), .enable("false")) multiplexer_9 (
    .in0(ERETin1), .in1(2'b00), .out(multiplexer_9_out), .sel(\同步清零_气泡_高电平有效 ));
  Multiplexer #(.select(1), .width(1), .disabled("Z"), .enable("false")) multiplexer_10 (
    .in0(ERETin1_2), .in1(1'b0), .out(multiplexer_10_out), .sel(\同步清零_气泡_高电平有效 ));
  Multiplexer #(.select(1), .width(5), .disabled("Z"), .enable("false")) multiplexer_11 (
    .in0(SHin5), .in1({5{1'b0}}), .out(multiplexer_11_out), .sel(\同步清零_气泡_高电平有效 ));
  Multiplexer #(.select(1), .width(16), .disabled("Z"), .enable("false")) multiplexer_12 (
    .in0(CTin16), .in1({16{1'b0}}), .out(multiplexer_12_out), .sel(\同步清零_气泡_高电平有效 ));
  Multiplexer #(.select(1), .width(2), .disabled("Z"), .enable("false")) multiplexer_13 (
    .in0(FWR1in2), .in1(2'b00), .out(multiplexer_13_out), .sel(\同步清零_气泡_高电平有效 ));
  Multiplexer #(.select(1), .width(2), .disabled("Z"), .enable("false")) multiplexer_14 (
    .in0(FWR2in2), .in1(2'b00), .out(multiplexer_14_out), .sel(\同步清零_气泡_高电平有效 ));
  Multiplexer #(.select(1), .width(1), .disabled("Z"), .enable("false")) multiplexer_15 (
    .in0(\传输状态In_表明当前传输数据有效 ), .in1(1'b0), .out(multiplexer_15_out), .sel(\同步清零_气泡_高电平有效 ));
  Pull_Resistor #(.pull(0)) pull_resistor_1 (.node(\同步清零_气泡_高电平有效 ));
  Pull_Resistor #(.pull(0)) pull_resistor_2 (.node(pull_resistor_2_node));
  not not_1 (pull_resistor_2_node, \使能端_低电平有效_stall_高电平有效 );
  Register #(.width(32), .trigger("rising"), .Select("low")) register_1 (
    .D(multiplexer_1_out), .en(pull_resistor_2_node), .Q(R1out32), .clk(CLK));  // open: clr
  Register #(.width(32), .trigger("rising"), .Select("low")) register_2 (
    .D(multiplexer_2_out), .en(pull_resistor_2_node), .Q(R2out32), .clk(CLK));  // open: clr
  Register #(.width(32), .trigger("rising"), .Select("low")) register_3 (
    .D(multiplexer_3_out), .en(pull_resistor_2_node), .Q(IRout32), .clk(CLK));  // open: clr
  Register #(.width(32), .trigger("rising"), .Select("low")) register_4 (
    .D(multiplexer_4_out), .en(pull_resistor_2_node), .Q(PCout32), .clk(CLK));  // open: clr
  Register #(.width(32), .trigger("rising"), .Select("low")) register_5 (
    .D(multiplexer_5_out), .en(pull_resistor_2_node), .Q(R1out32_2), .clk(CLK));  // open: clr
  Register #(.width(32), .trigger("rising"), .Select("low")) register_6 (
    .D(multiplexer_6_out), .en(pull_resistor_2_node), .Q(R1out32_3), .clk(CLK));  // open: clr
  Register #(.width(5), .trigger("rising"), .Select("low")) register_7 (
    .D(multiplexer_7_out), .en(pull_resistor_2_node), .Q(WBout5), .clk(CLK));  // open: clr
  Register #(.width(4), .trigger("rising"), .Select("low")) register_8 (
    .D(multiplexer_8_out), .en(pull_resistor_2_node), .Q(CTRL4_2), .clk(CLK));  // open: clr
  Register #(.width(2), .trigger("rising"), .Select("low")) register_9 (
    .D(multiplexer_9_out), .en(pull_resistor_2_node), .Q(SHout5), .clk(CLK));  // open: clr
  Register #(.width(1), .trigger("rising"), .Select("low")) register_10 (
    .D(multiplexer_10_out), .en(pull_resistor_2_node), .Q(SHout5_2), .clk(CLK));  // open: clr
  Register #(.width(5), .trigger("rising"), .Select("low")) register_11 (
    .D(multiplexer_11_out), .en(pull_resistor_2_node), .Q(SHout5_3), .clk(CLK));  // open: clr
  Register #(.width(16), .trigger("rising"), .Select("low")) register_12 (
    .D(multiplexer_12_out), .en(pull_resistor_2_node), .Q(CTout16), .clk(CLK));  // open: clr
  Register #(.width(2), .trigger("rising"), .Select("low")) register_13 (
    .D(multiplexer_13_out), .en(pull_resistor_2_node), .Q(WBout5_2), .clk(CLK));  // open: clr
  Register #(.width(2), .trigger("rising"), .Select("low")) register_14 (
    .D(multiplexer_14_out), .en(pull_resistor_2_node), .Q(SHout5_4), .clk(CLK));  // open: clr
  Register #(.width(1), .trigger("rising"), .Select("low")) register_15 (
    .D(multiplexer_15_out), .en(pull_resistor_2_node), .Q(\传输状态Out_表明当前传输数据有效 ), .clk(CLK));  // open: clr

  // Notes on the sheet:
  //   使能端_低电平有效_stall_高电平有效: pull=down
  //   同步清零_气泡_高电平有效: pull=down
endmodule

module EX_MEM (
  input  [31:0] ALUin32,
  input  [31:0] Memin32,
  input  CTin16,
  input  [3:0] CTin4,
  input  [31:0] Resullt2,
  input  ERETin2,
  input  [1:0] ERETin2_2,
  input  [31:0] IRin32,
  input  [31:0] PCin32,
  input  [4:0] WBin5,
  input  [31:0] LEDin32,
  input  [15:0] CTin16_2,
  input  \传输状态In_表明当前传输数据有效 ,
  input  CLK,
  input  \同步清零_气泡_高电平有效 ,
  input  \使能端_低电平有效_stall_高电平有效 ,
  output [31:0] ALUout32,
  output [31:0] Memout32,
  output CTout16,
  output [3:0] CTout16_2,
  output [31:0] CTout16_3,
  output CTout16_4,
  output [1:0] CTout16_5,
  output [31:0] IRout32,
  output [31:0] PCout32,
  output [4:0] WBout5,
  output [31:0] LEDout32,
  output [15:0] CTout16_6,
  output \传输状态Out_表明当前传输数据有效 
);

  wire multiplexer_3_out, multiplexer_6_out, multiplexer_13_out, pull_resistor_2_node;
  wire [1:0] multiplexer_7_out;
  wire [3:0] multiplexer_4_out;
  wire [4:0] multiplexer_10_out;
  wire [15:0] multiplexer_12_out;
  wire [31:0] multiplexer_1_out, multiplexer_2_out, multiplexer_5_out, multiplexer_8_out, multiplexer_9_out,
       multiplexer_11_out;

  Multiplexer #(.select(1), .width(32), .disabled("Z"), .enable("false")) multiplexer_1 (
    .in0(ALUin32), .in1({32{1'b0}}), .out(multiplexer_1_out), .sel(\同步清零_气泡_高电平有效 ));
  Multiplexer #(.select(1), .width(32), .disabled("Z"), .enable("false")) multiplexer_2 (
    .in0(Memin32), .in1({32{1'b0}}), .out(multiplexer_2_out), .sel(\同步清零_气泡_高电平有效 ));
  Multiplexer #(.select(1), .width(1), .disabled("Z"), .enable("false")) multiplexer_3 (
    .in0(CTin16), .in1(1'b0), .out(multiplexer_3_out), .sel(\同步清零_气泡_高电平有效 ));
  Multiplexer #(.select(1), .width(4), .disabled("Z"), .enable("false")) multiplexer_4 (
    .in0(CTin4), .in1(4'b0000), .out(multiplexer_4_out), .sel(\同步清零_气泡_高电平有效 ));
  Multiplexer #(.select(1), .width(32), .disabled("Z"), .enable("false")) multiplexer_5 (
    .in0(Resullt2), .in1({32{1'b0}}), .out(multiplexer_5_out), .sel(\同步清零_气泡_高电平有效 ));
  Multiplexer #(.select(1), .width(1), .disabled("Z"), .enable("false")) multiplexer_6 (
    .in0(ERETin2), .in1(1'b0), .out(multiplexer_6_out), .sel(\同步清零_气泡_高电平有效 ));
  Multiplexer #(.select(1), .width(2), .disabled("Z"), .enable("false")) multiplexer_7 (
    .in0(ERETin2_2), .in1(2'b00), .out(multiplexer_7_out), .sel(\同步清零_气泡_高电平有效 ));
  Multiplexer #(.select(1), .width(32), .disabled("Z"), .enable("false")) multiplexer_8 (
    .in0(IRin32), .in1({32{1'b0}}), .out(multiplexer_8_out), .sel(\同步清零_气泡_高电平有效 ));
  Multiplexer #(.select(1), .width(32), .disabled("Z"), .enable("false")) multiplexer_9 (
    .in0(PCin32), .in1({32{1'b0}}), .out(multiplexer_9_out), .sel(\同步清零_气泡_高电平有效 ));
  Multiplexer #(.select(1), .width(5), .disabled("Z"), .enable("false")) multiplexer_10 (
    .in0(WBin5), .in1({5{1'b0}}), .out(multiplexer_10_out), .sel(\同步清零_气泡_高电平有效 ));
  Multiplexer #(.select(1), .width(32), .disabled("Z"), .enable("false")) multiplexer_11 (
    .in0(LEDin32), .in1({32{1'b0}}), .out(multiplexer_11_out), .sel(\同步清零_气泡_高电平有效 ));
  Multiplexer #(.select(1), .width(16), .disabled("Z"), .enable("false")) multiplexer_12 (
    .in0(CTin16_2), .in1({16{1'b0}}), .out(multiplexer_12_out), .sel(\同步清零_气泡_高电平有效 ));
  Multiplexer #(.select(1), .width(1), .disabled("Z"), .enable("false")) multiplexer_13 (
    .in0(\传输状态In_表明当前传输数据有效 ), .in1(1'b0), .out(multiplexer_13_out), .sel(\同步清零_气泡_高电平有效 ));
  Pull_Resistor #(.pull(0)) pull_resistor_1 (.node(\同步清零_气泡_高电平有效 ));
  Pull_Resistor #(.pull(0)) pull_resistor_2 (.node(pull_resistor_2_node));
  not not_1 (pull_resistor_2_node, \使能端_低电平有效_stall_高电平有效 );
  Register #(.width(32), .trigger("rising"), .Select("low")) register_1 (
    .D(multiplexer_1_out), .en(pull_resistor_2_node), .Q(ALUout32), .clk(CLK));  // open: clr
  Register #(.width(32), .trigger("rising"), .Select("low")) register_2 (
    .D(multiplexer_2_out), .en(pull_resistor_2_node), .Q(Memout32), .clk(CLK));  // open: clr
  Register #(.width(1), .trigger("rising"), .Select("low")) register_3 (
    .D(multiplexer_3_out), .en(pull_resistor_2_node), .Q(CTout16), .clk(CLK));  // open: clr
  Register #(.width(4), .trigger("rising"), .Select("low")) register_4 (
    .D(multiplexer_4_out), .en(pull_resistor_2_node), .Q(CTout16_2), .clk(CLK));  // open: clr
  Register #(.width(32), .trigger("rising"), .Select("low")) register_5 (
    .D(multiplexer_5_out), .en(pull_resistor_2_node), .Q(CTout16_3), .clk(CLK));  // open: clr
  Register #(.width(1), .trigger("rising"), .Select("low")) register_6 (
    .D(multiplexer_6_out), .en(pull_resistor_2_node), .Q(CTout16_4), .clk(CLK));  // open: clr
  Register #(.width(2), .trigger("rising"), .Select("low")) register_7 (
    .D(multiplexer_7_out), .en(pull_resistor_2_node), .Q(CTout16_5), .clk(CLK));  // open: clr
  Register #(.width(32), .trigger("rising"), .Select("low")) register_8 (
    .D(multiplexer_8_out), .en(pull_resistor_2_node), .Q(IRout32), .clk(CLK));  // open: clr
  Register #(.width(32), .trigger("rising"), .Select("low")) register_9 (
    .D(multiplexer_9_out), .en(pull_resistor_2_node), .Q(PCout32), .clk(CLK));  // open: clr
  Register #(.width(5), .trigger("rising"), .Select("low")) register_10 (
    .D(multiplexer_10_out), .en(pull_resistor_2_node), .Q(WBout5), .clk(CLK));  // open: clr
  Register #(.width(32), .trigger("rising"), .Select("low")) register_11 (
    .D(multiplexer_11_out), .en(pull_resistor_2_node), .Q(LEDout32), .clk(CLK));  // open: clr
  Register #(.width(16), .trigger("rising"), .Select("low")) register_12 (
    .D(multiplexer_12_out), .en(pull_resistor_2_node), .Q(CTout16_6), .clk(CLK));  // open: clr
  Register #(.width(1), .trigger("rising"), .Select("low")) register_13 (
    .D(multiplexer_13_out), .en(pull_resistor_2_node), .Q(\传输状态Out_表明当前传输数据有效 ), .clk(CLK));  // open: clr

  // Notes on the sheet:
  //   同步清零_气泡_高电平有效: pull=down
  //   使能端_低电平有效_stall_高电平有效: pull=down
endmodule

module MEM_WB (
  input  [31:0] ALUin32,
  input  [31:0] MDin32,
  input  [31:0] IRin32,
  input  [31:0] PCin32,
  input  [3:0] CTin4,
  input  [31:0] RE2in32,
  input  ERETin1,
  input  [1:0] ERETin1_2,
  input  [4:0] WBin5,
  input  [31:0] LEDin32,
  input  CTin16,
  input  [15:0] CTin16_2,
  input  \传输状态In_表明当前传输数据有效 ,
  input  CLK,
  input  \同步清零_气泡_高电平有效 ,
  input  \使能端_低电平有效_stall_高电平有效 ,
  output [31:0] ALUout32,
  output [31:0] MDout32,
  output [31:0] IRout32,
  output [31:0] PCout32,
  output [3:0] CTout16,
  output [31:0] CTout16_2,
  output CTout16_3,
  output [1:0] CTout16_4,
  output [4:0] WBout5,
  output [31:0] LEDout32,
  output CTout16_5,
  output [15:0] CTout16_6,
  output \传输状态Out_表明当前传输数据有效 
);

  wire multiplexer_7_out, multiplexer_11_out, multiplexer_13_out, not_1_out;
  wire [1:0] multiplexer_8_out;
  wire [3:0] multiplexer_5_out;
  wire [4:0] multiplexer_9_out;
  wire [15:0] multiplexer_12_out;
  wire [31:0] multiplexer_1_out, multiplexer_2_out, multiplexer_3_out, multiplexer_4_out, multiplexer_6_out,
       multiplexer_10_out;

  Multiplexer #(.select(1), .width(32), .disabled("Z"), .enable("false")) multiplexer_1 (
    .in0(ALUin32), .in1({32{1'b0}}), .out(multiplexer_1_out), .sel(\同步清零_气泡_高电平有效 ));
  Multiplexer #(.select(1), .width(32), .disabled("Z"), .enable("false")) multiplexer_2 (
    .in0(MDin32), .in1({32{1'b0}}), .out(multiplexer_2_out), .sel(\同步清零_气泡_高电平有效 ));
  Multiplexer #(.select(1), .width(32), .disabled("Z"), .enable("false")) multiplexer_3 (
    .in0(IRin32), .in1({32{1'b0}}), .out(multiplexer_3_out), .sel(\同步清零_气泡_高电平有效 ));
  Multiplexer #(.select(1), .width(32), .disabled("Z"), .enable("false")) multiplexer_4 (
    .in0(PCin32), .in1({32{1'b0}}), .out(multiplexer_4_out), .sel(\同步清零_气泡_高电平有效 ));
  Multiplexer #(.select(1), .width(4), .disabled("Z"), .enable("false")) multiplexer_5 (
    .in0(CTin4), .in1(4'b0000), .out(multiplexer_5_out), .sel(\同步清零_气泡_高电平有效 ));
  Multiplexer #(.select(1), .width(32), .disabled("Z"), .enable("false")) multiplexer_6 (
    .in0(RE2in32), .in1({32{1'b0}}), .out(multiplexer_6_out), .sel(\同步清零_气泡_高电平有效 ));
  Multiplexer #(.select(1), .width(1), .disabled("Z"), .enable("false")) multiplexer_7 (
    .in0(ERETin1), .in1(1'b0), .out(multiplexer_7_out), .sel(\同步清零_气泡_高电平有效 ));
  Multiplexer #(.select(1), .width(2), .disabled("Z"), .enable("false")) multiplexer_8 (
    .in0(ERETin1_2), .in1(2'b00), .out(multiplexer_8_out), .sel(\同步清零_气泡_高电平有效 ));
  Multiplexer #(.select(1), .width(5), .disabled("Z"), .enable("false")) multiplexer_9 (
    .in0(WBin5), .in1({5{1'b0}}), .out(multiplexer_9_out), .sel(\同步清零_气泡_高电平有效 ));
  Multiplexer #(.select(1), .width(32), .disabled("Z"), .enable("false")) multiplexer_10 (
    .in0(LEDin32), .in1({32{1'b0}}), .out(multiplexer_10_out), .sel(\同步清零_气泡_高电平有效 ));
  Multiplexer #(.select(1), .width(1), .disabled("Z"), .enable("false")) multiplexer_11 (
    .in0(CTin16), .in1(1'b0), .out(multiplexer_11_out), .sel(\同步清零_气泡_高电平有效 ));
  Multiplexer #(.select(1), .width(16), .disabled("Z"), .enable("false")) multiplexer_12 (
    .in0(CTin16_2), .in1({16{1'b0}}), .out(multiplexer_12_out), .sel(\同步清零_气泡_高电平有效 ));
  Multiplexer #(.select(1), .width(1), .disabled("Z"), .enable("false")) multiplexer_13 (
    .in0(\传输状态In_表明当前传输数据有效 ), .in1(1'b0), .out(multiplexer_13_out), .sel(\同步清零_气泡_高电平有效 ));
  Pull_Resistor #(.pull(0)) pull_resistor_1 (.node(\同步清零_气泡_高电平有效 ));
  Register #(.width(32), .trigger("rising"), .Select("low")) register_1 (
    .D(multiplexer_1_out), .en(not_1_out), .Q(ALUout32), .clk(CLK));  // open: clr
  Register #(.width(32), .trigger("rising"), .Select("low")) register_2 (
    .D(multiplexer_2_out), .en(not_1_out), .Q(MDout32), .clk(CLK));  // open: clr
  Register #(.width(32), .trigger("rising"), .Select("low")) register_3 (
    .D(multiplexer_3_out), .en(not_1_out), .Q(IRout32), .clk(CLK));  // open: clr
  Register #(.width(32), .trigger("rising"), .Select("low")) register_4 (
    .D(multiplexer_4_out), .en(not_1_out), .Q(PCout32), .clk(CLK));  // open: clr
  Register #(.width(4), .trigger("rising"), .Select("low")) register_5 (
    .D(multiplexer_5_out), .en(not_1_out), .Q(CTout16), .clk(CLK));  // open: clr
  Register #(.width(32), .trigger("rising"), .Select("low")) register_6 (
    .D(multiplexer_6_out), .en(not_1_out), .Q(CTout16_2), .clk(CLK));  // open: clr
  Register #(.width(1), .trigger("rising"), .Select("low")) register_7 (
    .D(multiplexer_7_out), .en(not_1_out), .Q(CTout16_3), .clk(CLK));  // open: clr
  Register #(.width(2), .trigger("rising"), .Select("low")) register_8 (
    .D(multiplexer_8_out), .en(not_1_out), .Q(CTout16_4), .clk(CLK));  // open: clr
  not not_1 (not_1_out, \使能端_低电平有效_stall_高电平有效 );
  Register #(.width(5), .trigger("rising"), .Select("low")) register_9 (
    .D(multiplexer_9_out), .en(not_1_out), .Q(WBout5), .clk(CLK));  // open: clr
  Register #(.width(32), .trigger("rising"), .Select("low")) register_10 (
    .D(multiplexer_10_out), .en(not_1_out), .Q(LEDout32), .clk(CLK));  // open: clr
  Register #(.width(1), .trigger("rising"), .Select("low")) register_11 (
    .D(multiplexer_11_out), .en(not_1_out), .Q(CTout16_5), .clk(CLK));  // open: clr
  Register #(.width(16), .trigger("rising"), .Select("low")) register_12 (
    .D(multiplexer_12_out), .en(not_1_out), .Q(CTout16_6), .clk(CLK));  // open: clr
  Register #(.width(1), .trigger("rising"), .Select("low")) register_13 (
    .D(multiplexer_13_out), .en(not_1_out), .Q(\传输状态Out_表明当前传输数据有效 ), .clk(CLK));  // open: clr
  Pull_Resistor #(.pull(0)) pull_resistor_2 (.node(not_1_out));

  // Notes on the sheet:
  //   使能端_低电平有效_stall_高电平有效: pull=down
  //   同步清零_气泡_高电平有效: pull=down
endmodule

module MIPS_RAM (
  input  CLK,
  input  WE,
  input  [9:0] \字节地址 ,
  input  [31:0] Din,
  input  Mode,
  input  LH,
  output [31:0] DataOut
);

  wire [7:0] Dout0, Dout1, Dout2, Dout3, \计数器_q ;
  wire [15:0] multiplexer_1_out;
  wire [31:0] bit_extender_1_out;

  RAM #(.addrWidth(10), .dataWidth(8), .bus("separate"), .Select("high")) ram_1 (
    .addr(\字节地址 ), .din(Din[31:24]), .data(Dout3), .str(WE), .clk(CLK));  // open: sel, ld, clr
  RAM #(.addrWidth(10), .dataWidth(8), .bus("separate"), .Select("high")) ram_2 (
    .addr(\字节地址 ), .din(Din[23:16]), .data(Dout2), .str(WE), .clk(CLK));  // open: sel, ld, clr
  Multiplexer #(.select(1), .width(16), .disabled("Z"), .enable("false")) multiplexer_1 (
    .in0({Dout1, Dout0}), .in1({Dout3, Dout2}), .out(multiplexer_1_out), .sel(Mode));
  Multiplexer #(.select(1), .width(32), .disabled("Z"), .enable("false")) multiplexer_2 (
    .in0({Dout3, Dout2, Dout1, Dout0}), .in1(bit_extender_1_out), .out(DataOut), .sel(LH));
  assign bit_extender_1_out = {{16{multiplexer_1_out[15]}}, multiplexer_1_out};  // Bit_Extender bit_extender_1
  RAM #(.addrWidth(10), .dataWidth(8), .bus("separate"), .Select("high")) ram_3 (
    .addr(\字节地址 ), .din(Din[15:8]), .data(Dout1), .str(WE), .clk(CLK));  // open: sel, ld, clr
  // Probe on \计数器_q 
  Counter #(.width(8), .max('hff), .ongoal("wrap"), .trigger("rising"), .behavior("old")) \u_计数器  (
    .Q(\计数器_q ), .clk(CLK));  // open: load, D, count, carry, clr, preset
  RAM #(.addrWidth(10), .dataWidth(8), .bus("separate"), .Select("high")) ram_4 (
    .addr(\字节地址 ), .din(Din[7:0]), .data(Dout0), .str(WE), .clk(CLK));  // open: sel, ld, clr

  // Other names for the same wires on the sheet: Din0[7:0] = Din[7:0]; Din1[7:0] = Din[15:8]; Din2[7:0] = Din[23:16];
  //   Din3[7:0] = Din[31:24]; Dout[31:0] = DataOut

  // Notes on the sheet:
  //   输入引脚区
  //   输出引脚区
endmodule

module \重定向检测  (
  input  MEM_MemToReg,
  input  [4:0] ID_R1,
  input  [4:0] EX_WriteReg,
  input  EX_RegWrite,
  input  [4:0] MEM_WriteReg,
  input  MEM_RegWrite,
  input  EX_MemToReg,
  input  [5:0] OP,
  input  [5:0] Func,
  input  [4:0] ID_R2,
  output [1:0] ForwardToR1,
  output Load_Use,
  output [1:0] ForwardToR2
);

  wire and_1_out, and_2_out, and_3_out, and_4_out, and_5_out, and_6_out, and_7_out, and_8_out,
       comparator_1_eq, comparator_2_eq, comparator_3_eq, comparator_4_eq, comparator_5_eq, comparator_6_eq,
       not_1_out, not_2_out, or_1_out, or_2_out, or_3_out, \源寄存器使用情况_1_r1_used , \源寄存器使用情况_1_r2_used ;
  wire [1:0] multiplexer_1_out, multiplexer_2_out, multiplexer_4_out, multiplexer_6_out;

  Multiplexer #(.select(1), .width(2), .disabled("Z"), .enable("false")) multiplexer_1 (
    .in0(2'b01), .in1(2'b10), .out(multiplexer_1_out), .sel(MEM_MemToReg));
  Comparator #(.width(5), .mode("twosComplement")) comparator_1 (
    .a(ID_R1), .b(EX_WriteReg), .eq(comparator_1_eq));  // open: gt, lt
  Comparator #(.width(5), .mode("twosComplement")) comparator_2 (
    .a(ID_R1), .b(MEM_WriteReg), .eq(comparator_2_eq));  // open: gt, lt
  Comparator #(.width(5), .mode("twosComplement")) comparator_3 (
    .a(ID_R2), .b(EX_WriteReg), .eq(comparator_3_eq));  // open: gt, lt
  Comparator #(.width(5), .mode("twosComplement")) comparator_4 (
    .a(ID_R2), .b(MEM_WriteReg), .eq(comparator_4_eq));  // open: gt, lt
  Multiplexer #(.select(1), .width(2), .disabled("Z"), .enable("false")) multiplexer_2 (
    .in0(2'b01), .in1(2'b10), .out(multiplexer_2_out), .sel(MEM_MemToReg));
  Multiplexer #(.select(1), .width(2), .disabled("Z"), .enable("false")) multiplexer_3 (
    .in0(2'b00), .in1(multiplexer_4_out), .out(ForwardToR1), .sel(and_5_out));
  Multiplexer #(.select(1), .width(2), .disabled("Z"), .enable("false")) multiplexer_4 (
    .in0(multiplexer_1_out), .in1(2'b11), .out(multiplexer_4_out), .sel(comparator_1_eq));
  \源寄存器使用情况  \u_源寄存器使用情况_1  (
    .OP0(OP[0]), .OP1(OP[1]), .OP2(OP[2]), .OP3(OP[3]), .OP4(OP[4]), .OP5(OP[5]), .F0(Func[0]), .F1(Func[1]),
    .F2(Func[2]), .F3(Func[3]), .F4(Func[4]), .F5(Func[5]), .R1_used(\源寄存器使用情况_1_r1_used ),
    .R2_used(\源寄存器使用情况_1_r2_used ));
  Multiplexer #(.select(1), .width(2), .disabled("Z"), .enable("false")) multiplexer_5 (
    .in0(2'b00), .in1(multiplexer_6_out), .out(ForwardToR2), .sel(and_6_out));
  Multiplexer #(.select(1), .width(2), .disabled("Z"), .enable("false")) multiplexer_6 (
    .in0(multiplexer_2_out), .in1(2'b11), .out(multiplexer_6_out), .sel(comparator_3_eq));
  Comparator #(.width(5), .mode("twosComplement")) comparator_5 (
    .a(ID_R1), .b({5{1'b0}}), .eq(comparator_5_eq));  // open: gt, lt
  not not_1 (not_1_out, comparator_5_eq);
  and and_1 (and_1_out, comparator_1_eq, EX_RegWrite);
  and and_2 (and_2_out, comparator_2_eq, MEM_RegWrite);
  and and_3 (and_3_out, comparator_3_eq, EX_RegWrite);
  and and_4 (and_4_out, comparator_4_eq, MEM_RegWrite);
  Comparator #(.width(5), .mode("twosComplement")) comparator_6 (
    .a(ID_R2), .b({5{1'b0}}), .eq(comparator_6_eq));  // open: gt, lt
  not not_2 (not_2_out, comparator_6_eq);
  or or_1 (or_1_out, and_1_out, and_2_out);
  or or_2 (or_2_out, and_3_out, and_4_out);
  and and_5 (and_5_out, not_1_out, or_1_out, \源寄存器使用情况_1_r1_used );
  and and_6 (and_6_out, \源寄存器使用情况_1_r2_used , or_2_out, not_2_out);
  and and_7 (and_7_out, not_1_out, and_1_out, \源寄存器使用情况_1_r1_used );
  and and_8 (and_8_out, \源寄存器使用情况_1_r2_used , and_3_out, not_2_out);
  or or_3 (or_3_out, and_7_out, and_8_out);
  and and_9 (Load_Use, EX_MemToReg, or_3_out);
endmodule
module \源寄存器使用情况  (
  input  OP0,
  input  OP1,
  input  OP2,
  input  OP3,
  input  OP4,
  input  OP5,
  input  F0,
  input  F1,
  input  F2,
  input  F3,
  input  F4,
  input  F5,
  output R1_used,
  output R2_used
);

  wire and_1_out, and_2_out, and_3_out, and_4_out, and_5_out, and_6_out, and_7_out, and_8_out, and_9_out,
       and_10_out, and_11_out, and_12_out, and_13_out, and_14_out, and_15_out, and_16_out, and_17_out,
       and_18_out, and_19_out, and_20_out, and_21_out, and_22_out, and_23_out, and_24_out, and_25_out,
       and_26_out, and_27_out, and_28_out, and_29_out, and_30_out, and_31_out, and_32_out, and_33_out,
       and_34_out, and_35_out, and_36_out, and_37_out, and_38_out, and_39_out, and_40_out, and_41_out,
       and_42_out, and_43_out, and_44_out, not_1_out, not_2_out, not_3_out, not_4_out, not_5_out, not_6_out,
       not_7_out, not_8_out, not_9_out, not_10_out, not_11_out, not_12_out, not_13_out, not_14_out,
       not_15_out, not_16_out, not_17_out, not_18_out, not_19_out, not_20_out, not_21_out, not_22_out,
       not_23_out, not_24_out, not_25_out, not_26_out, not_27_out, not_28_out, not_29_out, not_30_out,
       not_31_out, not_32_out, not_33_out, not_34_out, not_35_out, not_36_out, not_37_out, not_38_out,
       not_39_out, not_40_out, not_41_out, not_42_out, not_43_out, not_44_out, not_45_out, not_46_out,
       not_47_out, not_48_out, not_49_out, not_50_out, not_51_out, not_52_out, not_53_out, not_54_out,
       not_55_out, not_56_out, not_57_out, not_58_out, not_59_out, not_60_out, not_61_out, not_62_out,
       not_63_out, not_64_out, not_65_out, not_66_out, not_67_out, not_68_out, not_69_out, not_70_out,
       not_71_out, not_72_out, not_73_out, not_74_out, not_75_out, not_76_out, not_77_out, not_78_out,
       not_79_out, not_80_out, not_81_out, not_82_out, not_83_out, not_84_out, not_85_out, not_86_out,
       not_87_out, not_88_out, not_89_out, not_90_out, not_91_out, not_92_out, not_93_out, not_94_out,
       not_95_out, not_96_out, not_97_out, not_98_out, not_99_out, not_100_out, not_101_out, not_102_out,
       not_103_out, not_104_out, not_105_out, not_106_out, not_107_out, not_108_out, not_109_out,
       not_110_out, not_111_out, not_112_out, not_113_out, not_114_out, not_115_out, not_116_out,
       not_117_out, not_118_out, not_119_out, not_120_out, not_121_out, not_122_out, not_123_out,
       not_124_out, not_125_out, not_126_out, not_127_out, not_128_out, not_129_out, not_130_out,
       not_131_out, not_132_out, not_133_out, not_134_out, not_135_out, not_136_out, not_137_out,
       not_138_out, not_139_out, not_140_out, not_141_out, not_142_out, not_143_out, not_144_out,
       not_145_out, not_146_out, not_147_out, not_148_out, not_149_out, not_150_out, not_151_out,
       not_152_out, not_153_out, not_154_out, not_155_out, not_156_out, not_157_out, not_158_out,
       not_159_out, not_160_out, not_161_out, not_162_out, not_163_out, not_164_out, not_165_out,
       not_166_out, not_167_out, not_168_out, not_169_out, not_170_out, not_171_out, not_172_out,
       not_173_out, not_174_out, not_175_out, not_176_out, not_177_out, not_178_out, not_179_out,
       not_180_out, not_181_out, not_182_out, not_183_out, not_184_out, not_185_out, not_186_out,
       not_187_out, not_188_out, not_189_out, not_190_out, not_191_out, not_192_out, not_193_out,
       not_194_out, not_195_out, not_196_out, not_197_out, not_198_out, not_199_out, not_200_out,
       not_201_out, not_202_out, not_203_out, not_204_out, not_205_out, not_206_out, not_207_out,
       not_208_out, not_209_out, not_210_out, not_211_out, not_212_out, not_213_out, not_214_out,
       not_215_out, not_216_out, not_217_out, not_218_out, not_219_out, not_220_out, not_221_out,
       not_222_out, not_223_out, not_224_out, not_225_out, not_226_out, not_227_out, not_228_out,
       not_229_out, not_230_out, not_231_out, not_232_out, not_233_out, not_234_out, not_235_out,
       not_236_out, not_237_out, not_238_out, not_239_out, not_240_out, not_241_out, not_242_out,
       not_243_out, not_244_out, not_245_out, not_246_out, not_247_out, not_248_out, not_249_out,
       not_250_out, not_251_out, not_252_out, not_253_out, not_254_out, not_255_out, not_256_out,
       not_257_out, not_258_out, not_259_out, not_260_out, not_261_out, not_262_out, not_263_out,
       not_264_out, not_265_out, not_266_out, not_267_out, not_268_out, not_269_out, not_270_out,
       not_271_out, not_272_out, not_273_out, not_274_out, not_275_out, not_276_out, not_277_out,
       not_278_out, not_279_out, not_280_out, not_281_out, not_282_out, not_283_out, not_284_out,
       not_285_out, not_286_out, not_287_out, not_288_out, not_289_out, not_290_out, not_291_out,
       not_292_out, not_293_out, not_294_out, not_295_out, not_296_out, not_297_out, not_298_out,
       not_299_out, not_300_out, not_301_out, not_302_out, not_303_out, not_304_out, not_305_out,
       not_306_out, not_307_out, not_308_out, not_309_out, not_310_out, not_311_out, not_312_out,
       not_313_out, not_314_out, not_315_out, not_316_out, not_317_out, not_318_out, not_319_out,
       not_320_out, not_321_out, not_322_out, not_323_out, not_324_out, not_325_out, not_326_out,
       not_327_out, not_328_out, not_329_out;

  not not_1 (not_1_out, OP5);
  not not_2 (not_2_out, OP4);
  not not_3 (not_3_out, OP3);
  not not_4 (not_4_out, OP2);
  not not_5 (not_5_out, OP1);
  not not_6 (not_6_out, OP0);
  not not_7 (not_7_out, F5);
  not not_8 (not_8_out, F4);
  not not_9 (not_9_out, F3);
  not not_10 (not_10_out, F2);
  not not_11 (not_11_out, F1);
  not not_12 (not_12_out, F0);
  not not_13 (not_13_out, OP5);
  not not_14 (not_14_out, OP4);
  not not_15 (not_15_out, OP3);
  not not_16 (not_16_out, OP2);
  not not_17 (not_17_out, OP1);
  not not_18 (not_18_out, OP0);
  not not_19 (not_19_out, F5);
  not not_20 (not_20_out, F4);
  not not_21 (not_21_out, F3);
  not not_22 (not_22_out, F2);
  not not_23 (not_23_out, OP5);
  not not_24 (not_24_out, OP4);
  not not_25 (not_25_out, OP3);
  not not_26 (not_26_out, OP2);
  not not_27 (not_27_out, OP1);
  not not_28 (not_28_out, OP0);
  not not_29 (not_29_out, F5);
  not not_30 (not_30_out, F4);
  not not_31 (not_31_out, F3);
  not not_32 (not_32_out, F2);
  not not_33 (not_33_out, F0);
  not not_34 (not_34_out, OP5);
  not not_35 (not_35_out, OP4);
  not not_36 (not_36_out, OP3);
  not not_37 (not_37_out, OP2);
  not not_38 (not_38_out, OP1);
  not not_39 (not_39_out, OP0);
  not not_40 (not_40_out, F4);
  not not_41 (not_41_out, F3);
  not not_42 (not_42_out, F2);
  not not_43 (not_43_out, F1);
  not not_44 (not_44_out, F0);
  not not_45 (not_45_out, OP5);
  not not_46 (not_46_out, OP4);
  not not_47 (not_47_out, OP3);
  not not_48 (not_48_out, OP2);
  not not_49 (not_49_out, OP1);
  not not_50 (not_50_out, OP0);
  not not_51 (not_51_out, F4);
  not not_52 (not_52_out, F3);
  not not_53 (not_53_out, F2);
  not not_54 (not_54_out, F1);
  not not_55 (not_55_out, OP5);
  not not_56 (not_56_out, OP4);
  not not_57 (not_57_out, OP3);
  not not_58 (not_58_out, OP2);
  not not_59 (not_59_out, OP1);
  not not_60 (not_60_out, OP0);
  not not_61 (not_61_out, F4);
  not not_62 (not_62_out, F3);
  not not_63 (not_63_out, F2);
  not not_64 (not_64_out, F0);
  not not_65 (not_65_out, OP5);
  not not_66 (not_66_out, OP4);
  not not_67 (not_67_out, OP3);
  not not_68 (not_68_out, OP2);
  not not_69 (not_69_out, OP1);
  not not_70 (not_70_out, OP0);
  not not_71 (not_71_out, F4);
  not not_72 (not_72_out, F3);
  not not_73 (not_73_out, F1);
  not not_74 (not_74_out, F0);
  not not_75 (not_75_out, OP5);
  not not_76 (not_76_out, OP4);
  not not_77 (not_77_out, OP3);
  not not_78 (not_78_out, OP2);
  not not_79 (not_79_out, OP1);
  not not_80 (not_80_out, OP0);
  not not_81 (not_81_out, F4);
  not not_82 (not_82_out, F3);
  not not_83 (not_83_out, F1);
  not not_84 (not_84_out, OP5);
  not not_85 (not_85_out, OP4);
  not not_86 (not_86_out, OP3);
  not not_87 (not_87_out, OP2);
  not not_88 (not_88_out, OP1);
  not not_89 (not_89_out, OP0);
  not not_90 (not_90_out, F4);
  not not_91 (not_91_out, F3);
  not not_92 (not_92_out, OP5);
  not not_93 (not_93_out, OP4);
  not not_94 (not_94_out, OP3);
  not not_95 (not_95_out, OP2);
  not not_96 (not_96_out, OP1);
  not not_97 (not_97_out, OP0);
  not not_98 (not_98_out, F4);
  not not_99 (not_99_out, F2);
  not not_100 (not_100_out, F0);
  not not_101 (not_101_out, OP5);
  not not_102 (not_102_out, OP4);
  not not_103 (not_103_out, OP3);
  not not_104 (not_104_out, OP2);
  not not_105 (not_105_out, OP1);
  not not_106 (not_106_out, OP0);
  not not_107 (not_107_out, F4);
  not not_108 (not_108_out, F2);
  not not_109 (not_109_out, OP5);
  not not_110 (not_110_out, OP4);
  not not_111 (not_111_out, OP3);
  not not_112 (not_112_out, OP2);
  not not_113 (not_113_out, OP1);
  not not_114 (not_114_out, OP0);
  not not_115 (not_115_out, F5);
  not not_116 (not_116_out, F4);
  not not_117 (not_117_out, F2);
  not not_118 (not_118_out, F1);
  not not_119 (not_119_out, F0);
  not not_120 (not_120_out, OP5);
  not not_121 (not_121_out, OP4);
  not not_122 (not_122_out, OP3);
  not not_123 (not_123_out, OP2);
  not not_124 (not_124_out, OP1);
  not not_125 (not_125_out, OP0);
  not not_126 (not_126_out, F5);
  not not_127 (not_127_out, F4);
  not not_128 (not_128_out, F1);
  not not_129 (not_129_out, F0);
  not not_130 (not_130_out, OP5);
  not not_131 (not_131_out, OP4);
  not not_132 (not_132_out, OP3);
  not not_133 (not_133_out, OP1);
  not not_134 (not_134_out, OP0);
  not not_135 (not_135_out, OP5);
  not not_136 (not_136_out, OP4);
  not not_137 (not_137_out, OP3);
  not not_138 (not_138_out, OP1);
  not not_139 (not_139_out, OP5);
  not not_140 (not_140_out, OP4);
  not not_141 (not_141_out, OP2);
  not not_142 (not_142_out, OP1);
  not not_143 (not_143_out, OP0);
  not not_144 (not_144_out, OP5);
  not not_145 (not_145_out, OP4);
  not not_146 (not_146_out, OP1);
  not not_147 (not_147_out, OP0);
  not not_148 (not_148_out, OP5);
  not not_149 (not_149_out, OP4);
  not not_150 (not_150_out, OP2);
  not not_151 (not_151_out, OP1);
  not not_152 (not_152_out, OP5);
  not not_153 (not_153_out, OP4);
  not not_154 (not_154_out, OP2);
  not not_155 (not_155_out, OP0);
  not not_156 (not_156_out, OP5);
  not not_157 (not_157_out, OP4);
  not not_158 (not_158_out, OP1);
  not not_159 (not_159_out, OP4);
  not not_160 (not_160_out, OP3);
  not not_161 (not_161_out, OP2);
  not not_162 (not_162_out, OP4);
  not not_163 (not_163_out, OP2);
  not not_164 (not_164_out, OP5);
  not not_165 (not_165_out, OP4);
  not not_166 (not_166_out, OP3);
  not not_167 (not_167_out, OP2);
  not not_168 (not_168_out, OP1);
  not not_169 (not_169_out, OP0);
  not not_170 (not_170_out, F5);
  not not_171 (not_171_out, F4);
  not not_172 (not_172_out, F3);
  not not_173 (not_173_out, OP5);
  not not_174 (not_174_out, OP4);
  not not_175 (not_175_out, OP0);
  not not_176 (not_176_out, OP4);
  not not_177 (not_177_out, OP3);
  not not_178 (not_178_out, OP2);
  not not_179 (not_179_out, OP1);
  not not_180 (not_180_out, OP5);
  not not_181 (not_181_out, OP4);
  not not_182 (not_182_out, OP3);
  not not_183 (not_183_out, OP2);
  not not_184 (not_184_out, OP1);
  not not_185 (not_185_out, OP5);
  not not_186 (not_186_out, OP4);
  not not_187 (not_187_out, OP3);
  not not_188 (not_188_out, OP2);
  not not_189 (not_189_out, OP1);
  not not_190 (not_190_out, OP0);
  not not_191 (not_191_out, F5);
  not not_192 (not_192_out, F4);
  not not_193 (not_193_out, F3);
  not not_194 (not_194_out, F2);
  not not_195 (not_195_out, F1);
  not not_196 (not_196_out, F0);
  not not_197 (not_197_out, OP5);
  not not_198 (not_198_out, OP4);
  not not_199 (not_199_out, OP3);
  not not_200 (not_200_out, OP2);
  not not_201 (not_201_out, OP1);
  not not_202 (not_202_out, OP0);
  not not_203 (not_203_out, F5);
  not not_204 (not_204_out, F4);
  not not_205 (not_205_out, F3);
  not not_206 (not_206_out, F2);
  not not_207 (not_207_out, OP5);
  not not_208 (not_208_out, OP4);
  not not_209 (not_209_out, OP3);
  not not_210 (not_210_out, OP2);
  not not_211 (not_211_out, OP1);
  not not_212 (not_212_out, OP0);
  not not_213 (not_213_out, F5);
  not not_214 (not_214_out, F4);
  not not_215 (not_215_out, F3);
  not not_216 (not_216_out, F2);
  not not_217 (not_217_out, F0);
  not not_218 (not_218_out, OP5);
  not not_219 (not_219_out, OP4);
  not not_220 (not_220_out, OP3);
  not not_221 (not_221_out, OP2);
  not not_222 (not_222_out, OP1);
  not not_223 (not_223_out, OP0);
  not not_224 (not_224_out, F4);
  not not_225 (not_225_out, F3);
  not not_226 (not_226_out, F2);
  not not_227 (not_227_out, F1);
  not not_228 (not_228_out, F0);
  not not_229 (not_229_out, OP5);
  not not_230 (not_230_out, OP4);
  not not_231 (not_231_out, OP3);
  not not_232 (not_232_out, OP2);
  not not_233 (not_233_out, OP1);
  not not_234 (not_234_out, OP0);
  not not_235 (not_235_out, F4);
  not not_236 (not_236_out, F3);
  not not_237 (not_237_out, F2);
  not not_238 (not_238_out, F1);
  not not_239 (not_239_out, OP5);
  not not_240 (not_240_out, OP4);
  not not_241 (not_241_out, OP3);
  not not_242 (not_242_out, OP2);
  not not_243 (not_243_out, OP1);
  not not_244 (not_244_out, OP0);
  not not_245 (not_245_out, F4);
  not not_246 (not_246_out, F3);
  not not_247 (not_247_out, F2);
  not not_248 (not_248_out, F0);
  not not_249 (not_249_out, OP5);
  not not_250 (not_250_out, OP4);
  not not_251 (not_251_out, OP3);
  not not_252 (not_252_out, OP2);
  not not_253 (not_253_out, OP1);
  not not_254 (not_254_out, OP0);
  not not_255 (not_255_out, F4);
  not not_256 (not_256_out, F3);
  not not_257 (not_257_out, F1);
  not not_258 (not_258_out, F0);
  not not_259 (not_259_out, OP5);
  not not_260 (not_260_out, OP4);
  not not_261 (not_261_out, OP3);
  not not_262 (not_262_out, OP2);
  not not_263 (not_263_out, OP1);
  not not_264 (not_264_out, OP0);
  not not_265 (not_265_out, F4);
  not not_266 (not_266_out, F3);
  not not_267 (not_267_out, F1);
  not not_268 (not_268_out, OP5);
  not not_269 (not_269_out, OP4);
  not not_270 (not_270_out, OP3);
  not not_271 (not_271_out, OP2);
  not not_272 (not_272_out, OP1);
  not not_273 (not_273_out, OP0);
  not not_274 (not_274_out, F4);
  not not_275 (not_275_out, F3);
  not not_276 (not_276_out, OP5);
  not not_277 (not_277_out, OP4);
  not not_278 (not_278_out, OP3);
  not not_279 (not_279_out, OP2);
  not not_280 (not_280_out, OP1);
  not not_281 (not_281_out, OP0);
  not not_282 (not_282_out, F4);
  not not_283 (not_283_out, F2);
  not not_284 (not_284_out, F0);
  not not_285 (not_285_out, OP5);
  not not_286 (not_286_out, OP4);
  not not_287 (not_287_out, OP3);
  not not_288 (not_288_out, OP2);
  not not_289 (not_289_out, OP1);
  not not_290 (not_290_out, OP0);
  not not_291 (not_291_out, F4);
  not not_292 (not_292_out, F2);
  not not_293 (not_293_out, OP5);
  not not_294 (not_294_out, OP4);
  not not_295 (not_295_out, OP3);
  not not_296 (not_296_out, OP2);
  not not_297 (not_297_out, OP1);
  not not_298 (not_298_out, OP0);
  not not_299 (not_299_out, F5);
  not not_300 (not_300_out, F4);
  not not_301 (not_301_out, F1);
  not not_302 (not_302_out, F0);
  not not_303 (not_303_out, OP5);
  not not_304 (not_304_out, OP4);
  not not_305 (not_305_out, OP3);
  not not_306 (not_306_out, OP1);
  not not_307 (not_307_out, OP0);
  not not_308 (not_308_out, OP5);
  not not_309 (not_309_out, OP4);
  not not_310 (not_310_out, OP3);
  not not_311 (not_311_out, OP1);
  not not_312 (not_312_out, OP4);
  not not_313 (not_313_out, OP3);
  not not_314 (not_314_out, OP2);
  not not_315 (not_315_out, OP4);
  not not_316 (not_316_out, OP2);
  not not_317 (not_317_out, OP5);
  not not_318 (not_318_out, OP4);
  not not_319 (not_319_out, OP3);
  not not_320 (not_320_out, OP2);
  not not_321 (not_321_out, OP1);
  not not_322 (not_322_out, OP0);
  not not_323 (not_323_out, F5);
  not not_324 (not_324_out, F4);
  not not_325 (not_325_out, F3);
  not not_326 (not_326_out, OP4);
  not not_327 (not_327_out, OP3);
  not not_328 (not_328_out, OP2);
  not not_329 (not_329_out, OP1);
  and and_1 (and_1_out, not_1_out, not_2_out, not_3_out, not_4_out, not_5_out, not_6_out, not_7_out, not_8_out, not_9_out, not_10_out, not_11_out, not_12_out);
  and and_2 (and_2_out, not_13_out, not_14_out, not_15_out, not_16_out, not_17_out, not_18_out, not_19_out, not_20_out, not_21_out, not_22_out, F1, F0);
  and and_3 (and_3_out, not_23_out, not_24_out, not_25_out, not_26_out, not_27_out, not_28_out, not_29_out, not_30_out, not_31_out, not_32_out, F1, not_33_out);
  and and_4 (and_4_out, not_34_out, not_35_out, not_36_out, not_37_out, not_38_out, not_39_out, F5, not_40_out, not_41_out, not_42_out, not_43_out, not_44_out);
  and and_5 (and_5_out, not_45_out, not_46_out, not_47_out, not_48_out, not_49_out, not_50_out, F5, not_51_out, not_52_out, not_53_out, not_54_out, F0);
  and and_6 (and_6_out, not_55_out, not_56_out, not_57_out, not_58_out, not_59_out, not_60_out, F5, not_61_out, not_62_out, not_63_out, F1, not_64_out);
  and and_7 (and_7_out, not_65_out, not_66_out, not_67_out, not_68_out, not_69_out, not_70_out, F5, not_71_out, not_72_out, F2, not_73_out, not_74_out);
  and and_8 (and_8_out, not_75_out, not_76_out, not_77_out, not_78_out, not_79_out, not_80_out, F5, not_81_out, not_82_out, F2, not_83_out, F0);
  and and_9 (and_9_out, not_84_out, not_85_out, not_86_out, not_87_out, not_88_out, not_89_out, F5, not_90_out, not_91_out, F2, F1, F0);
  and and_10 (and_10_out, not_92_out, not_93_out, not_94_out, not_95_out, not_96_out, not_97_out, F5, not_98_out, F3, not_99_out, F1, not_100_out);
  and and_11 (and_11_out, not_101_out, not_102_out, not_103_out, not_104_out, not_105_out, not_106_out, F5, not_107_out, F3, not_108_out, F1, F0);
  and and_12 (and_12_out, not_109_out, not_110_out, not_111_out, not_112_out, not_113_out, not_114_out, not_115_out, not_116_out, F3, not_117_out, not_118_out, not_119_out);
  and and_13 (and_13_out, not_120_out, not_121_out, not_122_out, not_123_out, not_124_out, not_125_out, not_126_out, not_127_out, F3, F2, not_128_out, not_129_out);
  and and_14 (and_14_out, not_130_out, not_131_out, not_132_out, OP2, not_133_out, not_134_out);
  and and_15 (and_15_out, not_135_out, not_136_out, not_137_out, OP2, not_138_out, OP0);
  and and_16 (and_16_out, not_139_out, not_140_out, OP3, not_141_out, not_142_out, not_143_out);
  and and_17 (and_17_out, not_144_out, not_145_out, OP3, OP2, not_146_out, not_147_out);
  and and_18 (and_18_out, not_148_out, not_149_out, OP3, not_150_out, not_151_out, OP0);
  and and_19 (and_19_out, not_152_out, not_153_out, OP3, not_154_out, OP1, not_155_out);
  and and_20 (and_20_out, not_156_out, not_157_out, OP3, OP2, not_158_out, OP0);
  and and_21 (and_21_out, OP5, not_159_out, not_160_out, not_161_out, OP1, OP0);
  and and_22 (and_22_out, OP5, not_162_out, OP3, not_163_out, OP1, OP0);
  and and_23 (and_23_out, not_164_out, not_165_out, not_166_out, not_167_out, not_168_out, not_169_out, not_170_out, not_171_out, not_172_out, F2, F1, F0);
  and and_24 (and_24_out, not_173_out, not_174_out, OP3, OP2, OP1, not_175_out);
  and and_25 (and_25_out, OP5, not_176_out, not_177_out, not_178_out, not_179_out, OP0);
  and and_26 (and_26_out, not_180_out, not_181_out, not_182_out, not_183_out, not_184_out, OP0);
  and and_27 (and_27_out, not_185_out, not_186_out, not_187_out, not_188_out, not_189_out, not_190_out, not_191_out, not_192_out, not_193_out, not_194_out, not_195_out, not_196_out);
  and and_28 (and_28_out, not_197_out, not_198_out, not_199_out, not_200_out, not_201_out, not_202_out, not_203_out, not_204_out, not_205_out, not_206_out, F1, F0);
  and and_29 (and_29_out, not_207_out, not_208_out, not_209_out, not_210_out, not_211_out, not_212_out, not_213_out, not_214_out, not_215_out, not_216_out, F1, not_217_out);
  and and_30 (and_30_out, not_218_out, not_219_out, not_220_out, not_221_out, not_222_out, not_223_out, F5, not_224_out, not_225_out, not_226_out, not_227_out, not_228_out);
  and and_31 (and_31_out, not_229_out, not_230_out, not_231_out, not_232_out, not_233_out, not_234_out, F5, not_235_out, not_236_out, not_237_out, not_238_out, F0);
  and and_32 (and_32_out, not_239_out, not_240_out, not_241_out, not_242_out, not_243_out, not_244_out, F5, not_245_out, not_246_out, not_247_out, F1, not_248_out);
  and and_33 (and_33_out, not_249_out, not_250_out, not_251_out, not_252_out, not_253_out, not_254_out, F5, not_255_out, not_256_out, F2, not_257_out, not_258_out);
  and and_34 (and_34_out, not_259_out, not_260_out, not_261_out, not_262_out, not_263_out, not_264_out, F5, not_265_out, not_266_out, F2, not_267_out, F0);
  and and_35 (and_35_out, not_268_out, not_269_out, not_270_out, not_271_out, not_272_out, not_273_out, F5, not_274_out, not_275_out, F2, F1, F0);
  and and_36 (and_36_out, not_276_out, not_277_out, not_278_out, not_279_out, not_280_out, not_281_out, F5, not_282_out, F3, not_283_out, F1, not_284_out);
  and and_37 (and_37_out, not_285_out, not_286_out, not_287_out, not_288_out, not_289_out, not_290_out, F5, not_291_out, F3, not_292_out, F1, F0);
  and and_38 (and_38_out, not_293_out, not_294_out, not_295_out, not_296_out, not_297_out, not_298_out, not_299_out, not_300_out, F3, F2, not_301_out, not_302_out);
  and and_39 (and_39_out, not_303_out, not_304_out, not_305_out, OP2, not_306_out, not_307_out);
  and and_40 (and_40_out, not_308_out, not_309_out, not_310_out, OP2, not_311_out, OP0);
  and and_41 (and_41_out, OP5, not_312_out, not_313_out, not_314_out, OP1, OP0);
  and and_42 (and_42_out, OP5, not_315_out, OP3, not_316_out, OP1, OP0);
  and and_43 (and_43_out, not_317_out, not_318_out, not_319_out, not_320_out, not_321_out, not_322_out, not_323_out, not_324_out, not_325_out, F2, F1, F0);
  and and_44 (and_44_out, OP5, not_326_out, not_327_out, not_328_out, not_329_out, OP0);
  or or_1 (R1_used, and_1_out, and_2_out, and_3_out, and_4_out, and_5_out, and_6_out, and_7_out, and_8_out, and_9_out, and_10_out, and_11_out, and_12_out, and_13_out, and_14_out, and_15_out, and_16_out, and_17_out, and_18_out, and_19_out, and_20_out, and_21_out, and_22_out, and_23_out, and_24_out, and_25_out, and_26_out);
  or or_2 (R2_used, and_27_out, and_28_out, and_29_out, and_30_out, and_31_out, and_32_out, and_33_out, and_34_out, and_35_out, and_36_out, and_37_out, and_38_out, and_39_out, and_40_out, and_41_out, and_42_out, and_43_out, and_44_out);
endmodule

module BHT (
  input  [31:0] IF_PC,
  input  [31:0] JumpAddr,
  input  [31:0] EX_PC,
  input  EX_Branch,
  input  CLK,
  input  in_6,
  output Jump,
  output [31:0] DataOut
);

  wire and_17_out, and_18_out, comparator_1_eq, comparator_2_eq, comparator_3_eq, comparator_4_eq,
       comparator_5_eq, comparator_6_eq, comparator_7_eq, comparator_8_eq, comparator_9_eq, comparator_10_eq,
       comparator_11_eq, comparator_12_eq, comparator_13_eq, comparator_14_eq, comparator_15_eq,
       comparator_16_eq, HIT, L0, l0_t, L1, l1_t, L2, l2_t, L3, l3_t, L4, l4_t, L5, l5_t, L6, l6_t, L7, l7_t,
       Miss, not_1_out, not_3_out, not_4_out, not_5_out, not_6_out, not_7_out, not_8_out, not_9_out,
       not_10_out, or_1_out, or_2_out, or_3_out, or_4_out, or_5_out, or_6_out, or_7_out, or_8_out, or_9_out,
       or_10_out, or_11_out, v0, v1, v2, v3, v4, v5, v6, v7, \全满 , \淘汰0 , \淘汰1 , \淘汰2 , \淘汰3 , \淘汰4 , \淘汰5 ,
       \淘汰6 , \淘汰7 ;
  wire [0:0] curState;
  wire [1:0] multiplexer_1_out, multiplexer_2_out, multiplexer_3_out, multiplexer_4_out, NewState, Stat_2_q,
       Stat_3_q, Stat_4_q, Stat_5_q, Stat_6_q, Stat_7_q, Stat_8_q, Stat_q, State;
  wire [2:0] Max, max3_1_max_num, max3_2_max_num, max3_3_max_num, max3_4_max_num, max3_5_max_num,
       max3_6_max_num, multiplexer_6_out, priority_encoder_2_out, Valued, \淘汰 ;
  wire [15:0] c0, c1, c2, c3, c4, c5, c6, c7, max3_1_max, max3_2_max, max3_3_max, max3_4_max, max3_5_max,
       max3_6_max;
  wire [31:0] tag0, tag1, tag2, tag3, tag4, tag5, tag6, tag7, \数据块副本_2_q , \数据块副本_3_q , \数据块副本_4_q ,
       \数据块副本_5_q , \数据块副本_6_q , \数据块副本_7_q , \数据块副本_8_q , \数据块副本_q ;

  Register #(.width(1), .trigger("rising"), .Select("low")) valid (
    .D(1'b1), .en(\淘汰3 ), .Q(v3), .clk(CLK));  // open: clr
  Register #(.width(1), .trigger("rising"), .Select("low")) valid_2 (
    .D(1'b1), .en(\淘汰0 ), .Q(v0), .clk(CLK));  // open: clr
  Register #(.width(1), .trigger("rising"), .Select("low")) valid_3 (
    .D(1'b1), .en(\淘汰1 ), .Q(v1), .clk(CLK));  // open: clr
  Register #(.width(1), .trigger("rising"), .Select("low")) valid_4 (
    .D(1'b1), .en(\淘汰2 ), .Q(v2), .clk(CLK));  // open: clr
  Comparator #(.width(32), .mode("twosComplement")) comparator_1 (
    .a(IF_PC), .b(tag0), .eq(comparator_1_eq));  // open: gt, lt
  Comparator #(.width(32), .mode("twosComplement")) comparator_2 (
    .a(IF_PC), .b(tag1), .eq(comparator_2_eq));  // open: gt, lt
  Comparator #(.width(32), .mode("twosComplement")) comparator_3 (
    .a(IF_PC), .b(tag2), .eq(comparator_3_eq));  // open: gt, lt
  Comparator #(.width(32), .mode("twosComplement")) comparator_4 (
    .a(IF_PC), .b(tag3), .eq(comparator_4_eq));  // open: gt, lt
  Comparator #(.width(32), .mode("twosComplement")) comparator_5 (
    .a(IF_PC), .b(tag4), .eq(comparator_5_eq));  // open: gt, lt
  Comparator #(.width(32), .mode("twosComplement")) comparator_6 (
    .a(IF_PC), .b(tag5), .eq(comparator_6_eq));  // open: gt, lt
  Comparator #(.width(32), .mode("twosComplement")) comparator_7 (
    .a(IF_PC), .b(tag6), .eq(comparator_7_eq));  // open: gt, lt
  Comparator #(.width(32), .mode("twosComplement")) comparator_8 (
    .a(IF_PC), .b(tag7), .eq(comparator_8_eq));  // open: gt, lt
  Register #(.width(32), .trigger("rising"), .Select("low")) \u_标志位  (
    .D(EX_PC), .en(\淘汰0 ), .Q(tag0), .clk(CLK));  // open: clr
  Register #(.width(32), .trigger("rising"), .Select("low")) \u_标志位_2  (
    .D(EX_PC), .en(\淘汰1 ), .Q(tag1), .clk(CLK));  // open: clr
  Register #(.width(32), .trigger("rising"), .Select("low")) \u_标志位_3  (
    .D(EX_PC), .en(\淘汰2 ), .Q(tag2), .clk(CLK));  // open: clr
  Register #(.width(32), .trigger("rising"), .Select("low")) \u_标志位_4  (
    .D(EX_PC), .en(\淘汰3 ), .Q(tag3), .clk(CLK));  // open: clr
  and and_1 (L0, v0, comparator_1_eq);
  and and_2 (L1, v1, comparator_2_eq);
  and and_3 (L2, v2, comparator_3_eq);
  and and_4 (L3, v3, comparator_4_eq);
  and and_5 (L4, v4, comparator_5_eq);
  and and_6 (L5, v5, comparator_6_eq);
  and and_7 (L6, v6, comparator_7_eq);
  and and_8 (L7, v7, comparator_8_eq);
  Counter #(.width(16), .max('hffff), .ongoal("wrap"), .trigger("rising"), .behavior("new")) \u_淘汰标志位  (
    .load(or_1_out), .D({16{1'b0}}), .Q(c0), .clk(CLK));  // open: count, carry, clr, preset, down
  or or_1 (or_1_out, L0, \淘汰0 );
  Counter #(.width(16), .max('hffff), .ongoal("wrap"), .trigger("rising"), .behavior("new")) \u_淘汰标志位_2  (
    .load(or_2_out), .D({16{1'b0}}), .Q(c1), .clk(CLK));  // open: count, carry, clr, preset, down
  or or_2 (or_2_out, L1, \淘汰1 );
  Counter #(.width(16), .max('hffff), .ongoal("wrap"), .trigger("rising"), .behavior("new")) \u_淘汰标志位_3  (
    .load(or_3_out), .D({16{1'b0}}), .Q(c2), .clk(CLK));  // open: count, carry, clr, preset, down
  or or_3 (or_3_out, L2, \淘汰2 );
  Counter #(.width(16), .max('hffff), .ongoal("wrap"), .trigger("rising"), .behavior("new")) \u_淘汰标志位_4  (
    .load(or_4_out), .D({16{1'b0}}), .Q(c3), .clk(CLK));  // open: count, carry, clr, preset, down
  or or_4 (or_4_out, L3, \淘汰3 );
  or or_5 (or_5_out, L0, L1, L2, L3);
  or or_6 (or_6_out, L4, L5, L6, L7);
  or or_7 (or_7_out, or_5_out, or_6_out);
  not not_1 (not_1_out, or_7_out);
  Register #(.width(32), .trigger("rising"), .Select("low")) \u_数据块副本  (
    .D(JumpAddr), .en(\淘汰0 ), .Q(\数据块副本_q ), .clk(CLK));  // open: clr
  Register #(.width(32), .trigger("rising"), .Select("low")) \u_数据块副本_2  (
    .D(JumpAddr), .en(\淘汰1 ), .Q(\数据块副本_2_q ), .clk(CLK));  // open: clr
  Register #(.width(32), .trigger("rising"), .Select("low")) \u_数据块副本_3  (
    .D(JumpAddr), .en(\淘汰2 ), .Q(\数据块副本_3_q ), .clk(CLK));  // open: clr
  Register #(.width(32), .trigger("rising"), .Select("low")) \u_数据块副本_4  (
    .D(JumpAddr), .en(\淘汰3 ), .Q(\数据块副本_4_q ), .clk(CLK));  // open: clr
  assign {Jump, curState[0]} = not_1_out ? 2'b00 : 2'bz;  // Controlled_Buffer controlled_buffer_1
  assign DataOut = L0 ? \数据块副本_q  : 32'bz;  // Controlled_Buffer controlled_buffer_2
  assign DataOut = L1 ? \数据块副本_2_q  : 32'bz;  // Controlled_Buffer controlled_buffer_3
  assign DataOut = L2 ? \数据块副本_3_q  : 32'bz;  // Controlled_Buffer controlled_buffer_4
  assign DataOut = L3 ? \数据块副本_4_q  : 32'bz;  // Controlled_Buffer controlled_buffer_5
  assign State = l0_t ? Stat_q : 2'bz;  // Controlled_Buffer controlled_buffer_6
  Register #(.width(2), .trigger("rising"), .Select("low")) Stat (
    .D(NewState), .en(\淘汰0 ), .Q(Stat_q), .clk(CLK));  // open: clr
  Register #(.width(2), .trigger("rising"), .Select("low")) Stat_2 (
    .D(NewState), .en(\淘汰1 ), .Q(Stat_2_q), .clk(CLK));  // open: clr
  Register #(.width(2), .trigger("rising"), .Select("low")) Stat_3 (
    .D(NewState), .en(\淘汰2 ), .Q(Stat_3_q), .clk(CLK));  // open: clr
  Register #(.width(2), .trigger("rising"), .Select("low")) Stat_4 (
    .D(NewState), .en(\淘汰3 ), .Q(Stat_4_q), .clk(CLK));  // open: clr
  assign {Jump, curState[0]} = L0 ? Stat_q : 2'bz;  // Controlled_Buffer controlled_buffer_7
  assign {Jump, curState[0]} = L1 ? Stat_2_q : 2'bz;  // Controlled_Buffer controlled_buffer_8
  assign State = l1_t ? Stat_2_q : 2'bz;  // Controlled_Buffer controlled_buffer_9
  assign {Jump, curState[0]} = L2 ? Stat_3_q : 2'bz;  // Controlled_Buffer controlled_buffer_10
  assign State = l2_t ? Stat_3_q : 2'bz;  // Controlled_Buffer controlled_buffer_11
  assign {Jump, curState[0]} = L3 ? Stat_4_q : 2'bz;  // Controlled_Buffer controlled_buffer_12
  assign State = l3_t ? Stat_4_q : 2'bz;  // Controlled_Buffer controlled_buffer_13
  Comparator #(.width(32), .mode("twosComplement")) comparator_9 (
    .a(EX_PC), .b(tag0), .eq(comparator_9_eq));  // open: gt, lt
  Comparator #(.width(32), .mode("twosComplement")) comparator_10 (
    .a(EX_PC), .b(tag1), .eq(comparator_10_eq));  // open: gt, lt
  Comparator #(.width(32), .mode("twosComplement")) comparator_11 (
    .a(EX_PC), .b(tag2), .eq(comparator_11_eq));  // open: gt, lt
  Comparator #(.width(32), .mode("twosComplement")) comparator_12 (
    .a(EX_PC), .b(tag3), .eq(comparator_12_eq));  // open: gt, lt
  Comparator #(.width(32), .mode("twosComplement")) comparator_13 (
    .a(EX_PC), .b(tag4), .eq(comparator_13_eq));  // open: gt, lt
  Comparator #(.width(32), .mode("twosComplement")) comparator_14 (
    .a(EX_PC), .b(tag5), .eq(comparator_14_eq));  // open: gt, lt
  Comparator #(.width(32), .mode("twosComplement")) comparator_15 (
    .a(EX_PC), .b(tag6), .eq(comparator_15_eq));  // open: gt, lt
  Comparator #(.width(32), .mode("twosComplement")) comparator_16 (
    .a(EX_PC), .b(tag7), .eq(comparator_16_eq));  // open: gt, lt
  Register #(.width(1), .trigger("rising"), .Select("low")) valid_5 (
    .D(1'b1), .en(\淘汰4 ), .Q(v4), .clk(CLK));  // open: clr
  Register #(.width(1), .trigger("rising"), .Select("low")) valid_6 (
    .D(1'b1), .en(\淘汰5 ), .Q(v5), .clk(CLK));  // open: clr
  Register #(.width(1), .trigger("rising"), .Select("low")) valid_7 (
    .D(1'b1), .en(\淘汰6 ), .Q(v6), .clk(CLK));  // open: clr
  Register #(.width(1), .trigger("rising"), .Select("low")) valid_8 (
    .D(1'b1), .en(\淘汰7 ), .Q(v7), .clk(CLK));  // open: clr
  and and_9 (l0_t, v0, comparator_9_eq);
  and and_10 (l1_t, v1, comparator_10_eq);
  and and_11 (l2_t, v2, comparator_11_eq);
  and and_12 (l3_t, v3, comparator_12_eq);
  and and_13 (l4_t, v4, comparator_13_eq);
  and and_14 (l5_t, v5, comparator_14_eq);
  and and_15 (l6_t, v6, comparator_15_eq);
  and and_16 (l7_t, v7, comparator_16_eq);
  Register #(.width(32), .trigger("rising"), .Select("low")) \u_标志位_5  (
    .D(EX_PC), .en(\淘汰4 ), .Q(tag4), .clk(CLK));  // open: clr
  Register #(.width(32), .trigger("rising"), .Select("low")) \u_标志位_6  (
    .D(EX_PC), .en(\淘汰5 ), .Q(tag5), .clk(CLK));  // open: clr
  Register #(.width(32), .trigger("rising"), .Select("low")) \u_标志位_7  (
    .D(EX_PC), .en(\淘汰6 ), .Q(tag6), .clk(CLK));  // open: clr
  Register #(.width(32), .trigger("rising"), .Select("low")) \u_标志位_8  (
    .D(EX_PC), .en(\淘汰7 ), .Q(tag7), .clk(CLK));  // open: clr
  not not_2 (HIT, Miss);
  Priority_Encoder #(.select(3), .disabled("Z")) priority_encoder_1 (
    .in0(l0_t), .in1(l1_t), .in2(l2_t), .in3(l3_t), .in4(l4_t), .in5(l5_t), .in6(l6_t), .in7(l7_t),
    .out(Valued), .en_out(Miss), .en_in(1'b1));  // open: gs
  Counter #(.width(16), .max('hffff), .ongoal("wrap"), .trigger("rising"), .behavior("new")) \u_淘汰标志位_5  (
    .load(or_8_out), .D({16{1'b0}}), .Q(c4), .clk(CLK));  // open: count, carry, clr, preset, down
  or or_8 (or_8_out, L4, \淘汰4 );
  Counter #(.width(16), .max('hffff), .ongoal("wrap"), .trigger("rising"), .behavior("new")) \u_淘汰标志位_6  (
    .load(or_9_out), .D({16{1'b0}}), .Q(c5), .clk(CLK));  // open: count, carry, clr, preset, down
  or or_9 (or_9_out, L5, \淘汰5 );
  Counter #(.width(16), .max('hffff), .ongoal("wrap"), .trigger("rising"), .behavior("new")) \u_淘汰标志位_7  (
    .load(or_10_out), .D({16{1'b0}}), .Q(c6), .clk(CLK));  // open: count, carry, clr, preset, down
  or or_10 (or_10_out, \淘汰6 , L6);
  Counter #(.width(16), .max('hffff), .ongoal("wrap"), .trigger("rising"), .behavior("new")) \u_淘汰标志位_8  (
    .load(or_11_out), .D({16{1'b0}}), .Q(c7), .clk(CLK));  // open: count, carry, clr, preset, down
  or or_11 (or_11_out, L7, \淘汰7 );
  Multiplexer #(.select(2), .width(2), .disabled("Z"), .enable("false")) multiplexer_1 (
    .in0(2'b00), .in1(2'b00), .in2(2'b11), .in3(2'b00), .out(multiplexer_1_out), .sel(State));
  Multiplexer #(.select(2), .width(2), .disabled("Z"), .enable("false")) multiplexer_2 (
    .in0(2'b01), .in1(2'b10), .in2(2'b10), .in3(2'b10), .out(multiplexer_2_out), .sel(State));
  Register #(.width(32), .trigger("rising"), .Select("low")) \u_数据块副本_5  (
    .D(JumpAddr), .en(\淘汰4 ), .Q(\数据块副本_5_q ), .clk(CLK));  // open: clr
  Register #(.width(32), .trigger("rising"), .Select("low")) \u_数据块副本_6  (
    .D(JumpAddr), .en(\淘汰5 ), .Q(\数据块副本_6_q ), .clk(CLK));  // open: clr
  Register #(.width(32), .trigger("rising"), .Select("low")) \u_数据块副本_7  (
    .D(JumpAddr), .en(\淘汰6 ), .Q(\数据块副本_7_q ), .clk(CLK));  // open: clr
  assign DataOut = L7 ? \数据块副本_8_q  : 32'bz;  // Controlled_Buffer controlled_buffer_14
  Register #(.width(32), .trigger("rising"), .Select("low")) \u_数据块副本_8  (
    .D(JumpAddr), .en(\淘汰7 ), .Q(\数据块副本_8_q ), .clk(CLK));  // open: clr
  Multiplexer #(.select(1), .width(2), .disabled("Z"), .enable("false")) multiplexer_3 (
    .in0(multiplexer_1_out), .in1(multiplexer_2_out), .out(multiplexer_3_out), .sel(in_6));
  assign DataOut = L4 ? \数据块副本_5_q  : 32'bz;  // Controlled_Buffer controlled_buffer_15
  assign DataOut = L5 ? \数据块副本_6_q  : 32'bz;  // Controlled_Buffer controlled_buffer_16
  assign DataOut = L6 ? \数据块副本_7_q  : 32'bz;  // Controlled_Buffer controlled_buffer_17
  and and_17 (and_17_out, v0, v1, v2, v3);
  and and_18 (and_18_out, v4, v5, v6, v7);
  Demultiplexer #(.select(3), .width(1), .tristate("false"), .disabled(0), .enable("true")) demultiplexer_1 (
    .out0(\淘汰0 ), .out1(\淘汰1 ), .out2(\淘汰2 ), .out3(\淘汰3 ), .out4(\淘汰4 ), .out5(\淘汰5 ), .out6(\淘汰6 ),
    .out7(\淘汰7 ), .in(EX_Branch), .sel(\淘汰 ), .en(EX_Branch));
  and and_19 (\全满 , and_17_out, and_18_out);
  Multiplexer #(.select(1), .width(2), .disabled("Z"), .enable("false")) multiplexer_4 (
    .in0(2'b01), .in1(2'b11), .out(multiplexer_4_out), .sel(in_6));
  Register #(.width(2), .trigger("rising"), .Select("low")) Stat_5 (
    .D(NewState), .en(\淘汰4 ), .Q(Stat_5_q), .clk(CLK));  // open: clr
  Register #(.width(2), .trigger("rising"), .Select("low")) Stat_6 (
    .D(NewState), .en(\淘汰5 ), .Q(Stat_6_q), .clk(CLK));  // open: clr
  Register #(.width(2), .trigger("rising"), .Select("low")) Stat_7 (
    .D(NewState), .en(\淘汰6 ), .Q(Stat_7_q), .clk(CLK));  // open: clr
  Register #(.width(2), .trigger("rising"), .Select("low")) Stat_8 (
    .D(NewState), .en(\淘汰7 ), .Q(Stat_8_q), .clk(CLK));  // open: clr
  Multiplexer #(.select(1), .width(2), .disabled("Z"), .enable("false")) multiplexer_5 (
    .in0(multiplexer_3_out), .in1(multiplexer_4_out), .out(NewState), .sel(Miss));
  assign {Jump, curState[0]} = L4 ? Stat_5_q : 2'bz;  // Controlled_Buffer controlled_buffer_18
  assign State = l4_t ? Stat_5_q : 2'bz;  // Controlled_Buffer controlled_buffer_19
  assign {Jump, curState[0]} = L5 ? Stat_6_q : 2'bz;  // Controlled_Buffer controlled_buffer_20
  assign State = l5_t ? Stat_6_q : 2'bz;  // Controlled_Buffer controlled_buffer_21
  assign {Jump, curState[0]} = L6 ? Stat_7_q : 2'bz;  // Controlled_Buffer controlled_buffer_22
  assign State = l6_t ? Stat_7_q : 2'bz;  // Controlled_Buffer controlled_buffer_23
  assign {Jump, curState[0]} = L7 ? Stat_8_q : 2'bz;  // Controlled_Buffer controlled_buffer_24
  assign State = l7_t ? Stat_8_q : 2'bz;  // Controlled_Buffer controlled_buffer_25
  not not_3 (not_3_out, v0);
  not not_4 (not_4_out, v1);
  not not_5 (not_5_out, v2);
  not not_6 (not_6_out, v3);
  not not_7 (not_7_out, v4);
  not not_8 (not_8_out, v5);
  not not_9 (not_9_out, v6);
  not not_10 (not_10_out, v7);
  Max3 max3_1 (.Y(c1), .MAX(max3_1_max), .X(c0), .Y_num(3'b001), .Max_num(max3_1_max_num), .X_num(3'b000));
  Max3 max3_2 (.Y(c3), .MAX(max3_2_max), .X(c2), .Y_num(3'b011), .Max_num(max3_2_max_num), .X_num(3'b010));
  Max3 max3_3 (.Y(c5), .MAX(max3_3_max), .X(c4), .Y_num(3'b101), .Max_num(max3_3_max_num), .X_num(3'b100));
  Max3 max3_4 (.Y(c7), .MAX(max3_4_max), .X(c6), .Y_num(3'b111), .Max_num(max3_4_max_num), .X_num(3'b110));
  Max3 max3_5 (
    .Y(max3_2_max), .MAX(max3_5_max), .X(max3_1_max), .Y_num(max3_2_max_num), .Max_num(max3_5_max_num),
    .X_num(max3_1_max_num));
  Max3 max3_6 (
    .Y(max3_4_max), .MAX(max3_6_max), .X(max3_3_max), .Y_num(max3_4_max_num), .Max_num(max3_6_max_num),
    .X_num(max3_3_max_num));
  Priority_Encoder #(.select(3), .disabled("Z")) priority_encoder_2 (
    .in0(not_3_out), .in1(not_4_out), .in2(not_5_out), .in3(not_6_out), .in4(not_7_out), .in5(not_8_out),
    .in6(not_9_out), .in7(not_10_out), .out(priority_encoder_2_out), .en_in(1'b1));  // open: gs, en_out
  Max3 max3_7 (
    .Y(max3_6_max), .X(max3_5_max), .Y_num(max3_6_max_num), .Max_num(Max), .X_num(max3_5_max_num));  // open: MAX
  Multiplexer #(.select(1), .width(3), .disabled("Z"), .enable("false")) multiplexer_6 (
    .in0(priority_encoder_2_out), .in1(Max), .out(multiplexer_6_out), .sel(\全满 ));
  Multiplexer #(.select(1), .width(3), .disabled("Z"), .enable("false")) multiplexer_7 (
    .in0(multiplexer_6_out), .in1(Valued), .out(\淘汰 ), .sel(HIT));

  // Other names for the same wires on the sheet: Blk[31:0] = JumpAddr; BlkReady = EX_Branch; curState[1] = Jump;
  //   EX_Branched = in_6; SlotData[31:0] = DataOut; Tag[31:0] = EX_PC; 字节地址[31:0] = IF_PC

  // Notes on the sheet:
  //   输入引脚区
  //   输出引脚区
endmodule

module Max3 (
  input  [15:0] Y,
  input  [15:0] X,
  input  [2:0] Y_num,
  input  [2:0] X_num,
  output [15:0] MAX,
  output [2:0] Max_num
);

  wire comparator_1_eq, comparator_1_gt, or_1_out;

  Multiplexer #(.select(1), .width(16), .disabled("Z"), .enable("false")) multiplexer_1 (
    .in0(Y), .in1(X), .out(MAX), .sel(or_1_out));
  Comparator #(.width(16), .mode("unsigned")) comparator_1 (
    .a(X), .b(Y), .gt(comparator_1_gt), .eq(comparator_1_eq));  // open: lt
  or or_1 (or_1_out, comparator_1_gt, comparator_1_eq);
  Multiplexer #(.select(1), .width(3), .disabled("Z"), .enable("false")) multiplexer_2 (
    .in0(Y_num), .in1(X_num), .out(Max_num), .sel(or_1_out));

  // Notes on the sheet:
  //   输出两个输入中的较大值，并输出较大值的3位编号
endmodule
